// Logisim project FinalVersion.circ as structural Verilog: 29 circuits, main circuit ◇单周期RISC-V
module \单周期RISC_V  (
  input  IR1,
  input  IR2,
  input  IR3,
  output RegWrite,
  output MemWrite,
  output [31:0] PC,
  output [31:0] IR,
  output [31:0] RDin,
  output [31:0] MDin,
  output [31:0] LedData
);

  wire Beq, Bge, Blt, Bne, branch, CLK, clock_1_out, comparator_1_eq, comparator_1_lt, d_ff_1_q, ecall,
       equal, Go, halt, IR1_t, IR2_t, IR3_t, IRA, IRB, IRC, JAL, JALR, jump, Lb, less, Lhu, MemToReg,
       multiplexer_9_out, multiplexer_10_out, nand_1_out, not_1_out, not_2_out, riscv_probe_1_p2, RST,
       S_type, W1, W2, W3, \单周期硬布线控制器_1_alu_src ;
  wire [0:0] or_1_out;
  wire [3:0] ALUOP, multiplexer_11_out, multiplexer_12_out, shifter_1_out;
  wire [4:0] multiplexer_4_out, multiplexer_5_out, multiplexer_13_out, multiplexer_14_out;
  wire [11:0] multiplier_1_out;
  wire [12:0] CNT_num;
  wire [15:0] \总周期数 ;
  wire [19:0] multiplier_2_out;
  wire [31:0] adder_2_out, adder_3_out, bit_extender_1_out, bit_extender_2_out, MemBData, MemData, MemHUData,
       multiplexer_1_out, multiplexer_3_out, multiplexer_6_out, multiplexer_7_out, multiplexer_8_out,
       PC_next, regifile_1_r1, result1, signed_imm_b, signed_imm_j;

  Button \u_继续运行  (.out(Go));
  Button _1 (.out(IRA));
  Button _2 (.out(IRB));
  Button _3 (.out(IRC));
  LED #(.active("true")) led_1 (.in(W1));
  LED #(.active("true")) led_2 (.in(W2));
  LED #(.active("true")) led_3 (.in(W3));
  Hex_Digit_Display hex_digit_display_1 (.value(LedData[31:28]));  // open: dp
  ecall_halt ecall_halt_1 (
    .go_button(Go), .ecall(ecall), .equal(equal), .R2_data(MDin), .clk(CLK), .halt(halt), .led_data(LedData));
  not not_1 (not_1_out, halt);
  Hex_Digit_Display hex_digit_display_2 (.value(LedData[27:24]));  // open: dp
  Hex_Digit_Display hex_digit_display_3 (.value(LedData[23:20]));  // open: dp
  Register #(.width(32), .trigger("rising"), .Select("low")) u_PC (
    .D(multiplexer_1_out), .en(not_1_out), .Q(PC), .clk(CLK), .clr(RST));
  Hex_Digit_Display hex_digit_display_4 (.value(LedData[15:12]));  // open: dp
  Hex_Digit_Display hex_digit_display_5 (.value(LedData[19:16]));  // open: dp
  Adder #(.width(32)) adder_1 (.a(PC), .b(32'h4), .out(PC_next));  // open: cin, cout
  Adder #(.width(32)) adder_2 (.a(PC), .b(signed_imm_b), .out(adder_2_out));  // open: cin, cout
  Adder #(.width(32)) adder_3 (.a(PC), .b(signed_imm_j), .out(adder_3_out));  // open: cin, cout
  Hex_Digit_Display hex_digit_display_6 (.value(LedData[11:8]));  // open: dp
  Hex_Digit_Display hex_digit_display_7 (.value(LedData[7:4]));  // open: dp
  // Probe on \总周期数 
  Hex_Digit_Display hex_digit_display_8 (.value(LedData[3:0]));  // open: dp
  // Probe on adder_3_out
  Multiplexer #(.select(2), .width(32), .disabled("Z"), .enable("false")) multiplexer_1 (
    .in0(PC_next), .in1(adder_2_out), .in2(adder_3_out), .in3({result1[31:1], 1'b0}),
    .out(multiplexer_1_out), .sel({jump, or_1_out[0]}));
  or or_1 (or_1_out[0], JALR, branch);
  or or_2 (IR1_t, IR1, IRA);
  or or_3 (jump, JAL, JALR);
  or or_4 (IR2_t, IR2, IRB);
  // RiscV_Probe riscv_probe_1: pin names not known; wires that end beside it: IR, riscv_probe_1_p2
  ROM #(.addrWidth(10), .dataWidth(32), .Select("high")) rom_1 (.addr(PC[11:2]), .data(IR));
  or or_5 (IR3_t, IR3, IRC);
  \单周期硬布线控制器  \u_单周期硬布线控制器_1  (
    .Funct({IR[30], IR[25], IR[14:12]}), .OP(IR[6:2]), .ALU_OP(ALUOP), .MemToReg(MemToReg),
    .MemWrite(MemWrite), .ALU_SRC(\单周期硬布线控制器_1_alu_src ), .RegWrite(RegWrite), .ecall(ecall),
    .S_type(S_type), .Beq(Beq), .in_3(IR[21]), .uret(riscv_probe_1_p2), .Jalr(JALR), .JAL(JAL), .Blt(Blt),
    .Bge(Bge), .Lb(Lb), .Lhu(Lhu), .Bne(Bne));  // open: CSRRSI, CSRRCI
  Multiplexer #(.select(2), .width(32), .disabled("Z"), .enable("false")) multiplexer_2 (
    .in0(result1), .in1(multiplexer_3_out), .in2(PC_next), .out(RDin), .sel({jump, MemToReg}));  // open: in3
  Multiplexer #(.select(2), .width(32), .disabled("Z"), .enable("false")) multiplexer_3 (
    .in0(MemData), .in1(MemHUData), .in2(MemBData), .out(multiplexer_3_out), .sel({Lb, Lhu}));  // open: in3
  assign bit_extender_1_out = {{20{IR[31]}}, IR[31:20]};  // Bit_Extender bit_extender_1
  assign bit_extender_2_out = {{20{1'b0}}, {IR[31:25], IR[11:7]}};  // Bit_Extender bit_extender_2
  Multiplier #(.width(12)) multiplier_1 (
    .a({IR[31], IR[7], IR[30:25], IR[11:8]}), .b(12'h2), .out(multiplier_1_out));  // open: cin, cout
  // Probe on S_type
  Multiplexer #(.select(1), .width(5), .disabled("Z"), .enable("false")) multiplexer_4 (
    .in0(IR[19:15]), .in1(5'b10001), .out(multiplexer_4_out), .sel(ecall));
  assign signed_imm_b = {{20{multiplier_1_out[11]}}, multiplier_1_out};  // Bit_Extender bit_extender_3
  Multiplier #(.width(20)) multiplier_2 (
    .a({IR[31], IR[19:12], IR[20], IR[30:21]}), .b(20'h2), .out(multiplier_2_out));  // open: cin, cout
  Multiplexer #(.select(1), .width(5), .disabled("Z"), .enable("false")) multiplexer_5 (
    .in0(IR[24:20]), .in1(5'b01010), .out(multiplexer_5_out), .sel(ecall));
  assign signed_imm_j = {{12{multiplier_2_out[19]}}, multiplier_2_out};  // Bit_Extender bit_extender_4
  Multiplexer #(.select(1), .width(32), .disabled("Z"), .enable("false")) multiplexer_6 (
    .in0(bit_extender_1_out), .in1(bit_extender_2_out), .out(multiplexer_6_out), .sel(S_type));
  Regifile regifile_1 (
    .Din(RDin), .Clk(CLK), .R1(regifile_1_r1), .R2(MDin), .WE(RegWrite), .W_num(IR[11:7]),
    .R1_num(multiplexer_4_out), .R2_num(multiplexer_5_out));
  Multiplexer #(.select(1), .width(32), .disabled("Z"), .enable("false")) multiplexer_7 (
    .in0(multiplexer_6_out), .in1(32'h22), .out(multiplexer_7_out), .sel(ecall));
  Multiplexer #(.select(1), .width(32), .disabled("Z"), .enable("false")) multiplexer_8 (
    .in0(MDin), .in1(multiplexer_7_out), .out(multiplexer_8_out), .sel(\单周期硬布线控制器_1_alu_src ));
  D_Flip_Flop #(.trigger("high"), .Pre_Clr_Positions("LEGACY"), .NegatePresetClear("false"), .enable("true"), .NewFFLayout("false")) d_ff_1 (.Q(d_ff_1_q));  // open: clk, D, Qn, preset, en, reset
  // Probe on 13'h608
  ALU alu_1 (
    .X(regifile_1_r1), .Y(multiplexer_8_out), .AluOP(ALUOP), .Equal(equal), .Result(result1), .out_6(less));  // open: Result_2, out_4
  Comparator #(.width(13), .mode("unsigned")) comparator_1 (
    .a(CNT_num), .b(13'h608), .eq(comparator_1_eq), .lt(comparator_1_lt));  // open: gt
  Clock #(.highDuration(1), .lowDuration(1)) clock_1 (.out(clock_1_out));
  Counter #(.width(13), .max('h1fff), .ongoal("stay"), .trigger("rising"), .behavior("old")) counter_1 (
    .count(comparator_1_lt), .Q(CNT_num), .clk(clock_1_out));  // open: load, D, carry, clr, preset
  Multiplexer #(.select(1), .width(1), .disabled("Z"), .enable("false")) multiplexer_9 (
    .in0(Bne), .in1(Beq), .out(multiplexer_9_out), .sel(equal));
  or or_6 (branch, multiplexer_9_out, multiplexer_10_out);
  Multiplexer #(.select(1), .width(1), .disabled("Z"), .enable("false")) multiplexer_10 (
    .in0(Bge), .in1(Blt), .out(multiplexer_10_out), .sel(less));
  nand nand_1 (nand_1_out, d_ff_1_q, comparator_1_eq);
  assign CLK = nand_1_out ? clock_1_out : 1'bz;  // Controlled_Buffer controlled_buffer_1
  Pull_Resistor #(.pull(1)) pull_resistor_1 (.node(CLK));
  Multiplexer #(.select(1), .width(4), .disabled("Z"), .enable("false")) multiplexer_11 (
    .in0(4'b0011), .in1(4'b1100), .out(multiplexer_11_out), .sel(result1[1]));
  Shifter #(.width(4), .shift("ll")) shifter_1 (.in(4'b0001), .\dist (result1[1:0]), .out(shifter_1_out));
  not not_2 (not_2_out, halt);
  Counter #(.width(16), .max('hffff), .ongoal("wrap"), .trigger("rising"), .behavior("new")) counter_2 (
    .count(not_2_out), .Q(\总周期数 ), .clk(CLK));  // open: load, D, carry, clr, preset, down
  Multiplexer #(.select(2), .width(4), .disabled("Z"), .enable("false")) multiplexer_12 (
    .in0(4'b1111), .in1(multiplexer_11_out), .in2(shifter_1_out), .out(multiplexer_12_out), .sel({Lb, Lhu}));  // open: in3
  // MIPS_RAM mips_ram_1: pin names not known; wires that end beside it: result1[11:2], MDin, MemWrite, multiplexer_12_out, CLK, MemData
  Pull_Resistor #(.pull(0)) pull_resistor_2 (.node(MemData));
  Multiplexer #(.select(1), .width(5), .disabled("Z"), .enable("false")) multiplexer_13 (
    .in0({5{1'b0}}), .in1(5'b10000), .out(multiplexer_13_out), .sel(result1[1]));
  Shifter #(.width(32), .shift("lr")) shifter_2 (.in(MemData), .\dist (multiplexer_13_out), .out(MemHUData));
  Multiplexer #(.select(2), .width(5), .disabled("Z"), .enable("false")) multiplexer_14 (
    .in0({5{1'b0}}), .in1(5'b01000), .in2(5'b10000), .in3(5'b11000), .out(multiplexer_14_out),
    .sel(result1[1:0]));
  Shifter #(.width(32), .shift("lr")) shifter_3 (.in(MemData), .\dist (multiplexer_14_out), .out(MemBData));

  // Other names for the same wires on the sheet: R2_data[31:0] = MDin

  // Notes on the sheet:
  //   中断源
  //   中断等待指示
  //   数码管输出应该用寄存器锁存，否则显示数据只能一闪而过
  //   数码管输出
  //   指令存储器
  //   指令探针
  //   contents of rom_1 (hex, n*v repeats v):
  //   100493 100006f 100493 200913 300993 100006f 100493 200913 300993 100006f 100493 200913 300993
  //   100006f 100493 200913 300993 3d0000ef 100413 100493 1f49493 900533 2200893 73 24d493 48463 fedff06f
  //   900533 2200893 73 100493 249493 900533 2200893 73 48463 fedff06f 100493 1f49493 900533 2200893 73
  //   4034d493 900533 2200893 73 4044d493 900533 2200893 73 4044d493 900533 2200893 73 4044d493 900533
  //   2200893 73 4044d493 900533 2200893 73 4044d493 900533 2200893 73 4044d493 900533 2200893 73 4044d493
  //   900533 2200893 73 100413 1f41993 41f9d993 433 c00913 300b13 140413 f47413 800293 100313 499993
  //   89e9b3 1300533 2200893 73 406282b3 fe0294e3 140413 f00f93 1f47433 1c41413 800293 100313 49d993
  //   89e9b3 1300533 2200893 73 406282b3 fe0294e3 1c45413 406b0b33 b0463 f95ff06f 2b3 fff2c293 829293
  //   ff2e293 500533 2200893 73 fff00413 493 84a023 140413 448493 84a023 140413 448493 84a023 140413
  //   448493 84a023 140413 448493 84a023 140413 448493 84a023 140413 448493 84a023 140413 448493 84a023
  //   140413 448493 84a023 140413 448493 84a023 140413 448493 84a023 140413 448493 84a023 140413 448493
  //   84a023 140413 448493 84a023 140413 448493 84a023 140413 448493 84a023 140413 448493 140413 433
  //   3c00493 42983 4aa03 149a2b3 28663 134a023 1442023 ffc48493 fe9412e3 800533 2200893 73 440413 3c00493
  //   fc9416e3 a00893 73 100293 300313 800493 849493 7648493 900533 2200893 73 800e13 5494b3 6494b3 900533
  //   2200893 73 fffe0e13 fe0e14e3 a00893 73 100293 300313 800493 849493 7648493 1449493 900533 2200893 73
  //   800e13 54d4b3 64d4b3 900533 2200893 73 fffe0e13 fe0e14e3 a00893 73 313 1000e13 8400493 849493
  //   8348493 400913 891913 490913 849493 8248493 849493 8148493 891913 490913 891913 490913 932023
  //   12484b3 430313 fffe0e13 fe0e18e3 2000e13 313 35483 900533 2200893 73 230313 fffe0e13 fe0e14e3 a00893
  //   73 ff100493 900533 2200893 73 148493 fe04c8e3 a00893 73 413 140413 800533 2200893 73 240413 800533
  //   2200893 73 340413 800533 2200893 73 440413 800533 2200893 73 540413 800533 2200893 73 640413 800533
  //   2200893 73 740413 800533 2200893 73 840413 800533 2200893 2200893 73 8067
  //   JAL
  //   JALR
  //   rs1
  //   rs2
  //   指令字
  //   rd
  //   imm_i
  //   imm_s
  //   imm_b
  //   imm_j
  //   URET
  //   Beq
  //   Bne
  //   ecall
  //   MemToReg
  //   MemWrite
  //   AluOP
  //   AluSrcB
  //   RegWrite
  //   S_type
  //   为方便自动评测，需要输出PC，IR，寄存器堆写如数据RDin
  //   RAM写使能MemWrite、RAM写入数据MDin等信号
  //   控制位
  //   暂停节拍，不能为0
  //   戳工具置1进入计数暂停模式，ctrl+k时钟自动运行到对应节拍暂停
  //   ctrl+k关闭时钟连续运行，将控制位置零，进入单步调试模式调试
  //   用这个时钟源需要去掉电路中的其他时钟源
  //   可计数暂停的时钟源
  //   数据存储器
endmodule

// 单周期硬布线控制器
module \单周期硬布线控制器  (
  input  [4:0] OP,
  input  [4:0] Funct,
  input  in_3,
  output [3:0] ALU_OP,
  output uret,
  output MemToReg,
  output MemWrite,
  output ALU_SRC,
  output Lhu,
  output ecall,
  output Lb,
  output Blt,
  output Bge,
  output RegWrite,
  output S_type,
  output Beq,
  output Bne,
  output Jalr,
  output JAL,
  output CSRRSI,
  output CSRRCI
);

  wire \控制信号自动生成_1_ecall ;

  \运算控制器自动生成  \u_运算控制器自动生成_1  (
    .OP2(OP[0]), .OP3(OP[1]), .OP4(OP[2]), .OP5(OP[3]), .OP6(OP[4]), .F12(Funct[0]), .F13(Funct[1]),
    .F14(Funct[2]), .F25(Funct[3]), .F30(Funct[4]), .S0(ALU_OP[0]), .S1(ALU_OP[1]), .S2(ALU_OP[2]),
    .S3(ALU_OP[3]));
  \控制信号自动生成  \u_控制信号自动生成_1  (
    .OP2(OP[0]), .OP3(OP[1]), .OP4(OP[2]), .OP5(OP[3]), .MemToReg(MemToReg), .OP6(OP[4]), .F12(Funct[0]),
    .F13(Funct[1]), .F14(Funct[2]), .F25(Funct[3]), .F30(Funct[4]), .MemWrite(MemWrite), .ALU_SRC(ALU_SRC),
    .LHU(Lhu), .LB(Lb), .BLT(Blt), .BGE(Bge), .CSRRSI(CSRRSI), .CSRRCI(CSRRCI), .RegWrite(RegWrite),
    .ecall(\控制信号自动生成_1_ecall ), .S_Type(S_type), .BEQ(Beq), .BNE(Bne), .JALR(Jalr), .JAL(JAL));
  and and_1 (uret, in_3, \控制信号自动生成_1_ecall );
  and and_2 (ecall, ~in_3, \控制信号自动生成_1_ecall );  // AND_Gate

  // Other names for the same wires on the sheet: IR21 = in_3; OP_CODE[4:0] = OP

  // Notes on the sheet:
  //   运算器控制器，根据指令生成运算器功能选择信号
  //   控制信号生成，产生数据通路需要的其他控制信号
endmodule

// 运算器控制器
module \运算控制器自动生成  (
  input  OP2,
  input  OP3,
  input  OP4,
  input  OP5,
  input  OP6,
  input  F12,
  input  F13,
  input  F14,
  input  F25,
  input  F30,
  output S0,
  output S1,
  output S2,
  output S3
);

  wire and_1_out, and_2_out, and_3_out, and_4_out, and_5_out, and_6_out, and_7_out, and_8_out, and_9_out,
       and_10_out, and_11_out, and_12_out, and_13_out, and_14_out, and_15_out, and_16_out, and_17_out,
       and_18_out, and_19_out, and_20_out, and_21_out, and_22_out, and_23_out, and_24_out, and_25_out,
       and_26_out, and_27_out, and_28_out, and_29_out, and_30_out, and_31_out, and_32_out, and_33_out,
       and_34_out, and_35_out, and_36_out, and_37_out, and_38_out, and_39_out, and_40_out, and_41_out,
       and_42_out, and_43_out, and_44_out, and_45_out, and_46_out, and_47_out, not_1_out, not_2_out,
       not_3_out, not_4_out, not_5_out, not_6_out, not_7_out, not_8_out, not_9_out, not_10_out, not_11_out,
       not_12_out, not_13_out, not_14_out, not_15_out, not_16_out, not_17_out, not_18_out, not_19_out,
       not_20_out, not_21_out, not_22_out, not_23_out, not_24_out, not_25_out, not_26_out, not_27_out,
       not_28_out, not_29_out, not_30_out, not_31_out, not_32_out, not_33_out, not_34_out, not_35_out,
       not_36_out, not_37_out, not_38_out, not_39_out, not_40_out, not_41_out, not_42_out, not_43_out,
       not_44_out, not_45_out, not_46_out, not_47_out, not_48_out, not_49_out, not_50_out, not_51_out,
       not_52_out, not_53_out, not_54_out, not_55_out, not_56_out, not_57_out, not_58_out, not_59_out,
       not_60_out, not_61_out, not_62_out, not_63_out, not_64_out, not_65_out, not_66_out, not_67_out,
       not_68_out, not_69_out, not_70_out, not_71_out, not_72_out, not_73_out, not_74_out, not_75_out,
       not_76_out, not_77_out, not_78_out, not_79_out, not_80_out, not_81_out, not_82_out, not_83_out,
       not_84_out, not_85_out, not_86_out, not_87_out, not_88_out, not_89_out, not_90_out, not_91_out,
       not_92_out, not_93_out, not_94_out, not_95_out, not_96_out, not_97_out, not_98_out, not_99_out,
       not_100_out, not_101_out, not_102_out, not_103_out, not_104_out, not_105_out, not_106_out,
       not_107_out, not_108_out, not_109_out, not_110_out, not_111_out, not_112_out, not_113_out,
       not_114_out, not_115_out, not_116_out, not_117_out, not_118_out, not_119_out, not_120_out,
       not_121_out, not_122_out, not_123_out, not_124_out, not_125_out, not_126_out, not_127_out,
       not_128_out, not_129_out, not_130_out, not_131_out, not_132_out, not_133_out, not_134_out,
       not_135_out, not_136_out, not_137_out, not_138_out, not_139_out, not_140_out, not_141_out,
       not_142_out, not_143_out, not_144_out, not_145_out, not_146_out, not_147_out, not_148_out,
       not_149_out, not_150_out, not_151_out, not_152_out, not_153_out, not_154_out, not_155_out,
       not_156_out, not_157_out, not_158_out, not_159_out, not_160_out, not_161_out, not_162_out,
       not_163_out, not_164_out, not_165_out, not_166_out, not_167_out, not_168_out, not_169_out,
       not_170_out, not_171_out, not_172_out, not_173_out, not_174_out, not_175_out, not_176_out,
       not_177_out, not_178_out, not_179_out, not_180_out, not_181_out, not_182_out, not_183_out,
       not_184_out, not_185_out, not_186_out, not_187_out, not_188_out, not_189_out, not_190_out,
       not_191_out, not_192_out, not_193_out, not_194_out, not_195_out, not_196_out, not_197_out,
       not_198_out, not_199_out, not_200_out, not_201_out, not_202_out, not_203_out, not_204_out,
       not_205_out, not_206_out, not_207_out, not_208_out, not_209_out, not_210_out, not_211_out,
       not_212_out, not_213_out, not_214_out, not_215_out, not_216_out, not_217_out, not_218_out,
       not_219_out, not_220_out, not_221_out, not_222_out, not_223_out, not_224_out, not_225_out,
       not_226_out, not_227_out, not_228_out, not_229_out, not_230_out, not_231_out, not_232_out,
       not_233_out, not_234_out, not_235_out, not_236_out, not_237_out, not_238_out, not_239_out,
       not_240_out, not_241_out, not_242_out, not_243_out, not_244_out, not_245_out, not_246_out,
       not_247_out, not_248_out, not_249_out, not_250_out, not_251_out, not_252_out, not_253_out,
       not_254_out, not_255_out, not_256_out, not_257_out, not_258_out, not_259_out, not_260_out,
       not_261_out, not_262_out, not_263_out, not_264_out;

  not not_1 (not_1_out, F30);
  not not_2 (not_2_out, F25);
  not not_3 (not_3_out, F14);
  not not_4 (not_4_out, F13);
  not not_5 (not_5_out, F12);
  not not_6 (not_6_out, OP6);
  not not_7 (not_7_out, OP3);
  not not_8 (not_8_out, OP2);
  not not_9 (not_9_out, F30);
  not not_10 (not_10_out, F25);
  not not_11 (not_11_out, OP6);
  not not_12 (not_12_out, OP3);
  not not_13 (not_13_out, OP2);
  not not_14 (not_14_out, F30);
  not not_15 (not_15_out, F25);
  not not_16 (not_16_out, F14);
  not not_17 (not_17_out, F12);
  not not_18 (not_18_out, OP6);
  not not_19 (not_19_out, OP3);
  not not_20 (not_20_out, OP2);
  not not_21 (not_21_out, F14);
  not not_22 (not_22_out, F13);
  not not_23 (not_23_out, F12);
  not not_24 (not_24_out, OP6);
  not not_25 (not_25_out, OP5);
  not not_26 (not_26_out, OP3);
  not not_27 (not_27_out, OP2);
  not not_28 (not_28_out, OP6);
  not not_29 (not_29_out, OP5);
  not not_30 (not_30_out, OP3);
  not not_31 (not_31_out, OP2);
  not not_32 (not_32_out, F13);
  not not_33 (not_33_out, F12);
  not not_34 (not_34_out, OP6);
  not not_35 (not_35_out, OP5);
  not not_36 (not_36_out, OP3);
  not not_37 (not_37_out, OP2);
  not not_38 (not_38_out, F14);
  not not_39 (not_39_out, F12);
  not not_40 (not_40_out, OP6);
  not not_41 (not_41_out, OP5);
  not not_42 (not_42_out, OP3);
  not not_43 (not_43_out, OP2);
  not not_44 (not_44_out, F25);
  not not_45 (not_45_out, F13);
  not not_46 (not_46_out, OP6);
  not not_47 (not_47_out, OP5);
  not not_48 (not_48_out, OP3);
  not not_49 (not_49_out, OP2);
  not not_50 (not_50_out, F14);
  not not_51 (not_51_out, F12);
  not not_52 (not_52_out, OP6);
  not not_53 (not_53_out, OP5);
  not not_54 (not_54_out, OP4);
  not not_55 (not_55_out, OP3);
  not not_56 (not_56_out, OP2);
  not not_57 (not_57_out, F14);
  not not_58 (not_58_out, F12);
  not not_59 (not_59_out, OP6);
  not not_60 (not_60_out, OP4);
  not not_61 (not_61_out, OP3);
  not not_62 (not_62_out, OP2);
  not not_63 (not_63_out, F14);
  not not_64 (not_64_out, F13);
  not not_65 (not_65_out, F12);
  not not_66 (not_66_out, OP4);
  not not_67 (not_67_out, OP3);
  not not_68 (not_68_out, OP3);
  not not_69 (not_69_out, OP2);
  not not_70 (not_70_out, F14);
  not not_71 (not_71_out, F13);
  not not_72 (not_72_out, F12);
  not not_73 (not_73_out, OP6);
  not not_74 (not_74_out, OP5);
  not not_75 (not_75_out, OP4);
  not not_76 (not_76_out, OP3);
  not not_77 (not_77_out, OP2);
  not not_78 (not_78_out, F13);
  not not_79 (not_79_out, OP4);
  not not_80 (not_80_out, OP3);
  not not_81 (not_81_out, OP2);
  not not_82 (not_82_out, F13);
  not not_83 (not_83_out, F12);
  not not_84 (not_84_out, OP4);
  not not_85 (not_85_out, OP3);
  not not_86 (not_86_out, OP2);
  not not_87 (not_87_out, F25);
  not not_88 (not_88_out, F14);
  not not_89 (not_89_out, F13);
  not not_90 (not_90_out, F12);
  not not_91 (not_91_out, OP6);
  not not_92 (not_92_out, OP3);
  not not_93 (not_93_out, OP2);
  not not_94 (not_94_out, F30);
  not not_95 (not_95_out, F25);
  not not_96 (not_96_out, OP6);
  not not_97 (not_97_out, OP3);
  not not_98 (not_98_out, OP2);
  not not_99 (not_99_out, F30);
  not not_100 (not_100_out, F25);
  not not_101 (not_101_out, F14);
  not not_102 (not_102_out, F12);
  not not_103 (not_103_out, OP6);
  not not_104 (not_104_out, OP3);
  not not_105 (not_105_out, OP2);
  not not_106 (not_106_out, OP6);
  not not_107 (not_107_out, OP5);
  not not_108 (not_108_out, OP3);
  not not_109 (not_109_out, OP2);
  not not_110 (not_110_out, F14);
  not not_111 (not_111_out, F12);
  not not_112 (not_112_out, OP6);
  not not_113 (not_113_out, OP5);
  not not_114 (not_114_out, OP3);
  not not_115 (not_115_out, OP2);
  not not_116 (not_116_out, F30);
  not not_117 (not_117_out, F25);
  not not_118 (not_118_out, F13);
  not not_119 (not_119_out, OP6);
  not not_120 (not_120_out, OP5);
  not not_121 (not_121_out, OP3);
  not not_122 (not_122_out, OP2);
  not not_123 (not_123_out, OP3);
  not not_124 (not_124_out, OP2);
  not not_125 (not_125_out, F30);
  not not_126 (not_126_out, F25);
  not not_127 (not_127_out, F13);
  not not_128 (not_128_out, OP6);
  not not_129 (not_129_out, OP3);
  not not_130 (not_130_out, OP2);
  not not_131 (not_131_out, F13);
  not not_132 (not_132_out, OP4);
  not not_133 (not_133_out, OP3);
  not not_134 (not_134_out, OP2);
  not not_135 (not_135_out, F13);
  not not_136 (not_136_out, OP6);
  not not_137 (not_137_out, OP5);
  not not_138 (not_138_out, OP4);
  not not_139 (not_139_out, OP3);
  not not_140 (not_140_out, OP2);
  not not_141 (not_141_out, F13);
  not not_142 (not_142_out, F12);
  not not_143 (not_143_out, OP4);
  not not_144 (not_144_out, OP3);
  not not_145 (not_145_out, OP2);
  not not_146 (not_146_out, F30);
  not not_147 (not_147_out, F25);
  not not_148 (not_148_out, F14);
  not not_149 (not_149_out, F13);
  not not_150 (not_150_out, F12);
  not not_151 (not_151_out, OP6);
  not not_152 (not_152_out, OP3);
  not not_153 (not_153_out, OP2);
  not not_154 (not_154_out, F25);
  not not_155 (not_155_out, F14);
  not not_156 (not_156_out, F13);
  not not_157 (not_157_out, F12);
  not not_158 (not_158_out, OP6);
  not not_159 (not_159_out, OP3);
  not not_160 (not_160_out, OP2);
  not not_161 (not_161_out, F30);
  not not_162 (not_162_out, F25);
  not not_163 (not_163_out, OP6);
  not not_164 (not_164_out, OP3);
  not not_165 (not_165_out, OP2);
  not not_166 (not_166_out, F30);
  not not_167 (not_167_out, F25);
  not not_168 (not_168_out, F14);
  not not_169 (not_169_out, OP6);
  not not_170 (not_170_out, OP3);
  not not_171 (not_171_out, OP2);
  not not_172 (not_172_out, F14);
  not not_173 (not_173_out, F13);
  not not_174 (not_174_out, F12);
  not not_175 (not_175_out, OP6);
  not not_176 (not_176_out, OP5);
  not not_177 (not_177_out, OP3);
  not not_178 (not_178_out, OP2);
  not not_179 (not_179_out, OP6);
  not not_180 (not_180_out, OP5);
  not not_181 (not_181_out, OP3);
  not not_182 (not_182_out, OP2);
  not not_183 (not_183_out, F14);
  not not_184 (not_184_out, F12);
  not not_185 (not_185_out, OP6);
  not not_186 (not_186_out, OP5);
  not not_187 (not_187_out, OP4);
  not not_188 (not_188_out, OP3);
  not not_189 (not_189_out, OP2);
  not not_190 (not_190_out, F14);
  not not_191 (not_191_out, F12);
  not not_192 (not_192_out, OP6);
  not not_193 (not_193_out, OP4);
  not not_194 (not_194_out, OP3);
  not not_195 (not_195_out, OP2);
  not not_196 (not_196_out, F14);
  not not_197 (not_197_out, F13);
  not not_198 (not_198_out, F12);
  not not_199 (not_199_out, OP4);
  not not_200 (not_200_out, OP3);
  not not_201 (not_201_out, OP3);
  not not_202 (not_202_out, OP2);
  not not_203 (not_203_out, F14);
  not not_204 (not_204_out, F13);
  not not_205 (not_205_out, F12);
  not not_206 (not_206_out, OP6);
  not not_207 (not_207_out, OP5);
  not not_208 (not_208_out, OP4);
  not not_209 (not_209_out, OP3);
  not not_210 (not_210_out, OP2);
  not not_211 (not_211_out, F13);
  not not_212 (not_212_out, OP6);
  not not_213 (not_213_out, OP5);
  not not_214 (not_214_out, OP4);
  not not_215 (not_215_out, OP3);
  not not_216 (not_216_out, OP2);
  not not_217 (not_217_out, F30);
  not not_218 (not_218_out, F25);
  not not_219 (not_219_out, F12);
  not not_220 (not_220_out, OP6);
  not not_221 (not_221_out, OP3);
  not not_222 (not_222_out, OP2);
  not not_223 (not_223_out, F30);
  not not_224 (not_224_out, F25);
  not not_225 (not_225_out, F14);
  not not_226 (not_226_out, F12);
  not not_227 (not_227_out, OP6);
  not not_228 (not_228_out, OP3);
  not not_229 (not_229_out, OP2);
  not not_230 (not_230_out, F30);
  not not_231 (not_231_out, F25);
  not not_232 (not_232_out, F14);
  not not_233 (not_233_out, OP6);
  not not_234 (not_234_out, OP3);
  not not_235 (not_235_out, OP2);
  not not_236 (not_236_out, F12);
  not not_237 (not_237_out, OP6);
  not not_238 (not_238_out, OP5);
  not not_239 (not_239_out, OP3);
  not not_240 (not_240_out, OP2);
  not not_241 (not_241_out, F13);
  not not_242 (not_242_out, F12);
  not not_243 (not_243_out, OP6);
  not not_244 (not_244_out, OP5);
  not not_245 (not_245_out, OP3);
  not not_246 (not_246_out, OP2);
  not not_247 (not_247_out, F14);
  not not_248 (not_248_out, F12);
  not not_249 (not_249_out, OP6);
  not not_250 (not_250_out, OP5);
  not not_251 (not_251_out, OP3);
  not not_252 (not_252_out, OP2);
  not not_253 (not_253_out, F12);
  not not_254 (not_254_out, OP3);
  not not_255 (not_255_out, OP2);
  not not_256 (not_256_out, F13);
  not not_257 (not_257_out, OP4);
  not not_258 (not_258_out, OP3);
  not not_259 (not_259_out, OP2);
  not not_260 (not_260_out, F13);
  not not_261 (not_261_out, F12);
  not not_262 (not_262_out, OP4);
  not not_263 (not_263_out, OP3);
  not not_264 (not_264_out, OP2);
  and and_1 (and_1_out, not_1_out, not_2_out, not_3_out, not_4_out, not_5_out, not_6_out, OP5, OP4, not_7_out, not_8_out);
  and and_2 (and_2_out, not_9_out, not_10_out, F14, F13, F12, not_11_out, OP5, OP4, not_12_out, not_13_out);
  and and_3 (and_3_out, not_14_out, not_15_out, not_16_out, F13, not_17_out, not_18_out, OP5, OP4, not_19_out, not_20_out);
  and and_4 (and_4_out, not_21_out, not_22_out, not_23_out, not_24_out, not_25_out, OP4, not_26_out, not_27_out);
  and and_5 (and_5_out, F14, F13, F12, not_28_out, not_29_out, OP4, not_30_out, not_31_out);
  and and_6 (and_6_out, F14, not_32_out, not_33_out, not_34_out, not_35_out, OP4, not_36_out, not_37_out);
  and and_7 (and_7_out, not_38_out, F13, not_39_out, not_40_out, not_41_out, OP4, not_42_out, not_43_out);
  and and_8 (and_8_out, F30, not_44_out, F14, not_45_out, F12, not_46_out, not_47_out, OP4, not_48_out, not_49_out);
  and and_9 (and_9_out, not_50_out, F13, not_51_out, not_52_out, not_53_out, not_54_out, not_55_out, not_56_out);
  and and_10 (and_10_out, not_57_out, F13, not_58_out, not_59_out, OP5, not_60_out, not_61_out, not_62_out);
  and and_11 (and_11_out, not_63_out, not_64_out, not_65_out, OP6, OP5, not_66_out, not_67_out, OP2);
  and and_12 (and_12_out, F14, F13, F12, OP6, OP5, OP4, not_68_out, not_69_out);
  and and_13 (and_13_out, not_70_out, not_71_out, not_72_out, not_73_out, not_74_out, not_75_out, not_76_out, not_77_out);
  and and_14 (and_14_out, F14, not_78_out, F12, OP6, OP5, not_79_out, not_80_out, not_81_out);
  and and_15 (and_15_out, F14, not_82_out, not_83_out, OP6, OP5, not_84_out, not_85_out, not_86_out);
  and and_16 (and_16_out, F30, not_87_out, not_88_out, not_89_out, not_90_out, not_91_out, OP5, OP4, not_92_out, not_93_out);
  and and_17 (and_17_out, not_94_out, not_95_out, F14, F13, F12, not_96_out, OP5, OP4, not_97_out, not_98_out);
  and and_18 (and_18_out, not_99_out, not_100_out, not_101_out, F13, not_102_out, not_103_out, OP5, OP4, not_104_out, not_105_out);
  and and_19 (and_19_out, F14, F13, F12, not_106_out, not_107_out, OP4, not_108_out, not_109_out);
  and and_20 (and_20_out, not_110_out, F13, not_111_out, not_112_out, not_113_out, OP4, not_114_out, not_115_out);
  and and_21 (and_21_out, not_116_out, not_117_out, F14, not_118_out, F12, not_119_out, not_120_out, OP4, not_121_out, not_122_out);
  and and_22 (and_22_out, F14, F13, F12, OP6, OP5, OP4, not_123_out, not_124_out);
  and and_23 (and_23_out, not_125_out, not_126_out, F14, not_127_out, F12, not_128_out, OP5, OP4, not_129_out, not_130_out);
  and and_24 (and_24_out, F14, not_131_out, F12, OP6, OP5, not_132_out, not_133_out, not_134_out);
  and and_25 (and_25_out, F14, not_135_out, F12, not_136_out, not_137_out, not_138_out, not_139_out, not_140_out);
  and and_26 (and_26_out, F14, not_141_out, not_142_out, OP6, OP5, not_143_out, not_144_out, not_145_out);
  and and_27 (and_27_out, not_146_out, not_147_out, not_148_out, not_149_out, not_150_out, not_151_out, OP5, OP4, not_152_out, not_153_out);
  and and_28 (and_28_out, F30, not_154_out, not_155_out, not_156_out, not_157_out, not_158_out, OP5, OP4, not_159_out, not_160_out);
  and and_29 (and_29_out, not_161_out, not_162_out, F14, F13, F12, not_163_out, OP5, OP4, not_164_out, not_165_out);
  and and_30 (and_30_out, not_166_out, not_167_out, not_168_out, F13, F12, not_169_out, OP5, OP4, not_170_out, not_171_out);
  and and_31 (and_31_out, not_172_out, not_173_out, not_174_out, not_175_out, not_176_out, OP4, not_177_out, not_178_out);
  and and_32 (and_32_out, F14, F13, F12, not_179_out, not_180_out, OP4, not_181_out, not_182_out);
  and and_33 (and_33_out, not_183_out, F13, not_184_out, not_185_out, not_186_out, not_187_out, not_188_out, not_189_out);
  and and_34 (and_34_out, not_190_out, F13, not_191_out, not_192_out, OP5, not_193_out, not_194_out, not_195_out);
  and and_35 (and_35_out, not_196_out, not_197_out, not_198_out, OP6, OP5, not_199_out, not_200_out, OP2);
  and and_36 (and_36_out, F14, F13, F12, OP6, OP5, OP4, not_201_out, not_202_out);
  and and_37 (and_37_out, not_203_out, not_204_out, not_205_out, not_206_out, not_207_out, not_208_out, not_209_out, not_210_out);
  and and_38 (and_38_out, F14, not_211_out, F12, not_212_out, not_213_out, not_214_out, not_215_out, not_216_out);
  and and_39 (and_39_out, not_217_out, not_218_out, F14, F13, not_219_out, not_220_out, OP5, OP4, not_221_out, not_222_out);
  and and_40 (and_40_out, not_223_out, not_224_out, not_225_out, F13, not_226_out, not_227_out, OP5, OP4, not_228_out, not_229_out);
  and and_41 (and_41_out, not_230_out, not_231_out, not_232_out, F13, F12, not_233_out, OP5, OP4, not_234_out, not_235_out);
  and and_42 (and_42_out, F14, F13, not_236_out, not_237_out, not_238_out, OP4, not_239_out, not_240_out);
  and and_43 (and_43_out, F14, not_241_out, not_242_out, not_243_out, not_244_out, OP4, not_245_out, not_246_out);
  and and_44 (and_44_out, not_247_out, F13, not_248_out, not_249_out, not_250_out, OP4, not_251_out, not_252_out);
  and and_45 (and_45_out, F14, F13, not_253_out, OP6, OP5, OP4, not_254_out, not_255_out);
  and and_46 (and_46_out, F14, not_256_out, F12, OP6, OP5, not_257_out, not_258_out, not_259_out);
  and and_47 (and_47_out, F14, not_260_out, not_261_out, OP6, OP5, not_262_out, not_263_out, not_264_out);
  or or_1 (S0, and_1_out, and_2_out, and_3_out, and_4_out, and_5_out, and_6_out, and_7_out, and_8_out, and_9_out, and_10_out, and_11_out, and_12_out, and_13_out, and_14_out, and_15_out);
  or or_2 (S1, and_16_out, and_17_out, and_18_out, and_19_out, and_20_out, and_21_out, and_22_out, and_23_out, and_24_out, and_25_out, and_26_out);
  or or_3 (S2, and_27_out, and_28_out, and_29_out, and_30_out, and_31_out, and_32_out, and_33_out, and_34_out, and_35_out, and_36_out, and_37_out, and_38_out);
  or or_4 (S3, and_39_out, and_40_out, and_41_out, and_42_out, and_43_out, and_44_out, and_45_out, and_46_out, and_47_out);
endmodule

// 控制信号生成
module \控制信号自动生成  (
  input  OP2,
  input  OP3,
  input  OP4,
  input  OP5,
  input  OP6,
  input  F12,
  input  F13,
  input  F14,
  input  F25,
  input  F30,
  output MemToReg,
  output MemWrite,
  output ALU_SRC,
  output LHU,
  output LB,
  output BLT,
  output BGE,
  output CSRRSI,
  output CSRRCI,
  output RegWrite,
  output ecall,
  output S_Type,
  output BEQ,
  output BNE,
  output JALR,
  output JAL
);

  wire and_1_out, and_2_out, and_4_out, and_5_out, and_6_out, and_7_out, and_8_out, and_9_out, and_10_out,
       and_11_out, and_12_out, and_19_out, and_20_out, and_21_out, and_22_out, and_23_out, and_24_out,
       and_25_out, and_26_out, and_27_out, and_28_out, not_1_out, not_2_out, not_3_out, not_4_out, not_5_out,
       not_6_out, not_7_out, not_8_out, not_9_out, not_10_out, not_11_out, not_12_out, not_13_out,
       not_14_out, not_15_out, not_16_out, not_17_out, not_18_out, not_19_out, not_20_out, not_21_out,
       not_22_out, not_23_out, not_24_out, not_25_out, not_26_out, not_27_out, not_28_out, not_29_out,
       not_30_out, not_31_out, not_32_out, not_33_out, not_34_out, not_35_out, not_36_out, not_37_out,
       not_38_out, not_39_out, not_40_out, not_41_out, not_42_out, not_43_out, not_44_out, not_45_out,
       not_46_out, not_47_out, not_48_out, not_49_out, not_50_out, not_51_out, not_52_out, not_53_out,
       not_54_out, not_55_out, not_56_out, not_57_out, not_58_out, not_59_out, not_60_out, not_61_out,
       not_62_out, not_63_out, not_64_out, not_65_out, not_66_out, not_67_out, not_68_out, not_69_out,
       not_70_out, not_71_out, not_72_out, not_73_out, not_74_out, not_75_out, not_76_out, not_77_out,
       not_78_out, not_79_out, not_80_out, not_81_out, not_82_out, not_83_out, not_84_out, not_85_out,
       not_86_out, not_87_out, not_88_out, not_89_out, not_90_out, not_91_out, not_92_out, not_93_out,
       not_94_out, not_95_out, not_96_out, not_97_out, not_98_out, not_99_out, not_100_out, not_101_out,
       not_102_out, not_103_out, not_104_out, not_105_out, not_106_out, not_107_out, not_108_out,
       not_109_out, not_110_out, not_111_out, not_112_out, not_113_out, not_114_out, not_115_out,
       not_116_out, not_117_out, not_118_out, not_119_out, not_120_out, not_121_out, not_122_out,
       not_123_out, not_124_out, not_125_out, not_126_out, not_127_out, not_128_out, not_129_out,
       not_130_out, not_131_out, not_132_out, not_133_out, not_134_out, not_135_out, not_136_out,
       not_137_out, not_138_out, not_139_out, not_140_out, not_141_out, not_142_out, not_143_out,
       not_144_out, not_145_out, not_146_out, not_147_out, not_148_out, not_149_out, not_150_out,
       not_151_out, not_152_out, not_153_out, not_154_out, not_155_out, not_156_out, not_157_out,
       not_158_out, not_159_out, not_160_out, not_161_out, not_162_out, not_163_out, not_164_out,
       not_165_out, not_166_out, not_167_out, not_168_out, not_169_out, not_170_out, not_171_out,
       not_172_out, not_173_out, not_174_out, not_175_out, not_176_out, not_177_out;

  not not_1 (not_1_out, OP2);
  not not_2 (not_2_out, OP3);
  not not_3 (not_3_out, OP4);
  not not_4 (not_4_out, OP5);
  not not_5 (not_5_out, OP6);
  not not_6 (not_6_out, F12);
  not not_7 (not_7_out, F14);
  not not_8 (not_8_out, OP2);
  not not_9 (not_9_out, OP3);
  not not_10 (not_10_out, OP4);
  not not_11 (not_11_out, OP5);
  not not_12 (not_12_out, OP6);
  not not_13 (not_13_out, F13);
  not not_14 (not_14_out, OP2);
  not not_15 (not_15_out, OP3);
  not not_16 (not_16_out, OP4);
  not not_17 (not_17_out, OP6);
  not not_18 (not_18_out, F12);
  not not_19 (not_19_out, F14);
  not not_20 (not_20_out, OP2);
  not not_21 (not_21_out, OP3);
  not not_22 (not_22_out, OP5);
  not not_23 (not_23_out, OP6);
  not not_24 (not_24_out, F12);
  not not_25 (not_25_out, F14);
  not not_26 (not_26_out, OP2);
  not not_27 (not_27_out, OP3);
  not not_28 (not_28_out, OP4);
  not not_29 (not_29_out, OP6);
  not not_30 (not_30_out, F12);
  not not_31 (not_31_out, F14);
  not not_32 (not_32_out, OP2);
  not not_33 (not_33_out, OP3);
  not not_34 (not_34_out, OP4);
  not not_35 (not_35_out, OP5);
  not not_36 (not_36_out, OP6);
  not not_37 (not_37_out, F13);
  not not_38 (not_38_out, OP2);
  not not_39 (not_39_out, OP3);
  not not_40 (not_40_out, OP5);
  not not_41 (not_41_out, OP6);
  not not_42 (not_42_out, F12);
  not not_43 (not_43_out, OP2);
  not not_44 (not_44_out, OP3);
  not not_45 (not_45_out, OP5);
  not not_46 (not_46_out, OP6);
  not not_47 (not_47_out, F13);
  not not_48 (not_48_out, F25);
  not not_49 (not_49_out, F30);
  not not_50 (not_50_out, OP2);
  not not_51 (not_51_out, OP3);
  not not_52 (not_52_out, OP5);
  not not_53 (not_53_out, OP6);
  not not_54 (not_54_out, F25);
  not not_55 (not_55_out, OP2);
  not not_56 (not_56_out, OP3);
  not not_57 (not_57_out, OP5);
  not not_58 (not_58_out, OP6);
  not not_59 (not_59_out, OP2);
  not not_60 (not_60_out, OP3);
  not not_61 (not_61_out, F12);
  not not_62 (not_62_out, F13);
  not not_63 (not_63_out, F14);
  not not_64 (not_64_out, F25);
  not not_65 (not_65_out, F30);
  not not_66 (not_66_out, OP3);
  not not_67 (not_67_out, OP4);
  not not_68 (not_68_out, F12);
  not not_69 (not_69_out, F13);
  not not_70 (not_70_out, F14);
  not not_71 (not_71_out, OP2);
  not not_72 (not_72_out, OP3);
  not not_73 (not_73_out, OP4);
  not not_74 (not_74_out, OP5);
  not not_75 (not_75_out, OP6);
  not not_76 (not_76_out, F13);
  not not_77 (not_77_out, OP2);
  not not_78 (not_78_out, OP3);
  not not_79 (not_79_out, OP4);
  not not_80 (not_80_out, OP5);
  not not_81 (not_81_out, OP6);
  not not_82 (not_82_out, F12);
  not not_83 (not_83_out, F13);
  not not_84 (not_84_out, F14);
  not not_85 (not_85_out, OP2);
  not not_86 (not_86_out, OP3);
  not not_87 (not_87_out, OP4);
  not not_88 (not_88_out, F12);
  not not_89 (not_89_out, F13);
  not not_90 (not_90_out, OP2);
  not not_91 (not_91_out, OP3);
  not not_92 (not_92_out, OP4);
  not not_93 (not_93_out, F13);
  not not_94 (not_94_out, F12);
  not not_95 (not_95_out, OP3);
  not not_96 (not_96_out, OP2);
  not not_97 (not_97_out, OP3);
  not not_98 (not_98_out, OP2);
  not not_99 (not_99_out, OP2);
  not not_100 (not_100_out, OP3);
  not not_101 (not_101_out, OP5);
  not not_102 (not_102_out, OP6);
  not not_103 (not_103_out, F12);
  not not_104 (not_104_out, F14);
  not not_105 (not_105_out, OP2);
  not not_106 (not_106_out, OP3);
  not not_107 (not_107_out, OP4);
  not not_108 (not_108_out, OP5);
  not not_109 (not_109_out, OP6);
  not not_110 (not_110_out, F13);
  not not_111 (not_111_out, OP2);
  not not_112 (not_112_out, OP3);
  not not_113 (not_113_out, OP5);
  not not_114 (not_114_out, OP6);
  not not_115 (not_115_out, F12);
  not not_116 (not_116_out, OP2);
  not not_117 (not_117_out, OP3);
  not not_118 (not_118_out, OP6);
  not not_119 (not_119_out, F12);
  not not_120 (not_120_out, F13);
  not not_121 (not_121_out, F14);
  not not_122 (not_122_out, F25);
  not not_123 (not_123_out, OP2);
  not not_124 (not_124_out, OP3);
  not not_125 (not_125_out, OP5);
  not not_126 (not_126_out, OP6);
  not not_127 (not_127_out, F25);
  not not_128 (not_128_out, OP2);
  not not_129 (not_129_out, OP3);
  not not_130 (not_130_out, OP5);
  not not_131 (not_131_out, OP6);
  not not_132 (not_132_out, OP2);
  not not_133 (not_133_out, OP3);
  not not_134 (not_134_out, OP6);
  not not_135 (not_135_out, F13);
  not not_136 (not_136_out, F25);
  not not_137 (not_137_out, F30);
  not not_138 (not_138_out, OP2);
  not not_139 (not_139_out, OP3);
  not not_140 (not_140_out, OP6);
  not not_141 (not_141_out, F25);
  not not_142 (not_142_out, F30);
  not not_143 (not_143_out, OP4);
  not not_144 (not_144_out, F12);
  not not_145 (not_145_out, F13);
  not not_146 (not_146_out, F14);
  not not_147 (not_147_out, OP4);
  not not_148 (not_148_out, OP2);
  not not_149 (not_149_out, OP3);
  not not_150 (not_150_out, F12);
  not not_151 (not_151_out, F13);
  not not_152 (not_152_out, F14);
  not not_153 (not_153_out, F25);
  not not_154 (not_154_out, F30);
  not not_155 (not_155_out, OP2);
  not not_156 (not_156_out, OP3);
  not not_157 (not_157_out, OP4);
  not not_158 (not_158_out, OP6);
  not not_159 (not_159_out, F12);
  not not_160 (not_160_out, F14);
  not not_161 (not_161_out, OP2);
  not not_162 (not_162_out, OP3);
  not not_163 (not_163_out, OP4);
  not not_164 (not_164_out, F12);
  not not_165 (not_165_out, F13);
  not not_166 (not_166_out, F14);
  not not_167 (not_167_out, OP2);
  not not_168 (not_168_out, OP3);
  not not_169 (not_169_out, OP4);
  not not_170 (not_170_out, F13);
  not not_171 (not_171_out, F14);
  not not_172 (not_172_out, OP3);
  not not_173 (not_173_out, OP4);
  not not_174 (not_174_out, F12);
  not not_175 (not_175_out, F13);
  not not_176 (not_176_out, F14);
  not not_177 (not_177_out, OP4);
  and and_1 (and_1_out, not_1_out, not_2_out, not_3_out, not_4_out, not_5_out, not_6_out, not_7_out);
  and and_2 (and_2_out, not_8_out, not_9_out, not_10_out, not_11_out, not_12_out, F12, not_13_out, F14);
  and and_3 (MemWrite, not_14_out, not_15_out, not_16_out, OP5, not_17_out, not_18_out, F13, not_19_out);
  and and_4 (and_4_out, not_20_out, not_21_out, not_22_out, not_23_out, not_24_out, not_25_out);
  and and_5 (and_5_out, not_26_out, not_27_out, not_28_out, not_29_out, not_30_out, F13, not_31_out);
  and and_6 (and_6_out, not_32_out, not_33_out, not_34_out, not_35_out, not_36_out, F12, not_37_out, F14);
  and and_7 (and_7_out, not_38_out, not_39_out, OP4, not_40_out, not_41_out, not_42_out);
  and and_8 (and_8_out, not_43_out, not_44_out, OP4, not_45_out, not_46_out, not_47_out, not_48_out, not_49_out);
  and and_9 (and_9_out, not_50_out, not_51_out, OP4, not_52_out, not_53_out, F14, not_54_out);
  and and_10 (and_10_out, not_55_out, not_56_out, OP4, not_57_out, not_58_out, F13, F14);
  and and_11 (and_11_out, not_59_out, not_60_out, OP4, OP5, OP6, not_61_out, not_62_out, not_63_out, not_64_out, not_65_out);
  and and_12 (and_12_out, OP2, not_66_out, not_67_out, OP5, OP6, not_68_out, not_69_out, not_70_out);
  and and_13 (LHU, not_71_out, not_72_out, not_73_out, not_74_out, not_75_out, F12, not_76_out, F14);
  and and_14 (LB, not_77_out, not_78_out, not_79_out, not_80_out, not_81_out, not_82_out, not_83_out, not_84_out);
  and and_15 (BLT, not_85_out, not_86_out, not_87_out, OP5, OP6, not_88_out, not_89_out, F14);
  and and_16 (BGE, not_90_out, not_91_out, not_92_out, OP5, OP6, F12, not_93_out, F14);
  and and_17 (CSRRSI, F14, F13, not_94_out, OP6, OP5, OP4, not_95_out, not_96_out);
  and and_18 (CSRRCI, F14, F13, F12, OP6, OP5, OP4, not_97_out, not_98_out);
  and and_19 (and_19_out, not_99_out, not_100_out, not_101_out, not_102_out, not_103_out, not_104_out);
  and and_20 (and_20_out, not_105_out, not_106_out, not_107_out, not_108_out, not_109_out, F12, not_110_out, F14);
  and and_21 (and_21_out, not_111_out, not_112_out, OP4, not_113_out, not_114_out, not_115_out);
  and and_22 (and_22_out, not_116_out, not_117_out, OP4, not_118_out, not_119_out, not_120_out, not_121_out, not_122_out);
  and and_23 (and_23_out, not_123_out, not_124_out, OP4, not_125_out, not_126_out, F14, not_127_out);
  and and_24 (and_24_out, not_128_out, not_129_out, OP4, not_130_out, not_131_out, F13, F14);
  and and_25 (and_25_out, not_132_out, not_133_out, OP4, not_134_out, F12, not_135_out, not_136_out, not_137_out);
  and and_26 (and_26_out, not_138_out, not_139_out, OP4, OP5, not_140_out, F13, not_141_out, not_142_out);
  and and_27 (and_27_out, OP2, not_143_out, OP5, OP6, not_144_out, not_145_out, not_146_out);
  and and_28 (and_28_out, OP2, OP3, not_147_out, OP5, OP6);
  and and_29 (ecall, not_148_out, not_149_out, OP4, OP5, OP6, not_150_out, not_151_out, not_152_out, not_153_out, not_154_out);
  and and_30 (S_Type, not_155_out, not_156_out, not_157_out, OP5, not_158_out, not_159_out, F13, not_160_out);
  and and_31 (BEQ, not_161_out, not_162_out, not_163_out, OP5, OP6, not_164_out, not_165_out, not_166_out);
  and and_32 (BNE, not_167_out, not_168_out, not_169_out, OP5, OP6, F12, not_170_out, not_171_out);
  and and_33 (JALR, OP2, not_172_out, not_173_out, OP5, OP6, not_174_out, not_175_out, not_176_out);
  and and_34 (JAL, OP2, OP3, not_177_out, OP5, OP6);
  or or_1 (MemToReg, and_1_out, and_2_out);
  or or_2 (ALU_SRC, and_4_out, and_5_out, and_6_out, and_7_out, and_8_out, and_9_out, and_10_out, and_11_out, and_12_out);
  or or_3 (RegWrite, and_19_out, and_20_out, and_21_out, and_22_out, and_23_out, and_24_out, and_25_out, and_26_out, and_27_out, and_28_out);
endmodule

// ALU
module ALU (
  input  [31:0] X,
  input  [31:0] Y,
  input  [3:0] AluOP,
  output out_4,
  output Equal,
  output out_6,
  output [31:0] Result,
  output [31:0] Result_2
);

  wire [0:0] comparator_1_lt, comparator_2_lt;
  wire [31:0] adder_1_out, AND_out, divider_1_out, divider_1_rem, multiplier_1_cout, multiplier_1_out,
       NOR_out, OR_out, shifter_1_out, shifter_2_out, shifter_3_out, subtractor_1_out, XOR_out;

  assign AND_out = X & Y;  // AND_Gate AND, 32 bits wide
  assign OR_out = X | Y;  // OR_Gate OR, 32 bits wide
  Shifter #(.width(32), .shift("ll")) shifter_1 (.in(X), .\dist (Y[4:0]), .out(shifter_1_out));
  Shifter #(.width(32), .shift("ar")) shifter_2 (.in(X), .\dist (Y[4:0]), .out(shifter_2_out));
  Shifter #(.width(32), .shift("lr")) shifter_3 (.in(X), .\dist (Y[4:0]), .out(shifter_3_out));
  Multiplier #(.width(32)) multiplier_1 (.a(X), .b(Y), .out(multiplier_1_out), .cout(multiplier_1_cout));  // open: cin
  Divider #(.width(32)) divider_1 (.a(X), .b(Y), .out(divider_1_out), .rem(divider_1_rem));  // open: upper
  Adder #(.width(32)) adder_1 (.a(X), .b(Y), .out(adder_1_out));  // open: cin, cout
  Subtractor #(.width(32)) subtractor_1 (.a(X), .b(Y), .out(subtractor_1_out));  // open: bin, bout
  assign XOR_out = X ^ Y;  // XOR_Gate XOR, 32 bits wide
  assign NOR_out = ~(X | Y);  // NOR_Gate NOR, 32 bits wide
  Comparator #(.width(32), .mode("twosComplement")) comparator_1 (
    .a(X), .b(Y), .eq(Equal), .lt(comparator_1_lt[0]));  // open: gt
  Comparator #(.width(32), .mode("unsigned")) comparator_2 (.a(X), .b(Y), .lt(comparator_2_lt[0]));  // open: gt, eq
  Multiplexer #(.select(4), .width(32), .disabled("Z"), .enable("false")) multiplexer_1 (
    .in0(shifter_1_out), .in1(shifter_2_out), .in2(shifter_3_out), .in3(multiplier_1_out),
    .in4(divider_1_out), .in5(adder_1_out), .in6(subtractor_1_out), .in7(AND_out), .in8(OR_out),
    .in9(XOR_out), .in10(NOR_out), .in11({{31{1'b0}}, comparator_1_lt[0]}),
    .in12({{31{1'b0}}, comparator_2_lt[0]}), .in13({32{1'b0}}), .in14({32{1'b0}}), .in15({32{1'b0}}),
    .out(Result), .sel(AluOP));
  Multiplexer #(.select(4), .width(32), .disabled("Z"), .enable("false")) multiplexer_2 (
    .in0({32{1'b0}}), .in1({32{1'b0}}), .in2({32{1'b0}}), .in3(multiplier_1_cout), .in4(divider_1_rem),
    .in5({32{1'b0}}), .in6({32{1'b0}}), .in7({32{1'b0}}), .in8({32{1'b0}}), .in9({32{1'b0}}),
    .in10({32{1'b0}}), .in11({32{1'b0}}), .in12({32{1'b0}}), .in13({32{1'b0}}), .in14({32{1'b0}}),
    .in15({32{1'b0}}), .out(Result_2), .sel(AluOP));
  Multiplexer #(.select(4), .width(1), .disabled("Z"), .enable("false")) multiplexer_3 (
    .in0(1'b0), .in1(1'b0), .in2(1'b0), .in3(1'b0), .in4(1'b0), .in5(1'b0), .in6(1'b0), .in7(1'b0),
    .in8(1'b0), .in9(1'b0), .in10(1'b0), .in11(comparator_1_lt[0]), .in12(comparator_2_lt[0]), .in13(1'b0),
    .in14(1'b0), .in15(1'b0), .out(out_6), .sel(AluOP));
  not not_1 (out_4, out_6);

  // Other names for the same wires on the sheet: Result2[31:0] = Result_2; S[3:0] = AluOP; tunnel = out_6;
  //   tunnel_t = out_4

  // Notes on the sheet:
  //   不要改变此引脚区域内容，也不要改变ALU封装形式
  //   输入引脚
  //   输出引脚
endmodule

module Regifile (
  input  [31:0] Din,
  input  Clk,
  input  WE,
  input  [4:0] R1_num,
  input  [4:0] R2_num,
  input  [4:0] W_num,
  output [31:0] R1,
  output [31:0] R2
);

  // RegisterFile registerfile_1: pin names not known; wires that end beside it: Din, Clk, WE, W_num, R1_num, R2_num, R1, R2
endmodule

module \理想流水线  (
  output RegWrite,
  output MemWrite,
  output [31:0] IF_PC,
  output [31:0] ID_PC,
  output [31:0] EX_PC,
  output [31:0] M_PC,
  output [31:0] WB_PC,
  output [31:0] RDin,
  output [31:0] MDin,
  output [31:0] LedData
);

  wire AluSrcB, Beq, Bge, Blt, Bne, CLK, clock_1_out, comparator_1_eq, comparator_1_lt, d_ff_1_q, equal,
       EX_AluSrcB, EX_Beq, EX_Bge, EX_Blt, EX_Bne, EX_ecall, EX_JAL, EX_Lb, EX_Lhu, ex_mem_1_jal_out,
       ex_mem_1_jalr_out, ex_mem_1_memtoreg_out, ex_mem_1_regwrite_out, EX_MemToReg, EX_MemWrite,
       EX_RegWrite, EX_S_type, EX_URET, Go, halt, IR1, IR2, IR3, less, MEM_Lb, multiplexer_10_out,
       multiplexer_12_out, nand_1_out, nop, not_1_out, not_2_out, RST, W1, W2, W3, WB_JAL, WB_JALR, WB_Lb,
       WB_Lhu, WB_MemToReg;
  wire [0:0] or_1_out;
  wire [1:0] BranchToken;
  wire [1:1] or_2_out;
  wire [3:0] AluOP, EX_AluOP, multiplexer_14_out, multiplexer_15_out, shifter_3_out;
  wire [4:0] ex_mem_1_rd_out, EX_RD, multiplexer_2_out, multiplexer_3_out, multiplexer_11_out,
       multiplexer_13_out, RD, WB_RD;
  wire [11:0] multiplier_1_out;
  wire [12:0] CNT_num;
  wire [15:0] \LoadUse次数 , \总周期数 , \插入气泡数 , \无条件分支数 , \条件分支成功数 ;
  wire [18:0] control_sign, \id_ex气泡生成器_1_control_sign_out ;
  wire [19:0] multiplier_2_out;
  wire [31:0] adder_1_out, adder_2_out, adder_3_out, bit_extender_1_out, bit_extender_2_out,
       bit_extender_3_out, bit_extender_4_out, EX_IR, ex_mem_1_result_out, EX_result, id_ex_1_rs1_out, ID_IR,
       IF_ID_instr_out, IF_IR, imm, MEM_IR, MemBData, MemData, MemHUData, mips_ram_1_p6, multiplexer_1_out,
       multiplexer_4_out, multiplexer_5_out, multiplexer_6_out, multiplexer_8_out, multiplexer_9_out,
       R2_data, regifile_1_r1, regifile_1_r2, result, rom_1_data, WB_IR;

  Button \u_总复位  (.out(RST));
  Button _1 (.out(IR1));
  Button _2 (.out(IR2));
  Button _3 (.out(IR3));
  // Probe on \总周期数 
  // Probe on \总周期数 
  Button \u_继续运行  (.out(Go));
  LED #(.active("true")) led_1 (.in(W1));
  LED #(.active("true")) led_2 (.in(W2));
  LED #(.active("true")) led_3 (.in(W3));
  Hex_Digit_Display hex_digit_display_1 (.value(LedData[31:28]));  // open: dp
  // Probe on IF_PC[19:0]
  // RiscV_Probe riscv_probe_1: pin names not known; wires that end beside it: IF_IR
  Hex_Digit_Display hex_digit_display_2 (.value(LedData[23:20]));  // open: dp
  Hex_Digit_Display hex_digit_display_3 (.value(LedData[27:24]));  // open: dp
  // Probe on ID_PC[19:0]
  // RiscV_Probe riscv_probe_2: pin names not known; wires that end beside it: ID_IR
  Hex_Digit_Display hex_digit_display_4 (.value(LedData[15:12]));  // open: dp
  Hex_Digit_Display hex_digit_display_5 (.value(LedData[19:16]));  // open: dp
  not not_1 (not_1_out, 1'b0);
  Hex_Digit_Display hex_digit_display_6 (.value(LedData[7:4]));  // open: dp
  Hex_Digit_Display hex_digit_display_7 (.value(LedData[11:8]));  // open: dp
  // Probe on EX_PC[19:0]
  // RiscV_Probe riscv_probe_3: pin names not known; wires that end beside it: EX_IR
  Register #(.width(32), .trigger("rising"), .Select("low")) PC (
    .D(multiplexer_1_out), .en(not_1_out), .Q(IF_PC), .clk(CLK), .clr(RST));
  Hex_Digit_Display hex_digit_display_8 (.value(LedData[3:0]));  // open: dp
  Adder #(.width(32)) adder_1 (.a(IF_PC), .b(32'h4), .out(adder_1_out));  // open: cin, cout
  Adder #(.width(32)) adder_2 (.a(EX_PC), .b(imm), .out(adder_2_out));  // open: cin, cout
  // Probe on \总周期数 
  // Probe on M_PC[19:0]
  // RiscV_Probe riscv_probe_4: pin names not known; wires that end beside it: MEM_IR
  // Probe on \总周期数 
  // Probe on \无条件分支数 
  // Probe on \条件分支成功数 
  // Probe on \插入气泡数 
  // Probe on \LoadUse次数 
  // Probe on IF_PC[11:0]
  // Probe on WB_PC[19:0]
  // RiscV_Probe riscv_probe_5: pin names not known; wires that end beside it: WB_IR
  Multiplexer #(.select(2), .width(32), .disabled("Z"), .enable("false")) multiplexer_1 (
    .in0(adder_1_out), .in1(adder_2_out), .in2({EX_result[31:1], 1'b0}), .out(multiplexer_1_out),
    .sel(BranchToken));  // open: in3
  // Probe on EX_PC[11:0]
  // Probe on ID_PC[11:0]
  ecall_halt ecall_halt_1 (
    .go_button(Go), .ecall(EX_ecall), .equal(equal), .R2_data(R2_data), .clk(CLK), .halt(halt),
    .led_data(LedData));
  // Probe on M_PC[11:0]
  D_Flip_Flop #(.trigger("high"), .Pre_Clr_Positions("LEGACY"), .NegatePresetClear("false"), .enable("true"), .NewFFLayout("false")) d_ff_1 (.Q(d_ff_1_q));  // open: clk, D, Qn, preset, en, reset
  // Probe on 13'h10
  ROM #(.addrWidth(10), .dataWidth(32), .Select("high")) rom_1 (.addr(IF_PC[11:2]), .data(rom_1_data));
  // Probe on WB_PC[11:0]
  Comparator #(.width(13), .mode("twosComplement")) comparator_1 (
    .a(CNT_num), .b(13'h10), .eq(comparator_1_eq), .lt(comparator_1_lt));  // open: gt
  Clock #(.highDuration(1), .lowDuration(1)) clock_1 (.out(clock_1_out));
  IF_ID IF_ID (
    .pc(IF_PC), .instr(rom_1_data), .clk(CLK), .pc_out(ID_PC),
    .instr_out({IF_ID_instr_out[31:12], RD, IF_ID_instr_out[6:0]}), .halt(1'b0));
  // Probe on IF_PC
  nand nand_1 (nand_1_out, d_ff_1_q, comparator_1_eq);
  Counter #(.width(13), .max('h1fff), .ongoal("stay"), .trigger("rising"), .behavior("old")) counter_1 (
    .count(comparator_1_lt), .Q(CNT_num), .clk(clock_1_out));  // open: load, D, carry, clr, preset
  assign CLK = nand_1_out ? clock_1_out : 1'bz;  // Controlled_Buffer controlled_buffer_1
  // RiscV_Probe riscv_probe_6: pin names not known; wires that end beside it: halt, CLK, ID_PC, {IF_ID_instr_out[31:12], RD, IF_ID_instr_out[6:0]}
  Pull_Resistor #(.pull(1)) pull_resistor_1 (.node(CLK));
  \冲突识别器  \u_冲突识别器_1  (.IR({IF_ID_instr_out[31:12], RD, IF_ID_instr_out[6:0]}), .stall(nop));  // open: CLK
  not not_2 (not_2_out, halt);
  Counter #(.width(16), .max('hffff), .ongoal("wrap"), .trigger("rising"), .behavior("new")) counter_2 (
    .count(not_2_out), .Q(\总周期数 ), .clk(CLK));  // open: load, D, carry, clr, preset, down
  \单周期硬布线控制器  \u_单周期硬布线控制器_1  (
    .Funct({IF_ID_instr_out[30], IF_ID_instr_out[25], IF_ID_instr_out[14:12]}), .OP(IF_ID_instr_out[6:2]),
    .ALU_OP(AluOP), .MemToReg(control_sign[8]), .MemWrite(control_sign[9]), .ALU_SRC(AluSrcB),
    .RegWrite(control_sign[15]), .ecall(control_sign[18]), .S_type(control_sign[17]), .Beq(Beq),
    .in_3(IF_ID_instr_out[21]), .uret(control_sign[5]), .Jalr(control_sign[1]), .JAL(control_sign[0]),
    .Blt(Blt), .Bge(Bge), .Lb(control_sign[4]), .Lhu(control_sign[16]), .Bne(Bne));  // open: CSRRSI, CSRRCI
  Multiplier #(.width(12)) multiplier_1 (
    .a({IF_ID_instr_out[31], RD[0], IF_ID_instr_out[30:25], RD[4:1]}), .b(12'h2), .out(multiplier_1_out));  // open: cin, cout
  Multiplier #(.width(20)) multiplier_2 (
    .a({IF_ID_instr_out[31], IF_ID_instr_out[19:12], IF_ID_instr_out[20], IF_ID_instr_out[30:21]}),
    .b(20'h2), .out(multiplier_2_out));  // open: cin, cout
  Multiplexer #(.select(1), .width(5), .disabled("Z"), .enable("false")) multiplexer_2 (
    .in0(IF_ID_instr_out[19:15]), .in1(5'b10001), .out(multiplexer_2_out), .sel(control_sign[18]));
  assign bit_extender_1_out = {{20{IF_ID_instr_out[31]}}, IF_ID_instr_out[31:20]};  // Bit_Extender bit_extender_1
  assign bit_extender_2_out = {{20{1'b0}}, {IF_ID_instr_out[31:25], RD}};  // Bit_Extender bit_extender_2
  assign bit_extender_3_out = {{20{multiplier_1_out[11]}}, multiplier_1_out};  // Bit_Extender bit_extender_3
  assign bit_extender_4_out = {{12{multiplier_2_out[19]}}, multiplier_2_out};  // Bit_Extender bit_extender_4
  Multiplexer #(.select(1), .width(5), .disabled("Z"), .enable("false")) multiplexer_3 (
    .in0(IF_ID_instr_out[24:20]), .in1(5'b01010), .out(multiplexer_3_out), .sel(control_sign[18]));
  Multiplexer #(.select(1), .width(32), .disabled("Z"), .enable("false")) multiplexer_4 (
    .in0(bit_extender_1_out), .in1(bit_extender_2_out), .out(multiplexer_4_out), .sel(control_sign[17]));
  Regifile regifile_1 (
    .Din(RDin), .Clk(CLK), .R1(regifile_1_r1), .R2(regifile_1_r2), .WE(RegWrite), .W_num(WB_RD),
    .R1_num(multiplexer_2_out), .R2_num(multiplexer_3_out));
  Multiplexer #(.select(1), .width(32), .disabled("Z"), .enable("false")) multiplexer_5 (
    .in0(multiplexer_4_out), .in1(32'h22), .out(multiplexer_5_out), .sel(control_sign[18]));
  Adder #(.width(32)) adder_3 (.a(WB_PC), .b(32'h4), .out(adder_3_out));  // open: cin, cout
  \ID_EX气泡生成器  \id_ex气泡生成器_1  (
    .control_sign_in({control_sign[18:15], AluSrcB, AluOP, control_sign[9:8], Bne, Beq, control_sign[5:4], Bge, Blt, control_sign[1:0]}),
    .control_sign_out(\id_ex气泡生成器_1_control_sign_out ), .data_harzard(1'b0), .branch_harzard(1'b0), .nop(nop));  // open: PC_in, PC_out
  Multiplexer #(.select(2), .width(32), .disabled("Z"), .enable("false")) multiplexer_6 (
    .in0(multiplexer_5_out), .in1(bit_extender_3_out), .in2(bit_extender_4_out), .out(multiplexer_6_out),
    .sel({control_sign[0], or_1_out[0]}));  // open: in3
  Multiplexer #(.select(2), .width(32), .disabled("Z"), .enable("false")) multiplexer_7 (
    .in0(result), .in1(multiplexer_8_out), .in2(adder_3_out), .out(RDin), .sel({or_2_out[1], WB_MemToReg}));  // open: in3
  Multiplexer #(.select(2), .width(32), .disabled("Z"), .enable("false")) multiplexer_8 (
    .in0(MemData), .in1(MemHUData), .in2(MemBData), .out(multiplexer_8_out), .sel({WB_Lb, WB_Lhu}));  // open: in3
  or or_1 (or_1_out[0], Bne, Beq, Bge, Blt);
  ID_EX id_ex_1 (
    .PC_in(ID_PC), .RS1_in(regifile_1_r1), .RS2_in(regifile_1_r2), .RD_in(RD),
    .control_sign_in(\id_ex气泡生成器_1_control_sign_out ), .Imm_in(multiplexer_6_out), .clk(CLK), .PC_out(EX_PC),
    .RS1_out(id_ex_1_rs1_out), .RS2_out(R2_data), .RD_out(EX_RD),
    .control_sign_out({EX_ecall, EX_S_type, EX_Lhu, EX_RegWrite, EX_AluSrcB, EX_AluOP, EX_MemWrite, EX_MemToReg, EX_Bne, EX_Beq, EX_URET, EX_Lb, EX_Bge, EX_Blt, BranchToken[1], EX_JAL}),
    .Imm_out(imm), .halt(1'b0));
  or or_2 (or_2_out[1], WB_JAL, WB_JALR);
  Multiplexer #(.select(1), .width(32), .disabled("Z"), .enable("false")) multiplexer_9 (
    .in0(R2_data), .in1(imm), .out(multiplexer_9_out), .sel(EX_AluSrcB));
  ALU alu_1 (
    .X(id_ex_1_rs1_out), .Y(multiplexer_9_out), .AluOP(EX_AluOP), .Equal(equal), .Result(EX_result),
    .out_6(less));  // open: Result_2, out_4
  Pull_Resistor #(.pull(0)) pull_resistor_2 (.node(MemData));
  EX_MEM ex_mem_1 (
    .pc_in(EX_PC), .result_in(EX_result), .wd_in(R2_data), .RD_in(EX_RD), .RegWrite_in(EX_RegWrite),
    .MemToReg_in(EX_MemToReg), .MemWrite_in(EX_MemWrite), .jal_in(EX_JAL), .jalr_in(BranchToken[1]),
    .lhu_in(EX_Lhu), .lb_in(EX_Lb), .CLK(CLK), .pc_out(M_PC), .result_out(ex_mem_1_result_out),
    .wd_out(MDin), .RD_out(ex_mem_1_rd_out), .RegWrite_out(ex_mem_1_regwrite_out),
    .MemToReg_out(ex_mem_1_memtoreg_out), .MemWrite_out(MemWrite), .jal_out(ex_mem_1_jal_out),
    .jalr_out(ex_mem_1_jalr_out), .lhu_out(MEM_Lb), .lb_out(MEM_Lb));
  or or_3 (BranchToken[0], multiplexer_10_out, EX_JAL, multiplexer_12_out);
  Multiplexer #(.select(1), .width(1), .disabled("Z"), .enable("false")) multiplexer_10 (
    .in0(EX_Bne), .in1(EX_Beq), .out(multiplexer_10_out), .sel(equal));
  Multiplexer #(.select(1), .width(5), .disabled("Z"), .enable("false")) multiplexer_11 (
    .in0({5{1'b0}}), .in1(5'b10000), .out(multiplexer_11_out), .sel(result[1]));
  Multiplexer #(.select(1), .width(1), .disabled("Z"), .enable("false")) multiplexer_12 (
    .in0(EX_Bge), .in1(EX_Blt), .out(multiplexer_12_out), .sel(less));
  Shifter #(.width(32), .shift("lr")) shifter_1 (.in(MemData), .\dist (multiplexer_11_out), .out(MemHUData));
  Multiplexer #(.select(2), .width(5), .disabled("Z"), .enable("false")) multiplexer_13 (
    .in0({5{1'b0}}), .in1(5'b01000), .in2(5'b10000), .in3(5'b11000), .out(multiplexer_13_out),
    .sel(result[1:0]));
  Shifter #(.width(32), .shift("lr")) shifter_2 (.in(MemData), .\dist (multiplexer_13_out), .out(MemBData));
  Multiplexer #(.select(1), .width(4), .disabled("Z"), .enable("false")) multiplexer_14 (
    .in0(4'b0011), .in1(4'b1100), .out(multiplexer_14_out), .sel(ex_mem_1_result_out[1]));
  Shifter #(.width(4), .shift("ll")) shifter_3 (.in(4'b0001), .\dist (ex_mem_1_result_out[1:0]), .out(shifter_3_out));
  Multiplexer #(.select(2), .width(4), .disabled("Z"), .enable("false")) multiplexer_15 (
    .in0(4'b1111), .in1(multiplexer_14_out), .in2(shifter_3_out), .out(multiplexer_15_out), .sel({2{MEM_Lb}}));  // open: in3
  // MIPS_RAM mips_ram_1: pin names not known; wires that end beside it: ex_mem_1_result_out[11:2], MDin, MemWrite, multiplexer_15_out, CLK, mips_ram_1_p6, WB_PC
  MEM_WB mem_wb_1 (
    .pc_in(M_PC), .result_in(ex_mem_1_result_out), .memdata_in(mips_ram_1_p6), .RD_in(ex_mem_1_rd_out),
    .RegWrite_in(ex_mem_1_regwrite_out), .MemToReg_in(ex_mem_1_memtoreg_out), .jal_in(ex_mem_1_jal_out),
    .jalr_in(ex_mem_1_jalr_out), .lhu_in(MEM_Lb), .lb_in(MEM_Lb), .CLK(CLK), .pc_out(WB_PC),
    .result_out(result), .memdata_out(MemData), .RD_out(WB_RD), .RegWrite_out(RegWrite),
    .MemToReg_out(WB_MemToReg), .jal_out(WB_JAL), .jalr_out(WB_JALR), .lhu_out(WB_Lhu), .lb_out(WB_Lb));

  // Other names for the same wires on the sheet: MEM_Lhu = MEM_Lb; EX_JALR = BranchToken[1]; JAL = control_sign[0];
  //   JALR = control_sign[1]; control_sign (some bits) = {AluSrcB, AluOP, Bne, Beq, Bge, Blt}; Lb = control_sign[4];
  //   URET = control_sign[5]; MemToReg = control_sign[8]; ID_MemWrite = control_sign[9];
  //   ID_RegWrite = control_sign[15]; Lhu = control_sign[16]; S_type = control_sign[17]; ecall = control_sign[18];
  //   MEM_MEMWrite = MemWrite; MEM_PC[31:0] = M_PC; PC[31:0] = IF_PC; WB_RegWrite = RegWrite

  // Notes on the sheet:
  //   中断源
  //   时空图监测，可删除
  //   中断等待指示
  //   数码管输出
  //   控制位
  //   指令存储器
  //   流水调试日志用
  //   暂停节拍，不能为0
  //   contents of rom_1 (hex, n*v repeats v):
  //   413 493 913 993 46413 14e493 296913 39e993 842023 942223 1242423 1342623 a00893 493 913 993 73
  //   戳工具置1进入计数暂停模式，ctrl+k时钟自动运行到对应节拍暂停
  //   ctrl+k关闭时钟连续运行，将控制位置零，进入单步调试模式调试
  //   用这个时钟源需要去掉电路中的其他时钟源
  //   可计数暂停的时钟源
  //   指令探针
  //   rs2
  //   指令字
  //   rd
  //   URET
  //   JAL
  //   JALR
  //   rs1
  //   imm_i
  //   imm_s
  //   imm_b
  //   imm_j
  //   Beq
  //   Bne
  //   MemToReg
  //   MemWrite
  //   AluOP
  //   AluSrcB
  //   RegWrite
  //   S_type
  //   ecall
  //   为方便自动评测，需要输出流水线各段保存的PC值，注意是PC不是PC+4，另外ID段寄存器写入信息，Mem段内存写入信息也要输出
  //   RS1
  //   RS2
endmodule

module \气泡流水线  (
  output RegWrite,
  output MemWrite,
  output [31:0] IF_PC,
  output [31:0] ID_PC,
  output [31:0] EX_PC,
  output [31:0] M_PC,
  output [31:0] WB_PC,
  output [31:0] RDin,
  output [31:0] MDin,
  output [31:0] LedData
);

  wire AluSrcB, Beq, Bge, Blt, Bne, branch_harzard, CLK, clock_1_out, comparator_1_eq, comparator_1_lt,
       comparator_3_eq, d_ff_1_q, data_harzard, equal, EX_AluSrcB, EX_Beq, EX_Bge, EX_Blt, EX_Bne, EX_ecall,
       EX_JAL, EX_Lb, EX_Lhu, ex_mem_1_jal_out, ex_mem_1_jalr_out, ex_mem_1_memtoreg_out,
       ex_mem_1_regwrite_out, EX_MemToReg, EX_MemWrite, EX_RegWrite, EX_S_type, EX_URET, Go, halt,
       \halt控制器_1_real_halt , \halt控制器_2_real_halt , IR1, IR2, IR3, less, MEM_Lb, MEM_Lhu,
       multiplexer_10_out, multiplexer_12_out, nand_1_out, nop, not_1_out, not_2_out, regwrite_to_ID_EX, RST,
       W1, W2, W3, WB_JAL, WB_JALR, WB_Lb, WB_Lhu, WB_MemToReg;
  wire [0:0] or_1_out;
  wire [1:0] BranchToken;
  wire [1:1] or_2_out;
  wire [3:0] AluOP, EX_AluOP, multiplexer_14_out, multiplexer_15_out, shifter_3_out;
  wire [4:0] ex_mem_1_rd_out, EX_RD, multiplexer_2_out, multiplexer_3_out, multiplexer_11_out,
       multiplexer_13_out, RD, WB_RD;
  wire [11:0] multiplier_1_out;
  wire [12:0] CNT_num;
  wire [15:0] \LoadUse次数 , \总周期数 , \插入气泡数 , \无条件分支数 , \条件分支成功数 ;
  wire [18:0] control_sign, \id_ex气泡生成器_1_control_sign_out ;
  wire [19:0] multiplier_2_out;
  wire [31:0] adder_1_out, adder_2_out, adder_3_out, bit_extender_1_out, bit_extender_2_out,
       bit_extender_3_out, bit_extender_4_out, EX_IR, ex_mem_1_result_out, EX_result, id_ex_1_rs1_out,
       \id_ex气泡生成器_1_pc_out , ID_IR, \if_id气泡生成器_1_ir_out , \if_id气泡生成器_1_pc_out , IF_IR, imm, MEM_IR,
       MemBData, MemData, MemHUData, mips_ram_1_p6, multiplexer_1_out, multiplexer_4_out, multiplexer_5_out,
       multiplexer_6_out, multiplexer_7_out, multiplexer_9_out, R2_data, regfile_hl_1_r1, regfile_hl_1_r2,
       result, riscv_probe_6_p1, rom_1_data, WB_IR;

  Button \u_总复位  (.out(RST));
  Button _1 (.out(IR1));
  Button _2 (.out(IR2));
  Button _3 (.out(IR3));
  // Probe on \总周期数 
  // Probe on \总周期数 
  Button \u_继续运行  (.out(Go));
  LED #(.active("true")) led_1 (.in(W1));
  LED #(.active("true")) led_2 (.in(W2));
  LED #(.active("true")) led_3 (.in(W3));
  Hex_Digit_Display hex_digit_display_1 (.value(LedData[31:28]));  // open: dp
  // Probe on IF_PC[19:0]
  // RiscV_Probe riscv_probe_1: pin names not known; wires that end beside it: IF_IR
  not not_1 (not_1_out, \halt控制器_1_real_halt );
  \halt控制器  \halt控制器_1  (
    .halt(halt), .data_harzard(data_harzard), .branch_harzard(branch_harzard),
    .real_halt(\halt控制器_1_real_halt ));
  Hex_Digit_Display hex_digit_display_2 (.value(LedData[27:24]));  // open: dp
  Hex_Digit_Display hex_digit_display_3 (.value(LedData[23:20]));  // open: dp
  // Probe on ID_PC[19:0]
  // RiscV_Probe riscv_probe_2: pin names not known; wires that end beside it: ID_IR
  Hex_Digit_Display hex_digit_display_4 (.value(LedData[15:12]));  // open: dp
  Hex_Digit_Display hex_digit_display_5 (.value(LedData[19:16]));  // open: dp
  Hex_Digit_Display hex_digit_display_6 (.value(LedData[7:4]));  // open: dp
  Hex_Digit_Display hex_digit_display_7 (.value(LedData[11:8]));  // open: dp
  // Probe on EX_PC[19:0]
  // RiscV_Probe riscv_probe_3: pin names not known; wires that end beside it: EX_IR
  Register #(.width(32), .trigger("rising"), .Select("low")) PC (
    .D(multiplexer_1_out), .en(not_1_out), .Q(IF_PC), .clk(CLK), .clr(RST));
  Hex_Digit_Display hex_digit_display_8 (.value(LedData[3:0]));  // open: dp
  // Probe on \总周期数 
  // Probe on M_PC[19:0]
  // RiscV_Probe riscv_probe_4: pin names not known; wires that end beside it: MEM_IR
  Adder #(.width(32)) adder_1 (.a(IF_PC), .b(32'h4), .out(adder_1_out));  // open: cin, cout
  Adder #(.width(32)) adder_2 (.a(EX_PC), .b(imm), .out(adder_2_out));  // open: cin, cout
  // Probe on \总周期数 
  // Probe on \无条件分支数 
  // Probe on \条件分支成功数 
  // Probe on \插入气泡数 
  // Probe on \LoadUse次数 
  // Probe on IF_PC[11:0]
  // Probe on WB_PC[19:0]
  // RiscV_Probe riscv_probe_5: pin names not known; wires that end beside it: WB_IR
  // Probe on ID_PC[11:0]
  // Probe on EX_PC[11:0]
  ecall_halt ecall_halt_1 (
    .go_button(Go), .ecall(EX_ecall), .equal(equal), .R2_data(R2_data), .clk(CLK), .halt(halt),
    .led_data(LedData));
  Multiplexer #(.select(2), .width(32), .disabled("Z"), .enable("false")) multiplexer_1 (
    .in0(adder_1_out), .in1(adder_2_out), .in2({EX_result[31:1], 1'b0}), .out(multiplexer_1_out),
    .sel(BranchToken));  // open: in3
  // Probe on M_PC[11:0]
  D_Flip_Flop #(.trigger("high"), .Pre_Clr_Positions("LEGACY"), .NegatePresetClear("false"), .enable("true"), .NewFFLayout("false")) d_ff_1 (.Q(d_ff_1_q));  // open: clk, D, Qn, preset, en, reset
  // Probe on 13'h19
  ROM #(.addrWidth(10), .dataWidth(32), .Select("high")) rom_1 (.addr(IF_PC[11:2]), .data(rom_1_data));
  // Probe on WB_PC[11:0]
  Comparator #(.width(13), .mode("unsigned")) comparator_1 (
    .a(CNT_num), .b(13'h19), .eq(comparator_1_eq), .lt(comparator_1_lt));  // open: gt
  Clock #(.highDuration(1), .lowDuration(1)) clock_1 (.out(clock_1_out));
  nand nand_1 (nand_1_out, d_ff_1_q, comparator_1_eq);
  Counter #(.width(13), .max('h1fff), .ongoal("stay"), .trigger("rising"), .behavior("old")) counter_1 (
    .count(comparator_1_lt), .Q(CNT_num), .clk(clock_1_out));  // open: load, D, carry, clr, preset
  \IF_ID气泡生成器  \if_id气泡生成器_1  (
    .IR_in(rom_1_data), .data_harzard(data_harzard), .branch_harzard(branch_harzard),
    .IR_out(\if_id气泡生成器_1_ir_out ), .PC_in(IF_PC), .PC_out(\if_id气泡生成器_1_pc_out ));
  assign CLK = nand_1_out ? clock_1_out : 1'bz;  // Controlled_Buffer controlled_buffer_1
  \halt控制器  \halt控制器_2  (
    .halt(halt), .data_harzard(data_harzard), .branch_harzard(branch_harzard),
    .real_halt(\halt控制器_2_real_halt ));
  Pull_Resistor #(.pull(1)) pull_resistor_1 (.node(CLK));
  // RiscV_Probe riscv_probe_6: pin names not known; wires that end beside it: {riscv_probe_6_p1[31:12], RD, riscv_probe_6_p1[6:0]}, CLK, ID_PC
  IF_ID IF_ID (
    .pc(\if_id气泡生成器_1_pc_out ), .instr(\if_id气泡生成器_1_ir_out ), .clk(CLK), .pc_out(ID_PC),
    .instr_out({riscv_probe_6_p1[31:12], RD, riscv_probe_6_p1[6:0]}), .halt(\halt控制器_2_real_halt ));
  not not_2 (not_2_out, halt);
  Counter #(.width(16), .max('hffff), .ongoal("wrap"), .trigger("rising"), .behavior("new")) counter_2 (
    .count(not_2_out), .Q(\总周期数 ), .clk(CLK));  // open: load, D, carry, clr, preset, down
  \单周期硬布线控制器  \u_单周期硬布线控制器_1  (
    .Funct({riscv_probe_6_p1[30], riscv_probe_6_p1[25], riscv_probe_6_p1[14:12]}),
    .OP(riscv_probe_6_p1[6:2]), .ALU_OP(AluOP), .MemToReg(control_sign[8]), .MemWrite(control_sign[9]),
    .ALU_SRC(AluSrcB), .RegWrite(control_sign[15]), .ecall(control_sign[18]), .S_type(control_sign[17]),
    .Beq(Beq), .in_3(riscv_probe_6_p1[21]), .uret(control_sign[5]), .Jalr(control_sign[1]),
    .JAL(control_sign[0]), .Blt(Blt), .Bge(Bge), .Lb(control_sign[4]), .Lhu(control_sign[16]), .Bne(Bne));  // open: CSRRSI, CSRRCI
  Comparator #(.width(32), .mode("unsigned")) comparator_2 (
    .a({riscv_probe_6_p1[31:12], RD, riscv_probe_6_p1[6:0]}), .b({32{1'b0}}), .eq(nop));  // open: gt, lt
  assign bit_extender_1_out = {{20{riscv_probe_6_p1[31]}}, riscv_probe_6_p1[31:20]};  // Bit_Extender bit_extender_1
  assign bit_extender_2_out = {{20{1'b0}}, {riscv_probe_6_p1[31:25], RD}};  // Bit_Extender bit_extender_2
  Multiplier #(.width(12)) multiplier_1 (
    .a({riscv_probe_6_p1[31], RD[0], riscv_probe_6_p1[30:25], RD[4:1]}), .b(12'h2), .out(multiplier_1_out));  // open: cin, cout
  Multiplier #(.width(20)) multiplier_2 (
    .a({riscv_probe_6_p1[31], riscv_probe_6_p1[19:12], riscv_probe_6_p1[20], riscv_probe_6_p1[30:21]}),
    .b(20'h2), .out(multiplier_2_out));  // open: cin, cout
  Multiplexer #(.select(1), .width(5), .disabled("Z"), .enable("false")) multiplexer_2 (
    .in0(riscv_probe_6_p1[19:15]), .in1(5'b10001), .out(multiplexer_2_out), .sel(control_sign[18]));
  assign bit_extender_3_out = {{20{multiplier_1_out[11]}}, multiplier_1_out};  // Bit_Extender bit_extender_3
  assign bit_extender_4_out = {{12{multiplier_2_out[19]}}, multiplier_2_out};  // Bit_Extender bit_extender_4
  \数据冲突识别器  \u_数据冲突识别器_1  (
    .R2(multiplexer_3_out), .AluSrcB(AluSrcB), .R1(multiplexer_2_out), .rd_to_ID_EX(RD),
    .regwrite_to_ID_EX(regwrite_to_ID_EX), .CLK(CLK), .data_harzard(data_harzard), .nop(nop),
    .ecall(control_sign[18]), .jal(control_sign[0]), .sw(control_sign[17]));
  Multiplexer #(.select(1), .width(5), .disabled("Z"), .enable("false")) multiplexer_3 (
    .in0(riscv_probe_6_p1[24:20]), .in1(5'b01010), .out(multiplexer_3_out), .sel(control_sign[18]));
  regfile_hl regfile_hl_1 (
    .Din(RDin), .Clk(CLK), .R1(regfile_hl_1_r1), .R2(regfile_hl_1_r2), .WE(RegWrite), .W_num(WB_RD),
    .R1_num(multiplexer_2_out), .R2_num(multiplexer_3_out));
  Multiplexer #(.select(1), .width(32), .disabled("Z"), .enable("false")) multiplexer_4 (
    .in0(bit_extender_1_out), .in1(bit_extender_2_out), .out(multiplexer_4_out), .sel(control_sign[17]));
  Multiplexer #(.select(1), .width(32), .disabled("Z"), .enable("false")) multiplexer_5 (
    .in0(multiplexer_4_out), .in1(32'h22), .out(multiplexer_5_out), .sel(control_sign[18]));
  Adder #(.width(32)) adder_3 (.a(WB_PC), .b(32'h4), .out(adder_3_out));  // open: cin, cout
  Multiplexer #(.select(2), .width(32), .disabled("Z"), .enable("false")) multiplexer_6 (
    .in0(MemData), .in1(MemHUData), .in2(MemBData), .out(multiplexer_6_out), .sel({WB_Lb, WB_Lhu}));  // open: in3
  \ID_EX气泡生成器  \id_ex气泡生成器_1  (
    .control_sign_in({control_sign[18:15], AluSrcB, AluOP, control_sign[9:8], Bne, Beq, control_sign[5:4], Bge, Blt, control_sign[1:0]}),
    .control_sign_out({\id_ex气泡生成器_1_control_sign_out [18:16], regwrite_to_ID_EX, \id_ex气泡生成器_1_control_sign_out [14:0]}),
    .data_harzard(data_harzard), .branch_harzard(branch_harzard), .nop(nop), .PC_in(ID_PC),
    .PC_out(\id_ex气泡生成器_1_pc_out ));
  Multiplexer #(.select(2), .width(32), .disabled("Z"), .enable("false")) multiplexer_7 (
    .in0(multiplexer_5_out), .in1(bit_extender_3_out), .in2(bit_extender_4_out), .out(multiplexer_7_out),
    .sel({control_sign[0], or_1_out[0]}));  // open: in3
  Multiplexer #(.select(2), .width(32), .disabled("Z"), .enable("false")) multiplexer_8 (
    .in0(result), .in1(multiplexer_6_out), .in2(adder_3_out), .out(RDin), .sel({or_2_out[1], WB_MemToReg}));  // open: in3
  or or_1 (or_1_out[0], Bne, Beq, Bge, Blt);
  ID_EX id_ex_1 (
    .PC_in(\id_ex气泡生成器_1_pc_out ), .RS1_in(regfile_hl_1_r1), .RS2_in(regfile_hl_1_r2), .RD_in(RD),
    .control_sign_in({\id_ex气泡生成器_1_control_sign_out [18:16], regwrite_to_ID_EX, \id_ex气泡生成器_1_control_sign_out [14:0]}),
    .Imm_in(multiplexer_7_out), .clk(CLK), .PC_out(EX_PC), .RS1_out(id_ex_1_rs1_out), .RS2_out(R2_data),
    .RD_out(EX_RD),
    .control_sign_out({EX_ecall, EX_S_type, EX_Lhu, EX_RegWrite, EX_AluSrcB, EX_AluOP, EX_MemWrite, EX_MemToReg, EX_Bne, EX_Beq, EX_URET, EX_Lb, EX_Bge, EX_Blt, BranchToken[1], EX_JAL}),
    .Imm_out(imm), .halt(halt));
  or or_2 (or_2_out[1], WB_JAL, WB_JALR);
  Multiplexer #(.select(1), .width(32), .disabled("Z"), .enable("false")) multiplexer_9 (
    .in0(R2_data), .in1(imm), .out(multiplexer_9_out), .sel(EX_AluSrcB));
  ALU alu_1 (
    .X(id_ex_1_rs1_out), .Y(multiplexer_9_out), .AluOP(EX_AluOP), .Equal(equal), .Result(EX_result),
    .out_6(less));  // open: Result_2, out_4
  Pull_Resistor #(.pull(0)) pull_resistor_2 (.node(MemData));
  EX_MEM ex_mem_1 (
    .pc_in(EX_PC), .result_in(EX_result), .wd_in(R2_data), .RD_in(EX_RD), .RegWrite_in(EX_RegWrite),
    .MemToReg_in(EX_MemToReg), .MemWrite_in(EX_MemWrite), .jal_in(EX_JAL), .jalr_in(BranchToken[1]),
    .lhu_in(EX_Lhu), .lb_in(EX_Lb), .CLK(CLK), .pc_out(M_PC), .result_out(ex_mem_1_result_out),
    .wd_out(MDin), .RD_out(ex_mem_1_rd_out), .RegWrite_out(ex_mem_1_regwrite_out),
    .MemToReg_out(ex_mem_1_memtoreg_out), .MemWrite_out(MemWrite), .jal_out(ex_mem_1_jal_out),
    .jalr_out(ex_mem_1_jalr_out), .lhu_out(MEM_Lhu), .lb_out(MEM_Lb));
  not not_3 (branch_harzard, comparator_3_eq);
  Comparator #(.width(2), .mode("unsigned")) comparator_3 (
    .a(BranchToken), .b(2'b00), .eq(comparator_3_eq));  // open: gt, lt
  Multiplexer #(.select(1), .width(1), .disabled("Z"), .enable("false")) multiplexer_10 (
    .in0(EX_Bne), .in1(EX_Beq), .out(multiplexer_10_out), .sel(equal));
  or or_3 (BranchToken[0], multiplexer_10_out, EX_JAL, multiplexer_12_out);
  Multiplexer #(.select(1), .width(5), .disabled("Z"), .enable("false")) multiplexer_11 (
    .in0({5{1'b0}}), .in1(5'b10000), .out(multiplexer_11_out), .sel(result[1]));
  Multiplexer #(.select(1), .width(1), .disabled("Z"), .enable("false")) multiplexer_12 (
    .in0(EX_Bge), .in1(EX_Blt), .out(multiplexer_12_out), .sel(less));
  Shifter #(.width(32), .shift("lr")) shifter_1 (.in(MemData), .\dist (multiplexer_11_out), .out(MemHUData));
  Multiplexer #(.select(2), .width(5), .disabled("Z"), .enable("false")) multiplexer_13 (
    .in0({5{1'b0}}), .in1(5'b01000), .in2(5'b10000), .in3(5'b11000), .out(multiplexer_13_out),
    .sel(result[1:0]));
  Shifter #(.width(32), .shift("lr")) shifter_2 (.in(MemData), .\dist (multiplexer_13_out), .out(MemBData));
  Shifter #(.width(4), .shift("ll")) shifter_3 (.in(4'b0001), .\dist (ex_mem_1_result_out[1:0]), .out(shifter_3_out));
  Multiplexer #(.select(1), .width(4), .disabled("Z"), .enable("false")) multiplexer_14 (
    .in0(4'b0011), .in1(4'b1100), .out(multiplexer_14_out), .sel(ex_mem_1_result_out[1]));
  Multiplexer #(.select(2), .width(4), .disabled("Z"), .enable("false")) multiplexer_15 (
    .in0(4'b1111), .in1(multiplexer_14_out), .in2(shifter_3_out), .out(multiplexer_15_out),
    .sel({MEM_Lb, MEM_Lhu}));  // open: in3
  // MIPS_RAM mips_ram_1: pin names not known; wires that end beside it: ex_mem_1_result_out[11:2], MDin, MemWrite, multiplexer_15_out, CLK, mips_ram_1_p6, WB_PC
  MEM_WB mem_wb_1 (
    .pc_in(M_PC), .result_in(ex_mem_1_result_out), .memdata_in(mips_ram_1_p6), .RD_in(ex_mem_1_rd_out),
    .RegWrite_in(ex_mem_1_regwrite_out), .MemToReg_in(ex_mem_1_memtoreg_out), .jal_in(ex_mem_1_jal_out),
    .jalr_in(ex_mem_1_jalr_out), .lhu_in(MEM_Lhu), .lb_in(MEM_Lb), .CLK(CLK), .pc_out(WB_PC),
    .result_out(result), .memdata_out(MemData), .RD_out(WB_RD), .RegWrite_out(RegWrite),
    .MemToReg_out(WB_MemToReg), .jal_out(WB_JAL), .jalr_out(WB_JALR), .lhu_out(WB_Lhu), .lb_out(WB_Lb));

  // Other names for the same wires on the sheet: EX_JALR = BranchToken[1]; JAL = control_sign[0];
  //   JALR = control_sign[1]; control_sign (some bits) = {AluSrcB, AluOP, Bne, Beq, Bge, Blt}; Lb = control_sign[4];
  //   URET = control_sign[5]; MemToReg = control_sign[8]; ID_MemWrite = control_sign[9];
  //   ID_RegWrite = control_sign[15]; Lhu = control_sign[16]; S_type = control_sign[17]; ecall = control_sign[18];
  //   MEM_MEMWrite = MemWrite; MEM_PC[31:0] = M_PC; PC[31:0] = IF_PC; WB_RegWrite = RegWrite

  // Notes on the sheet:
  //   中断源
  //   时空图监测，可删除
  //   中断等待指示
  //   数码管输出
  //   控制位
  //   指令存储器
  //   流水调试日志用
  //   暂停节拍，不能为0
  //   contents of rom_1 (hex, n*v repeats v):
  //   100493 100006f 100493 200913 300993 100006f 100493 200913 300993 100006f 100493 200913 300993
  //   100006f 100493 200913 300993 29c000ef 100413 100493 1f49493 900533 2200893 73 24d493 48463 fedff06f
  //   900533 2200893 73 100493 249493 900533 2200893 73 48463 fedff06f 100493 1f49493 900533 2200893 73
  //   4034d493 900533 2200893 73 4044d493 900533 2200893 73 4044d493 900533 2200893 73 4044d493 900533
  //   2200893 73 4044d493 900533 2200893 73 4044d493 900533 2200893 73 4044d493 900533 2200893 73 4044d493
  //   900533 2200893 73 100413 1f41993 41f9d993 433 c00913 300b13 140413 f47413 800293 100313 499993
  //   89e9b3 1300533 2200893 73 406282b3 fe0294e3 140413 f00f93 1f47433 1c41413 800293 100313 49d993
  //   89e9b3 1300533 2200893 73 406282b3 fe0294e3 1c45413 406b0b33 b0463 f95ff06f 2b3 fff2c293 829293
  //   ff2e293 500533 2200893 73 fff00413 493 84a023 140413 448493 84a023 140413 448493 84a023 140413
  //   448493 84a023 140413 448493 84a023 140413 448493 84a023 140413 448493 84a023 140413 448493 84a023
  //   140413 448493 84a023 140413 448493 84a023 140413 448493 84a023 140413 448493 84a023 140413 448493
  //   84a023 140413 448493 84a023 140413 448493 84a023 140413 448493 84a023 140413 448493 140413 433
  //   3c00493 42983 4aa03 149a2b3 28663 134a023 1442023 ffc48493 fe9412e3 800533 2200893 73 440413 3c00493
  //   fc9416e3 a00893 73 413 140413 800533 2200893 73 240413 800533 2200893 73 340413 800533 2200893 73
  //   440413 800533 2200893 73 540413 800533 2200893 73 640413 800533 2200893 73 740413 800533 2200893 73
  //   840413 800533 2200893 2200893 73 8067
  //   戳工具置1进入计数暂停模式，ctrl+k时钟自动运行到对应节拍暂停
  //   ctrl+k关闭时钟连续运行，将控制位置零，进入单步调试模式调试
  //   用这个时钟源需要去掉电路中的其他时钟源
  //   可计数暂停的时钟源
  //   指令探针
  //   JAL
  //   JALR
  //   rs1
  //   rs2
  //   指令字
  //   rd
  //   imm_i
  //   imm_s
  //   imm_b
  //   imm_j
  //   URET
  //   Beq
  //   Bne
  //   ecall
  //   为方便自动评测，需要输出流水线各段保存的PC值，注意是PC不是PC+4，另外ID段寄存器写入信息，Mem段内存写入信息也要输出
  //   MemToReg
  //   MemWrite
  //   AluOP
  //   AluSrcB
  //   RegWrite
  //   S_type
  //   RS1
  //   RS2
endmodule

module \重定向流水线  (
  output RegWrite,
  output MemWrite,
  output [31:0] IF_PC,
  output [31:0] ID_PC,
  output [31:0] EX_PC,
  output [31:0] M_PC,
  output [31:0] WB_PC,
  output [31:0] RDin,
  output [31:0] MDin,
  output [31:0] LedData
);

  wire AluSrcB, Beq, Bge, Blt, Bne, branch_harzard, CLK, clock_1_out, comparator_1_eq, comparator_1_lt,
       comparator_3_eq, d_ff_1_q, data_harzard, equal, EX_AluSrcB, EX_Beq, EX_Bge, EX_Blt, EX_Bne, EX_ecall,
       EX_JAL, EX_Lb, EX_Lhu, ex_mem_1_jal_out, ex_mem_1_jalr_out, ex_mem_1_memtoreg_out,
       ex_mem_1_regwrite_out, EX_MemToReg, EX_MemWrite, EX_RegWrite, EX_S_type, EX_URET, Go, halt,
       \halt控制器_1_real_halt , \halt控制器_2_real_halt , IR1, IR2, IR3, jal_to_ID_EX, jalr_to_ID_EX, less,
       MEM_Lb, MEM_Lhu, memtoreg_to_ID_EX, multiplexer_12_out, multiplexer_13_out, nand_1_out, nop,
       not_1_out, not_2_out, regwrite_to_ID_EX, RST, W1, W2, W3, WB_JAL, WB_JALR, WB_Lb, WB_Lhu, WB_MemToReg;
  wire [0:0] or_1_out;
  wire [1:0] BranchToken;
  wire [1:1] or_2_out;
  wire [2:0] R1_relaycode, R2_relaycode;
  wire [3:0] AluOP, EX_AluOP, multiplexer_14_out, multiplexer_15_out, shifter_3_out;
  wire [4:0] ex_mem_1_rd_out, EX_RD, multiplexer_2_out, multiplexer_3_out, multiplexer_10_out,
       multiplexer_11_out, RD, WB_RD;
  wire [11:0] multiplier_1_out;
  wire [12:0] CNT_num;
  wire [15:0] \LoadUse次数 , \总周期数 , \插入气泡数 , \无条件分支数 , \条件分支成功数 ;
  wire [18:0] control_sign;
  wire [18:2] \id_ex气泡生成器_1_control_sign_out ;
  wire [19:0] multiplier_2_out;
  wire [31:0] adder_1_out, adder_2_out, adder_3_out, bit_extender_1_out, bit_extender_2_out,
       bit_extender_3_out, bit_extender_4_out, EX_IR, EX_result, id_ex_1_rs1_out, id_ex_1_rs2_out,
       \id_ex气泡生成器_1_pc_out , ID_IR, \if_id气泡生成器_1_ir_out , \if_id气泡生成器_1_pc_out , IF_IR, imm, MEM_IR,
       MEM_result, MemBData, MemData, MemHUData, mips_ram_1_p6, multiplexer_1_out, multiplexer_4_out,
       multiplexer_5_out, multiplexer_7_out, multiplexer_8_out, multiplexer_9_out, R2_data, regfile_hl_1_r1,
       regfile_hl_1_r2, riscv_probe_6_p1, rom_1_data, WB_IR, WB_result, \数据转发器_1_ex_r1 ;

  Button \u_总复位  (.out(RST));
  Button _1 (.out(IR1));
  Button _2 (.out(IR2));
  Button _3 (.out(IR3));
  // Probe on \总周期数 
  // Probe on \总周期数 
  Button \u_继续运行  (.out(Go));
  LED #(.active("true")) led_1 (.in(W1));
  LED #(.active("true")) led_2 (.in(W2));
  LED #(.active("true")) led_3 (.in(W3));
  // Probe on IF_PC[19:0]
  // RiscV_Probe riscv_probe_1: pin names not known; wires that end beside it: IF_IR
  Hex_Digit_Display hex_digit_display_1 (.value(LedData[31:28]));  // open: dp
  Hex_Digit_Display hex_digit_display_2 (.value(LedData[23:20]));  // open: dp
  Hex_Digit_Display hex_digit_display_3 (.value(LedData[27:24]));  // open: dp
  // Probe on ID_PC[19:0]
  // RiscV_Probe riscv_probe_2: pin names not known; wires that end beside it: ID_IR
  Hex_Digit_Display hex_digit_display_4 (.value(LedData[15:12]));  // open: dp
  Hex_Digit_Display hex_digit_display_5 (.value(LedData[19:16]));  // open: dp
  Hex_Digit_Display hex_digit_display_6 (.value(LedData[7:4]));  // open: dp
  Hex_Digit_Display hex_digit_display_7 (.value(LedData[11:8]));  // open: dp
  // Probe on EX_PC[19:0]
  // RiscV_Probe riscv_probe_3: pin names not known; wires that end beside it: EX_IR
  \halt控制器  \halt控制器_1  (
    .halt(halt), .data_harzard(data_harzard), .branch_harzard(branch_harzard),
    .real_halt(\halt控制器_1_real_halt ));
  Hex_Digit_Display hex_digit_display_8 (.value(LedData[3:0]));  // open: dp
  not not_1 (not_1_out, \halt控制器_1_real_halt );
  // Probe on \总周期数 
  // Probe on M_PC[19:0]
  // RiscV_Probe riscv_probe_4: pin names not known; wires that end beside it: MEM_IR
  // Probe on \总周期数 
  // Probe on \无条件分支数 
  // Probe on \条件分支成功数 
  // Probe on \插入气泡数 
  // Probe on \LoadUse次数 
  // RiscV_Probe riscv_probe_5: pin names not known; wires that end beside it: WB_IR
  // Probe on IF_PC[11:0]
  // Probe on WB_PC[19:0]
  Register #(.width(32), .trigger("rising"), .Select("low")) PC (
    .D(multiplexer_1_out), .en(not_1_out), .Q(IF_PC), .clk(CLK), .clr(RST));
  // Probe on ID_PC[11:0]
  // Probe on EX_PC[11:0]
  Adder #(.width(32)) adder_1 (.a(IF_PC), .b(32'h4), .out(adder_1_out));  // open: cin, cout
  Adder #(.width(32)) adder_2 (.a(EX_PC), .b(imm), .out(adder_2_out));  // open: cin, cout
  // Probe on M_PC[11:0]
  D_Flip_Flop #(.trigger("high"), .Pre_Clr_Positions("LEGACY"), .NegatePresetClear("false"), .enable("true"), .NewFFLayout("false")) d_ff_1 (.Q(d_ff_1_q));  // open: clk, D, Qn, preset, en, reset
  // Probe on 13'h8f5
  // Probe on WB_PC[11:0]
  Comparator #(.width(13), .mode("unsigned")) comparator_1 (
    .a(CNT_num), .b(13'h8f5), .eq(comparator_1_eq), .lt(comparator_1_lt));  // open: gt
  Clock #(.highDuration(1), .lowDuration(1)) clock_1 (.out(clock_1_out));
  nand nand_1 (nand_1_out, d_ff_1_q, comparator_1_eq);
  Counter #(.width(13), .max('h1fff), .ongoal("stay"), .trigger("rising"), .behavior("old")) counter_1 (
    .count(comparator_1_lt), .Q(CNT_num), .clk(clock_1_out));  // open: load, D, carry, clr, preset
  Multiplexer #(.select(2), .width(32), .disabled("Z"), .enable("false")) multiplexer_1 (
    .in0(adder_1_out), .in1(adder_2_out), .in2({EX_result[31:1], 1'b0}), .out(multiplexer_1_out),
    .sel(BranchToken));  // open: in3
  assign CLK = nand_1_out ? clock_1_out : 1'bz;  // Controlled_Buffer controlled_buffer_1
  ecall_halt ecall_halt_1 (
    .go_button(Go), .ecall(EX_ecall), .equal(equal), .R2_data(R2_data), .clk(CLK), .halt(halt),
    .led_data(LedData));
  Pull_Resistor #(.pull(1)) pull_resistor_1 (.node(CLK));
  ROM #(.addrWidth(10), .dataWidth(32), .Select("high")) rom_1 (.addr(IF_PC[11:2]), .data(rom_1_data));
  not not_2 (not_2_out, halt);
  \IF_ID气泡生成器  \if_id气泡生成器_1  (
    .IR_in(rom_1_data), .data_harzard(data_harzard), .branch_harzard(branch_harzard),
    .IR_out(\if_id气泡生成器_1_ir_out ), .PC_in(IF_PC), .PC_out(\if_id气泡生成器_1_pc_out ));
  Counter #(.width(16), .max('hffff), .ongoal("wrap"), .trigger("rising"), .behavior("new")) counter_2 (
    .count(not_2_out), .Q(\总周期数 ), .clk(CLK));  // open: load, D, carry, clr, preset, down
  // RiscV_Probe riscv_probe_6: pin names not known; wires that end beside it: {riscv_probe_6_p1[31:12], RD, riscv_probe_6_p1[6:0]}, CLK, ID_PC
  \halt控制器  \halt控制器_2  (
    .halt(halt), .data_harzard(data_harzard), .branch_harzard(branch_harzard),
    .real_halt(\halt控制器_2_real_halt ));
  IF_ID IF_ID (
    .pc(\if_id气泡生成器_1_pc_out ), .instr(\if_id气泡生成器_1_ir_out ), .clk(CLK), .pc_out(ID_PC),
    .instr_out({riscv_probe_6_p1[31:12], RD, riscv_probe_6_p1[6:0]}), .halt(\halt控制器_2_real_halt ));
  \单周期硬布线控制器  \u_单周期硬布线控制器_1  (
    .Funct({riscv_probe_6_p1[30], riscv_probe_6_p1[25], riscv_probe_6_p1[14:12]}),
    .OP(riscv_probe_6_p1[6:2]), .ALU_OP(AluOP), .MemToReg(control_sign[8]), .MemWrite(control_sign[9]),
    .ALU_SRC(AluSrcB), .RegWrite(control_sign[15]), .ecall(control_sign[18]), .S_type(control_sign[17]),
    .Beq(Beq), .in_3(riscv_probe_6_p1[21]), .uret(control_sign[5]), .Jalr(control_sign[1]),
    .JAL(control_sign[0]), .Blt(Blt), .Bge(Bge), .Lb(control_sign[4]), .Lhu(control_sign[16]), .Bne(Bne));  // open: CSRRSI, CSRRCI
  Multiplexer #(.select(1), .width(5), .disabled("Z"), .enable("false")) multiplexer_2 (
    .in0(riscv_probe_6_p1[19:15]), .in1(5'b10001), .out(multiplexer_2_out), .sel(control_sign[18]));
  Comparator #(.width(32), .mode("unsigned")) comparator_2 (
    .a({riscv_probe_6_p1[31:12], RD, riscv_probe_6_p1[6:0]}), .b({32{1'b0}}), .eq(nop));  // open: gt, lt
  assign bit_extender_1_out = {{20{riscv_probe_6_p1[31]}}, riscv_probe_6_p1[31:20]};  // Bit_Extender bit_extender_1
  assign bit_extender_2_out = {{20{1'b0}}, {riscv_probe_6_p1[31:25], RD}};  // Bit_Extender bit_extender_2
  Multiplier #(.width(12)) multiplier_1 (
    .a({riscv_probe_6_p1[31], RD[0], riscv_probe_6_p1[30:25], RD[4:1]}), .b(12'h2), .out(multiplier_1_out));  // open: cin, cout
  Multiplier #(.width(20)) multiplier_2 (
    .a({riscv_probe_6_p1[31], riscv_probe_6_p1[19:12], riscv_probe_6_p1[20], riscv_probe_6_p1[30:21]}),
    .b(20'h2), .out(multiplier_2_out));  // open: cin, cout
  Multiplexer #(.select(1), .width(5), .disabled("Z"), .enable("false")) multiplexer_3 (
    .in0(riscv_probe_6_p1[24:20]), .in1(5'b01010), .out(multiplexer_3_out), .sel(control_sign[18]));
  assign bit_extender_3_out = {{20{multiplier_1_out[11]}}, multiplier_1_out};  // Bit_Extender bit_extender_3
  assign bit_extender_4_out = {{12{multiplier_2_out[19]}}, multiplier_2_out};  // Bit_Extender bit_extender_4
  \数据冲突识别器_重定向  \u_数据冲突识别器_重定向_1  (
    .AluSrcB(AluSrcB), .R2(multiplexer_3_out), .ecall(control_sign[18]), .jal(control_sign[0]),
    .R1(multiplexer_2_out), .nop(nop), .rd_to_ID_EX(RD), .regwrite_to_ID_EX(regwrite_to_ID_EX), .CLK(CLK),
    .memtoreg_to_ID_EX(memtoreg_to_ID_EX), .jalr_to_ID_EX(jalr_to_ID_EX), .jal_to_ID_EX(jal_to_ID_EX),
    .R2_relaycode(R2_relaycode), .stall(data_harzard), .R1_relaycode(R1_relaycode), .sw(control_sign[17]));
  Multiplexer #(.select(1), .width(32), .disabled("Z"), .enable("false")) multiplexer_4 (
    .in0(bit_extender_1_out), .in1(bit_extender_2_out), .out(multiplexer_4_out), .sel(control_sign[17]));
  regfile_hl regfile_hl_1 (
    .Din(RDin), .Clk(CLK), .R1(regfile_hl_1_r1), .R2(regfile_hl_1_r2), .WE(RegWrite), .W_num(WB_RD),
    .R1_num(multiplexer_2_out), .R2_num(multiplexer_3_out));
  Multiplexer #(.select(1), .width(32), .disabled("Z"), .enable("false")) multiplexer_5 (
    .in0(multiplexer_4_out), .in1(32'h22), .out(multiplexer_5_out), .sel(control_sign[18]));
  Adder #(.width(32)) adder_3 (.a(WB_PC), .b(32'h4), .out(adder_3_out));  // open: cin, cout
  Multiplexer #(.select(2), .width(32), .disabled("Z"), .enable("false")) multiplexer_6 (
    .in0(WB_result), .in1(multiplexer_7_out), .in2(adder_3_out), .out(RDin), .sel({or_2_out[1], WB_MemToReg}));  // open: in3
  Multiplexer #(.select(2), .width(32), .disabled("Z"), .enable("false")) multiplexer_7 (
    .in0(MemData), .in1(MemHUData), .in2(MemBData), .out(multiplexer_7_out), .sel({WB_Lb, WB_Lhu}));  // open: in3
  \ID_EX气泡生成器  \id_ex气泡生成器_1  (
    .control_sign_in({control_sign[18:15], AluSrcB, AluOP, control_sign[9:8], Bne, Beq, control_sign[5:4], Bge, Blt, control_sign[1:0]}),
    .control_sign_out({\id_ex气泡生成器_1_control_sign_out [18:16], regwrite_to_ID_EX, \id_ex气泡生成器_1_control_sign_out [14:9], memtoreg_to_ID_EX, \id_ex气泡生成器_1_control_sign_out [7:2], jalr_to_ID_EX, jal_to_ID_EX}),
    .data_harzard(data_harzard), .branch_harzard(branch_harzard), .nop(nop), .PC_in(ID_PC),
    .PC_out(\id_ex气泡生成器_1_pc_out ));
  Multiplexer #(.select(2), .width(32), .disabled("Z"), .enable("false")) multiplexer_8 (
    .in0(multiplexer_5_out), .in1(bit_extender_3_out), .in2(bit_extender_4_out), .out(multiplexer_8_out),
    .sel({control_sign[0], or_1_out[0]}));  // open: in3
  or or_1 (or_1_out[0], Bne, Beq, Bge, Blt);
  ID_EX id_ex_1 (
    .PC_in(\id_ex气泡生成器_1_pc_out ), .RS1_in(regfile_hl_1_r1), .RS2_in(regfile_hl_1_r2), .RD_in(RD),
    .control_sign_in({\id_ex气泡生成器_1_control_sign_out [18:16], regwrite_to_ID_EX, \id_ex气泡生成器_1_control_sign_out [14:9], memtoreg_to_ID_EX, \id_ex气泡生成器_1_control_sign_out [7:2], jalr_to_ID_EX, jal_to_ID_EX}),
    .Imm_in(multiplexer_8_out), .clk(CLK), .PC_out(EX_PC), .RS1_out(id_ex_1_rs1_out),
    .RS2_out(id_ex_1_rs2_out), .RD_out(EX_RD),
    .control_sign_out({EX_ecall, EX_S_type, EX_Lhu, EX_RegWrite, EX_AluSrcB, EX_AluOP, EX_MemWrite, EX_MemToReg, EX_Bne, EX_Beq, EX_URET, EX_Lb, EX_Bge, EX_Blt, BranchToken[1], EX_JAL}),
    .Imm_out(imm), .halt(halt));
  or or_2 (or_2_out[1], WB_JAL, WB_JALR);
  Pull_Resistor #(.pull(0)) pull_resistor_2 (.node(MemData));
  \数据转发器  \u_数据转发器_1  (
    .ID_EX_R1(id_ex_1_rs1_out), .WB_result(WB_result), .RDin(RDin), .WB_PC(WB_PC),
    .ID_EX_R2(id_ex_1_rs2_out), .MEM_result(MEM_result), .MEM_PC(M_PC), .R1_relaycode(R1_relaycode),
    .R2_relaycode(R2_relaycode), .EX_R1(\数据转发器_1_ex_r1 ), .EX_R2(R2_data), .CLK(CLK));
  Multiplexer #(.select(1), .width(32), .disabled("Z"), .enable("false")) multiplexer_9 (
    .in0(R2_data), .in1(imm), .out(multiplexer_9_out), .sel(EX_AluSrcB));
  ALU alu_1 (
    .X(\数据转发器_1_ex_r1 ), .Y(multiplexer_9_out), .AluOP(EX_AluOP), .Equal(equal), .Result(EX_result),
    .out_6(less));  // open: Result_2, out_4
  Multiplexer #(.select(1), .width(5), .disabled("Z"), .enable("false")) multiplexer_10 (
    .in0({5{1'b0}}), .in1(5'b10000), .out(multiplexer_10_out), .sel(WB_result[1]));
  Shifter #(.width(32), .shift("lr")) shifter_1 (.in(MemData), .\dist (multiplexer_10_out), .out(MemHUData));
  Multiplexer #(.select(2), .width(5), .disabled("Z"), .enable("false")) multiplexer_11 (
    .in0({5{1'b0}}), .in1(5'b01000), .in2(5'b10000), .in3(5'b11000), .out(multiplexer_11_out),
    .sel(WB_result[1:0]));
  Comparator #(.width(2), .mode("unsigned")) comparator_3 (
    .a(BranchToken), .b(2'b00), .eq(comparator_3_eq));  // open: gt, lt
  or or_3 (BranchToken[0], multiplexer_12_out, EX_JAL, multiplexer_13_out);
  Shifter #(.width(32), .shift("lr")) shifter_2 (.in(MemData), .\dist (multiplexer_11_out), .out(MemBData));
  not not_3 (branch_harzard, comparator_3_eq);
  Multiplexer #(.select(1), .width(1), .disabled("Z"), .enable("false")) multiplexer_12 (
    .in0(EX_Bne), .in1(EX_Beq), .out(multiplexer_12_out), .sel(equal));
  Multiplexer #(.select(1), .width(1), .disabled("Z"), .enable("false")) multiplexer_13 (
    .in0(EX_Bge), .in1(EX_Blt), .out(multiplexer_13_out), .sel(less));
  EX_MEM ex_mem_1 (
    .pc_in(EX_PC), .result_in(EX_result), .wd_in(R2_data), .RD_in(EX_RD), .RegWrite_in(EX_RegWrite),
    .MemToReg_in(EX_MemToReg), .MemWrite_in(EX_MemWrite), .jal_in(EX_JAL), .jalr_in(BranchToken[1]),
    .lhu_in(EX_Lhu), .lb_in(EX_Lb), .CLK(CLK), .pc_out(M_PC), .result_out(MEM_result), .wd_out(MDin),
    .RD_out(ex_mem_1_rd_out), .RegWrite_out(ex_mem_1_regwrite_out), .MemToReg_out(ex_mem_1_memtoreg_out),
    .MemWrite_out(MemWrite), .jal_out(ex_mem_1_jal_out), .jalr_out(ex_mem_1_jalr_out), .lhu_out(MEM_Lhu),
    .lb_out(MEM_Lb));
  Multiplexer #(.select(1), .width(4), .disabled("Z"), .enable("false")) multiplexer_14 (
    .in0(4'b0011), .in1(4'b1100), .out(multiplexer_14_out), .sel(MEM_result[1]));
  Shifter #(.width(4), .shift("ll")) shifter_3 (.in(4'b0001), .\dist (MEM_result[1:0]), .out(shifter_3_out));
  Multiplexer #(.select(2), .width(4), .disabled("Z"), .enable("false")) multiplexer_15 (
    .in0(4'b1111), .in1(multiplexer_14_out), .in2(shifter_3_out), .out(multiplexer_15_out),
    .sel({MEM_Lb, MEM_Lhu}));  // open: in3
  // MIPS_RAM mips_ram_1: pin names not known; wires that end beside it: MEM_result[11:2], MDin, MemWrite, multiplexer_15_out, CLK, mips_ram_1_p6, WB_PC
  MEM_WB mem_wb_1 (
    .pc_in(M_PC), .result_in(MEM_result), .memdata_in(mips_ram_1_p6), .RD_in(ex_mem_1_rd_out),
    .RegWrite_in(ex_mem_1_regwrite_out), .MemToReg_in(ex_mem_1_memtoreg_out), .jal_in(ex_mem_1_jal_out),
    .jalr_in(ex_mem_1_jalr_out), .lhu_in(MEM_Lhu), .lb_in(MEM_Lb), .CLK(CLK), .pc_out(WB_PC),
    .result_out(WB_result), .memdata_out(MemData), .RD_out(WB_RD), .RegWrite_out(RegWrite),
    .MemToReg_out(WB_MemToReg), .jal_out(WB_JAL), .jalr_out(WB_JALR), .lhu_out(WB_Lhu), .lb_out(WB_Lb));

  // Other names for the same wires on the sheet: EX_JALR = BranchToken[1]; JAL = control_sign[0];
  //   JALR = control_sign[1]; control_sign (some bits) = {AluSrcB, AluOP, Bne, Beq, Bge, Blt}; Lb = control_sign[4];
  //   URET = control_sign[5]; MemToReg = control_sign[8]; ID_MemWrite = control_sign[9];
  //   ID_RegWrite = control_sign[15]; Lhu = control_sign[16]; S_type = control_sign[17]; ecall = control_sign[18];
  //   MEM_MEMWrite = MemWrite; MEM_PC[31:0] = M_PC; PC[31:0] = IF_PC; WB_RegWrite = RegWrite

  // Notes on the sheet:
  //   中断源
  //   时空图监测，可删除
  //   中断等待指示
  //   数码管输出
  //   控制位
  //   流水调试日志用
  //   暂停节拍，不能为0
  //   戳工具置1进入计数暂停模式，ctrl+k时钟自动运行到对应节拍暂停
  //   ctrl+k关闭时钟连续运行，将控制位置零，进入单步调试模式调试
  //   用这个时钟源需要去掉电路中的其他时钟源
  //   可计数暂停的时钟源
  //   指令存储器
  //   contents of rom_1 (hex, n*v repeats v):
  //   313 1000e13 8400493 849493 8348493 400913 891913 490913 849493 8248493 849493 8148493 891913 490913
  //   891913 490913 932023 12484b3 430313 fffe0e13 fe0e18e3 2000e13 313 35483 900533 2200893 73 230313
  //   fffe0e13 fe0e14e3 a00893 73
  //   为方便自动评测，需要输出流水线各段保存的PC值，注意是PC不是PC+4，另外ID段寄存器写入信息，Mem段内存写入信息也要输出
  //   指令探针
  //   指令字
  //   JAL
  //   JALR
  //   rs1
  //   rs2
  //   rd
  //   imm_i
  //   imm_s
  //   imm_b
  //   imm_j
  //   URET
  //   Beq
  //   Bne
  //   AluOP
  //   AluSrcB
  //   RegWrite
  //   S_type
  //   MemToReg
  //   MemWrite
  //   RS1
  //   RS2
endmodule

module \中断按键参考电路  (
  input  \同步清零信号 ,
  output \与中断屏蔽位与 
);

  wire \_1号中断_out , and_1_out, clock_1_out, d_ff_1_q, or_1_out, or_2_out;

  Clock #(.highDuration(1), .lowDuration(1)) clock_1 (.out(clock_1_out));
  Button \_1号中断  (.out(\_1号中断_out ));
  or or_1 (or_1_out, \与中断屏蔽位与 , d_ff_1_q);
  LED #(.active("true")) \_1号中断等待指示灯  (.in(or_1_out));
  D_Flip_Flop #(.trigger("rising"), .Pre_Clr_Positions("LEGACY"), .NegatePresetClear("false"), .enable("true"), .NewFFLayout("false")) d_ff_1 (
    .clk(\_1号中断_out ), .D(1'b1), .Q(d_ff_1_q), .reset(\与中断屏蔽位与 ));  // open: Qn, preset, en
  or or_2 (or_2_out, d_ff_1_q, \与中断屏蔽位与 );
  and and_1 (and_1_out, or_2_out, ~\同步清零信号 );  // AND_Gate
  D_Flip_Flop #(.trigger("rising"), .Pre_Clr_Positions("LEGACY"), .NegatePresetClear("false"), .enable("true"), .NewFFLayout("false")) IR1 (
    .clk(clock_1_out), .D(and_1_out), .Q(\与中断屏蔽位与 ));  // open: Qn, preset, en, reset

  // Notes on the sheet:
  //   中断信号采样参考电路
  //   Reset 
endmodule
module \单周期_多级中断  (
  input  IR1,
  input  IR2,
  input  IR3,
  output RegWrite,
  output MemWrite,
  output [31:0] PC,
  output [31:0] IR,
  output [31:0] RDin,
  output [31:0] MDin,
  output [31:0] LedData
);

  wire and_1_out, and_2_out, and_3_out, Beq, Bge, Blt, Bne, branch, clear1, clear2, clear3, CLK, clock_1_out,
       comparator_1_eq, comparator_2_eq, comparator_3_eq, comparator_4_eq, comparator_5_eq, comparator_6_eq,
       comparator_6_lt, comparator_7_gt, comparator_8_eq, CSRRCI, CSRRSI, d_ff_1_q, d_ff_2_q, d_ff_3_q,
       d_ff_4_q, decoder_1_out1, decoder_1_out2, decoder_1_out3, ecall, equal, Go, halt, IE, interrupt_sign,
       IR1_q, IR1_t, IR2_q, IR2_t, IR3_q, IR3_t, IRA, IRB, IRC, JAL, JALR, jump, Lb, less, Lhu, MemToReg,
       multiplexer_11_out, multiplexer_12_out, nand_1_out, not_1_out, not_2_out, not_3_out, or_1_out,
       or_2_out, or_12_out, or_13_out, or_14_out, or_15_out, or_16_out, pri_interrupt, pri_interrupt_sign,
       S_type, uret, W1, W2, W3, \单周期硬布线控制器_1_alu_src ;
  wire [0:0] or_4_out;
  wire [1:0] current_interrupt_num, interrupt_num;
  wire [3:0] ALUOP, multiplexer_13_out, multiplexer_14_out, shifter_1_out;
  wire [4:0] multiplexer_5_out, multiplexer_7_out, multiplexer_15_out, multiplexer_16_out;
  wire [11:0] multiplier_1_out;
  wire [12:0] CNT_num;
  wire [15:0] \总周期数 ;
  wire [19:0] multiplier_2_out;
  wire [31:0] adder_2_out, adder_3_out, bit_extender_1_out, bit_extender_2_out, EPC, interrupt_PC, MemBData,
       MemData, MemHUData, multiplexer_1_out, multiplexer_2_out, multiplexer_4_out, multiplexer_8_out,
       multiplexer_9_out, multiplexer_10_out, PC_4, PC_next, regifile_1_r1, result1, signed_imm_b,
       signed_imm_j;

  Button \u_继续运行  (.out(Go));
  Button _1 ();  // open: out
  Button _2 ();  // open: out
  Button _3 ();  // open: out
  LED #(.active("true")) led_1 (.in(W1));
  LED #(.active("true")) led_2 (.in(W2));
  LED #(.active("true")) led_3 (.in(W3));
  Multiplexer #(.select(1), .width(32), .disabled("Z"), .enable("false")) multiplexer_1 (
    .in0(interrupt_PC), .in1(PC_next), .out(multiplexer_1_out), .sel(not_1_out));
  not not_1 (not_1_out, pri_interrupt);
  Hex_Digit_Display hex_digit_display_1 (.value(LedData[31:28]));  // open: dp
  Comparator #(.width(16), .mode("twosComplement")) comparator_1 (
    .a(\总周期数 ), .b(16'h7), .eq(comparator_1_eq));  // open: gt, lt
  Comparator #(.width(16), .mode("twosComplement")) comparator_2 (
    .a(\总周期数 ), .b(16'h241), .eq(comparator_2_eq));  // open: gt, lt
  ecall_halt ecall_halt_1 (
    .go_button(Go), .ecall(ecall), .equal(equal), .R2_data(MDin), .clk(CLK), .halt(halt), .led_data(LedData));
  Multiplexer #(.select(1), .width(32), .disabled("Z"), .enable("false")) multiplexer_2 (
    .in0(EPC), .in1(multiplexer_1_out), .out(multiplexer_2_out), .sel(not_2_out));
  not not_2 (not_2_out, uret);
  not not_3 (not_3_out, halt);
  Hex_Digit_Display hex_digit_display_2 (.value(LedData[23:20]));  // open: dp
  Hex_Digit_Display hex_digit_display_3 (.value(LedData[27:24]));  // open: dp
  Comparator #(.width(16), .mode("twosComplement")) comparator_3 (
    .a(16'h258), .b(\总周期数 ), .eq(comparator_3_eq));  // open: gt, lt
  or or_1 (or_1_out, comparator_3_eq, comparator_4_eq);
  Comparator #(.width(16), .mode("twosComplement")) comparator_4 (
    .a(\总周期数 ), .b(16'h1), .eq(comparator_4_eq));  // open: gt, lt
  Comparator #(.width(16), .mode("twosComplement")) comparator_5 (
    .a(\总周期数 ), .b(16'h4), .eq(comparator_5_eq));  // open: gt, lt
  or or_2 (or_2_out, comparator_1_eq, comparator_2_eq);
  Register #(.width(32), .trigger("rising"), .Select("low")) u_PC (
    .D(multiplexer_2_out), .en(not_3_out), .Q(PC), .clk(CLK));  // open: clr
  Hex_Digit_Display hex_digit_display_4 (.value(LedData[19:16]));  // open: dp
  Hex_Digit_Display hex_digit_display_5 (.value(LedData[15:12]));  // open: dp
  Pull_Resistor #(.pull(0)) pull_resistor_1 (.node(IRA));
  assign IRA = or_1_out ? ~CLK : 1'bz;  // Controlled_Inverter controlled_inverter_1
  Pull_Resistor #(.pull(0)) pull_resistor_2 (.node(IRB));
  assign IRB = comparator_5_eq ? ~CLK : 1'bz;  // Controlled_Inverter controlled_inverter_2
  Pull_Resistor #(.pull(0)) pull_resistor_3 (.node(IRC));
  assign IRC = or_2_out ? ~CLK : 1'bz;  // Controlled_Inverter controlled_inverter_3
  Adder #(.width(32)) adder_1 (.a(PC), .b(32'h4), .out(PC_4));  // open: cin, cout
  Adder #(.width(32)) adder_2 (.a(PC), .b(signed_imm_b), .out(adder_2_out));  // open: cin, cout
  Adder #(.width(32)) adder_3 (.a(PC), .b(signed_imm_j), .out(adder_3_out));  // open: cin, cout
  Hex_Digit_Display hex_digit_display_6 (.value(LedData[11:8]));  // open: dp
  Hex_Digit_Display hex_digit_display_7 (.value(LedData[7:4]));  // open: dp
  // Probe on \总周期数 
  // Probe on adder_3_out
  Hex_Digit_Display hex_digit_display_8 (.value(LedData[3:0]));  // open: dp
  or or_3 (jump, JAL, JALR);
  Multiplexer #(.select(2), .width(32), .disabled("Z"), .enable("false")) multiplexer_3 (
    .in0(PC_4), .in1(adder_2_out), .in2(adder_3_out), .in3({result1[31:1], 1'b0}), .out(PC_next),
    .sel({jump, or_4_out[0]}));
  or or_4 (or_4_out[0], JALR, branch);
  or or_5 (IR1_t, IR1, IRA);
  // RiscV_Probe riscv_probe_1: pin names not known; wires that end beside it: IR
  ROM #(.addrWidth(10), .dataWidth(32), .Select("high")) rom_1 (.addr(PC[11:2]), .data(IR));
  or or_6 (IR2_t, IR2, IRB);
  or or_7 (IR3_t, IR3, IRC);
  \单周期硬布线控制器  \u_单周期硬布线控制器_1  (
    .Funct({IR[30], IR[25], IR[14:12]}), .OP(IR[6:2]), .ALU_OP(ALUOP), .MemToReg(MemToReg),
    .MemWrite(MemWrite), .ALU_SRC(\单周期硬布线控制器_1_alu_src ), .RegWrite(RegWrite), .ecall(ecall),
    .S_type(S_type), .Beq(Beq), .in_3(IR[21]), .uret(uret), .Jalr(JALR), .JAL(JAL), .Blt(Blt), .Bge(Bge),
    .Lb(Lb), .Lhu(Lhu), .Bne(Bne), .CSRRSI(CSRRSI), .CSRRCI(CSRRCI));
  Multiplexer #(.select(2), .width(32), .disabled("Z"), .enable("false")) multiplexer_4 (
    .in0(MemData), .in1(MemHUData), .in2(MemBData), .out(multiplexer_4_out), .sel({Lb, Lhu}));  // open: in3
  Multiplexer #(.select(1), .width(5), .disabled("Z"), .enable("false")) multiplexer_5 (
    .in0(IR[19:15]), .in1(5'b10001), .out(multiplexer_5_out), .sel(ecall));
  Multiplexer #(.select(2), .width(32), .disabled("Z"), .enable("false")) multiplexer_6 (
    .in0(result1), .in1(multiplexer_4_out), .in2(PC_4), .out(RDin), .sel({jump, MemToReg}));  // open: in3
  assign bit_extender_1_out = {{20{IR[31]}}, IR[31:20]};  // Bit_Extender bit_extender_1
  assign bit_extender_2_out = {{20{1'b0}}, {IR[31:25], IR[11:7]}};  // Bit_Extender bit_extender_2
  Multiplier #(.width(12)) multiplier_1 (
    .a({IR[31], IR[7], IR[30:25], IR[11:8]}), .b(12'h2), .out(multiplier_1_out));  // open: cin, cout
  assign signed_imm_b = {{20{multiplier_1_out[11]}}, multiplier_1_out};  // Bit_Extender bit_extender_3
  Multiplier #(.width(20)) multiplier_2 (
    .a({IR[31], IR[19:12], IR[20], IR[30:21]}), .b(20'h2), .out(multiplier_2_out));  // open: cin, cout
  // Probe on S_type
  Multiplexer #(.select(1), .width(5), .disabled("Z"), .enable("false")) multiplexer_7 (
    .in0(IR[24:20]), .in1(5'b01010), .out(multiplexer_7_out), .sel(ecall));
  assign signed_imm_j = {{12{multiplier_2_out[19]}}, multiplier_2_out};  // Bit_Extender bit_extender_4
  Multiplexer #(.select(1), .width(32), .disabled("Z"), .enable("false")) multiplexer_8 (
    .in0(bit_extender_1_out), .in1(bit_extender_2_out), .out(multiplexer_8_out), .sel(S_type));
  Regifile regifile_1 (
    .Din(RDin), .Clk(CLK), .R1(regifile_1_r1), .R2(MDin), .WE(RegWrite), .W_num(IR[11:7]),
    .R1_num(multiplexer_5_out), .R2_num(multiplexer_7_out));
  Multiplexer #(.select(1), .width(32), .disabled("Z"), .enable("false")) multiplexer_9 (
    .in0(MDin), .in1(multiplexer_10_out), .out(multiplexer_9_out), .sel(\单周期硬布线控制器_1_alu_src ));
  Multiplexer #(.select(1), .width(32), .disabled("Z"), .enable("false")) multiplexer_10 (
    .in0(multiplexer_8_out), .in1(32'h22), .out(multiplexer_10_out), .sel(ecall));
  Multiplexer #(.select(1), .width(1), .disabled("Z"), .enable("false")) multiplexer_11 (
    .in0(Bne), .in1(Beq), .out(multiplexer_11_out), .sel(equal));
  or or_8 (branch, multiplexer_11_out, multiplexer_12_out);
  Multiplexer #(.select(1), .width(1), .disabled("Z"), .enable("false")) multiplexer_12 (
    .in0(Bge), .in1(Blt), .out(multiplexer_12_out), .sel(less));
  D_Flip_Flop #(.trigger("high"), .Pre_Clr_Positions("LEGACY"), .NegatePresetClear("false"), .enable("true"), .NewFFLayout("false")) d_ff_1 (.Q(d_ff_1_q));  // open: clk, D, Qn, preset, en, reset
  // Probe on 13'h28
  ALU alu_1 (
    .X(regifile_1_r1), .Y(multiplexer_9_out), .AluOP(ALUOP), .Equal(equal), .Result(result1), .out_6(less));  // open: Result_2, out_4
  Comparator #(.width(13), .mode("twosComplement")) comparator_6 (
    .a(CNT_num), .b(13'h28), .eq(comparator_6_eq), .lt(comparator_6_lt));  // open: gt
  Clock #(.highDuration(1), .lowDuration(1)) clock_1 (.out(clock_1_out));
  Multiplexer #(.select(1), .width(4), .disabled("Z"), .enable("false")) multiplexer_13 (
    .in0(4'b0011), .in1(4'b1100), .out(multiplexer_13_out), .sel(result1[1]));
  Shifter #(.width(4), .shift("ll")) shifter_1 (.in(4'b0001), .\dist (result1[1:0]), .out(shifter_1_out));
  Counter #(.width(13), .max('h1fff), .ongoal("stay"), .trigger("rising"), .behavior("old")) counter_1 (
    .count(comparator_6_lt), .Q(CNT_num), .clk(clock_1_out));  // open: load, D, carry, clr, preset
  nand nand_1 (nand_1_out, d_ff_1_q, comparator_6_eq);
  or or_9 (W1, IR1_q, d_ff_3_q);
  or or_10 (W2, IR2_q, d_ff_4_q);
  D_Flip_Flop #(.trigger("rising"), .Pre_Clr_Positions("LEGACY"), .NegatePresetClear("false"), .enable("true"), .NewFFLayout("false")) d_ff_2 (
    .clk(IR3_t), .D(1'b1), .Q(d_ff_2_q), .reset(IR3_q));  // open: Qn, preset, en
  or or_11 (W3, IR3_q, d_ff_2_q);
  Multiplexer #(.select(2), .width(4), .disabled("Z"), .enable("false")) multiplexer_14 (
    .in0(4'b1111), .in1(multiplexer_13_out), .in2(shifter_1_out), .out(multiplexer_14_out), .sel({Lb, Lhu}));  // open: in3
  assign CLK = nand_1_out ? clock_1_out : 1'bz;  // Controlled_Buffer controlled_buffer_1
  Pull_Resistor #(.pull(1)) pull_resistor_4 (.node(CLK));
  D_Flip_Flop #(.trigger("rising"), .Pre_Clr_Positions("LEGACY"), .NegatePresetClear("false"), .enable("true"), .NewFFLayout("false")) d_ff_3 (
    .clk(IR1_t), .D(1'b1), .Q(d_ff_3_q), .reset(IR1_q));  // open: Qn, preset, en
  D_Flip_Flop #(.trigger("rising"), .Pre_Clr_Positions("LEGACY"), .NegatePresetClear("false"), .enable("true"), .NewFFLayout("false")) d_ff_4 (
    .clk(IR2_t), .D(1'b1), .Q(d_ff_4_q), .reset(IR2_q));  // open: Qn, preset, en
  Counter #(.width(16), .max('hffff), .ongoal("stay"), .trigger("rising"), .behavior("old")) counter_2 (
    .Q(\总周期数 ), .clk(CLK));  // open: load, D, count, carry, clr, preset
  or or_12 (or_12_out, d_ff_3_q, IR1_q);
  and and_1 (and_1_out, or_12_out, ~clear1);  // AND_Gate
  or or_13 (or_13_out, d_ff_4_q, IR2_q);
  and and_2 (and_2_out, or_13_out, ~clear2);  // AND_Gate
  or or_14 (or_14_out, d_ff_2_q, IR3_q);
  and and_3 (and_3_out, or_14_out, ~clear3);  // AND_Gate
  // MIPS_RAM mips_ram_1: pin names not known; wires that end beside it: result1[11:2], MDin, MemWrite, multiplexer_14_out, CLK, MemData
  Pull_Resistor #(.pull(0)) pull_resistor_5 (.node(MemData));
  D_Flip_Flop #(.trigger("falling"), .Pre_Clr_Positions("LEGACY"), .NegatePresetClear("false"), .enable("true"), .NewFFLayout("false")) u_IR1 (
    .clk(CLK), .D(and_1_out), .Q(IR1_q));  // open: Qn, preset, en, reset
  D_Flip_Flop #(.trigger("falling"), .Pre_Clr_Positions("LEGACY"), .NegatePresetClear("false"), .enable("true"), .NewFFLayout("false")) u_IR2 (
    .clk(CLK), .D(and_2_out), .Q(IR2_q));  // open: Qn, preset, en, reset
  D_Flip_Flop #(.trigger("falling"), .Pre_Clr_Positions("LEGACY"), .NegatePresetClear("false"), .enable("true"), .NewFFLayout("false")) u_IR3 (
    .clk(CLK), .D(and_3_out), .Q(IR3_q));  // open: Qn, preset, en, reset
  Multiplexer #(.select(1), .width(5), .disabled("Z"), .enable("false")) multiplexer_15 (
    .in0({5{1'b0}}), .in1(5'b10000), .out(multiplexer_15_out), .sel(result1[1]));
  Shifter #(.width(32), .shift("lr")) shifter_2 (.in(MemData), .\dist (multiplexer_15_out), .out(MemHUData));
  Multiplexer #(.select(2), .width(5), .disabled("Z"), .enable("false")) multiplexer_16 (
    .in0({5{1'b0}}), .in1(5'b01000), .in2(5'b10000), .in3(5'b11000), .out(multiplexer_16_out),
    .sel(result1[1:0]));
  Shifter #(.width(32), .shift("lr")) shifter_3 (.in(MemData), .\dist (multiplexer_16_out), .out(MemBData));
  Priority_Encoder #(.select(2), .disabled("Z")) priority_encoder_1 (
    .in0(1'b0), .in1(IR1_q), .in2(IR2_q), .in3(IR3_q), .out(interrupt_num), .gs(interrupt_sign));  // open: en_out, en_in
  Multiplexer #(.select(2), .width(32), .disabled("Z"), .enable("false")) multiplexer_17 (
    .in1(32'h30ac), .in2(32'h3158), .in3(32'h3204), .out(interrupt_PC), .sel(interrupt_num));  // open: in0
  Comparator #(.width(2), .mode("unsigned")) comparator_7 (
    .a(interrupt_num), .b(current_interrupt_num), .gt(comparator_7_gt));  // open: eq, lt
  and and_4 (pri_interrupt, IE, pri_interrupt_sign);
  stack_32bits_size3 PC_Stack (.\input (PC_next), .clk(CLK), .pop(uret), .push(pri_interrupt), .top(EPC));
  Decoder #(.select(2), .tristate("false"), .disabled("Z"), .enable("false")) decoder_1 (
    .out1(decoder_1_out1), .out2(decoder_1_out2), .out3(decoder_1_out3), .sel(interrupt_num));  // open: out0
  and and_5 (pri_interrupt_sign, interrupt_sign, comparator_7_gt);
  or or_15 (or_15_out, CSRRSI, uret);
  or or_16 (or_16_out, CSRRCI, pri_interrupt);
  and and_6 (clear1, decoder_1_out1, uret);
  and and_7 (clear2, decoder_1_out2, uret);
  and and_8 (clear3, decoder_1_out3, uret);
  Comparator #(.width(13), .mode("unsigned")) comparator_8 (
    .a(CNT_num), .b({13{1'b0}}), .eq(comparator_8_eq));  // open: gt, lt
  J_K_Flip_Flop #(.trigger("rising"), .Pre_Clr_Positions("ABOVE_BELOW"), .NegatePresetClear("false"), .enable("false"), .NewFFLayout("true")) j_k_ff_1 (
    .J(or_15_out), .clk(CLK), .K(or_16_out), .Q(IE), .preset(comparator_8_eq));  // open: Qn, reset
  stack_2bits_size3 stack_2bits_size3_1 (
    .\input (interrupt_num), .clk(CLK), .pop(uret), .push(pri_interrupt), .top(current_interrupt_num));

  // Other names for the same wires on the sheet: R2_data[31:0] = MDin

  // Notes on the sheet:
  //   中断源
  //   中断等待指示
  //   总复位信号应将除ROM以外所有存储组件全部清零
  //   多级中断测试信号模拟器
  //   数码管输出
  //   数码管输出应该用寄存器锁存，否则显示数据只能一闪而过
  //   指令探针
  //   指令存储器
  //   contents of rom_1 (hex, n*v repeats v):
  //   7d000113 100413 1f41993 41f9d993 433 c00913 800b13 140413 f47413 800293 100313 499993 89e9b3 1300533
  //   2200893 73 406282b3 fe0294e3 140413 f00f93 1f47433 1c41413 800293 100313 49d993 89e9b3 1300533
  //   2200893 73 406282b3 fe0294e3 1c45413 406b0b33 b0463 f95ff06f 2b3 fff2c293 1029293 fff2e293 500533
  //   2200893 73 f5dff06f 1112023 410113 a12023 410113 812023 410113 1312023 410113 1412023 410113 1512023
  //   410113 1612023 410113 40e073 100b13 300a13 100a93 1600433 441413 14469b3 1300533 2200893 73 fe0416e3
  //   415a0a33 fe0a10e3 40f073 ffc10113 12b03 ffc10113 12a83 ffc10113 12a03 ffc10113 12983 ffc10113 12403
  //   ffc10113 12503 ffc10113 12883 200073 1112023 410113 a12023 410113 812023 410113 1312023 410113
  //   1412023 410113 1512023 410113 1612023 410113 40e073 200b13 300a13 100a93 1600433 441413 14469b3
  //   1300533 2200893 73 fe0416e3 415a0a33 fe0a10e3 40f073 ffc10113 12b03 ffc10113 12a83 ffc10113 12a03
  //   ffc10113 12983 ffc10113 12403 ffc10113 12503 ffc10113 12883 200073 1112023 410113 a12023 410113
  //   812023 410113 1312023 410113 1412023 410113 1512023 410113 1612023 410113 40e073 300b13 300a13
  //   100a93 1600433 441413 14469b3 1300533 2200893 73 fe0416e3 415a0a33 fe0a10e3 40f073 ffc10113 12b03
  //   ffc10113 12a83 ffc10113 12a03 ffc10113 12983 ffc10113 12403 ffc10113 12503 ffc10113 12883 200073
  //   指令字
  //   rs1
  //   rs2
  //   rd
  //   imm_i
  //   imm_s
  //   imm_b
  //   imm_j
  //   Beq
  //   Bne
  //   MemToReg
  //   MemWrite
  //   AluOP
  //   AluSrcB
  //   RegWrite
  //   S_type
  //   ecall
  //   为方便自动评测，需要输出PC，IR，寄存器堆写如数据RDin
  //   RAM写使能MemWrite、RAM写入数据MDin等信号
  //   控制位
  //   暂停节拍，不能为0
  //   戳工具置1进入计数暂停模式，ctrl+k时钟自动运行到对应节拍暂停
  //   ctrl+k关闭时钟连续运行，将控制位置零，进入单步调试模式调试
  //   可计数暂停的时钟源
  //   数据存储器
  //   Reset 
  //   同步清零信号
  //   Reset 
  //   同步清零信号
  //   Reset 
  //   同步清零信号
  //   中断使能寄存器IE
endmodule

module \单周期_单级中断  (
  input  IR1,
  input  IR2,
  input  IR3,
  output RegWrite,
  output MemWrite,
  output [31:0] PC,
  output [31:0] IR,
  output [31:0] RDin,
  output [31:0] MDin,
  output [31:0] LedData
);

  wire and_1_out, and_2_out, and_3_out, and_4_out, Beq, Bge, Blt, Bne, branch, clear1, clear2, clear3, CLK,
       clock_1_out, comparator_1_eq, comparator_2_eq, comparator_3_eq, comparator_4_eq, comparator_5_eq,
       comparator_5_lt, d_ff_1_q, d_ff_2_q, d_ff_3_q, d_ff_4_q, decoder_1_out1, decoder_1_out2,
       decoder_1_out3, ecall, equal, Go, halt, IE, interrupt, interrupt_sign, IR1_q, IR1_t, IR2_q, IR2_t,
       IR3_q, IR3_t, IRA, IRB, IRC, JAL, JALR, jump, Lb, less, Lhu, MemToReg, multiplexer_10_out,
       multiplexer_11_out, nand_1_out, not_1_out, not_2_out, not_3_out, not_4_out, or_1_out, or_11_out,
       or_12_out, or_13_out, S_type, uret, W1, W2, W3, \单周期硬布线控制器_1_alu_src ;
  wire [0:0] or_3_out;
  wire [1:0] interrupt_num, register_1_q;
  wire [3:0] ALUOP, multiplexer_13_out, multiplexer_14_out, shifter_1_out;
  wire [4:0] multiplexer_4_out, multiplexer_7_out, multiplexer_15_out, multiplexer_16_out;
  wire [11:0] multiplier_1_out;
  wire [12:0] CNT_num;
  wire [15:0] \总周期数 ;
  wire [19:0] multiplier_2_out;
  wire [31:0] adder_2_out, adder_3_out, bit_extender_1_out, bit_extender_2_out, EPC, interrupt_PC, MemBData,
       MemData, MemHUData, multiplexer_1_out, multiplexer_2_out, multiplexer_6_out, multiplexer_8_out,
       multiplexer_9_out, multiplexer_12_out, PC_4, PC_next, regifile_1_r1, result1, signed_imm_b,
       signed_imm_j;

  Button \u_继续运行  (.out(Go));
  Button _1 ();  // open: out
  Button _2 ();  // open: out
  Button _3 ();  // open: out
  LED #(.active("true")) led_1 (.in(W1));
  LED #(.active("true")) led_2 (.in(W2));
  LED #(.active("true")) led_3 (.in(W3));
  Multiplexer #(.select(1), .width(32), .disabled("Z"), .enable("false")) multiplexer_1 (
    .in0(interrupt_PC), .in1(PC_next), .out(multiplexer_1_out), .sel(not_1_out));
  not not_1 (not_1_out, interrupt);
  Hex_Digit_Display hex_digit_display_1 (.value(LedData[31:28]));  // open: dp
  Comparator #(.width(16), .mode("twosComplement")) comparator_1 (
    .a(16'h23b), .b(\总周期数 ), .eq(comparator_1_eq));  // open: gt, lt
  Comparator #(.width(16), .mode("twosComplement")) comparator_2 (
    .a(\总周期数 ), .b(16'h1), .eq(comparator_2_eq));  // open: gt, lt
  Comparator #(.width(16), .mode("twosComplement")) comparator_3 (
    .a(\总周期数 ), .b(16'h4), .eq(comparator_3_eq));  // open: gt, lt
  Comparator #(.width(16), .mode("twosComplement")) comparator_4 (
    .a(\总周期数 ), .b(16'h7), .eq(comparator_4_eq));  // open: gt, lt
  ecall_halt ecall_halt_1 (
    .go_button(Go), .ecall(ecall), .equal(equal), .R2_data(MDin), .clk(CLK), .halt(halt), .led_data(LedData));
  Multiplexer #(.select(1), .width(32), .disabled("Z"), .enable("false")) multiplexer_2 (
    .in0(EPC), .in1(multiplexer_1_out), .out(multiplexer_2_out), .sel(not_3_out));
  not not_2 (not_2_out, halt);
  not not_3 (not_3_out, uret);
  Hex_Digit_Display hex_digit_display_2 (.value(LedData[23:20]));  // open: dp
  Hex_Digit_Display hex_digit_display_3 (.value(LedData[27:24]));  // open: dp
  or or_1 (or_1_out, comparator_1_eq, comparator_2_eq);
  assign IRA = or_1_out ? ~CLK : 1'bz;  // Controlled_Inverter controlled_inverter_1
  assign IRB = comparator_3_eq ? ~CLK : 1'bz;  // Controlled_Inverter controlled_inverter_2
  assign IRC = comparator_4_eq ? ~CLK : 1'bz;  // Controlled_Inverter controlled_inverter_3
  Register #(.width(32), .trigger("rising"), .Select("low")) u_PC (
    .D(multiplexer_2_out), .en(not_2_out), .Q(PC), .clk(CLK));  // open: clr
  Hex_Digit_Display hex_digit_display_4 (.value(LedData[15:12]));  // open: dp
  Hex_Digit_Display hex_digit_display_5 (.value(LedData[19:16]));  // open: dp
  Pull_Resistor #(.pull(0)) pull_resistor_1 (.node(IRA));
  Pull_Resistor #(.pull(0)) pull_resistor_2 (.node(IRB));
  Pull_Resistor #(.pull(0)) pull_resistor_3 (.node(IRC));
  Adder #(.width(32)) adder_1 (.a(PC), .b(32'h4), .out(PC_4));  // open: cin, cout
  Adder #(.width(32)) adder_2 (.a(PC), .b(signed_imm_b), .out(adder_2_out));  // open: cin, cout
  Adder #(.width(32)) adder_3 (.a(PC), .b(signed_imm_j), .out(adder_3_out));  // open: cin, cout
  Hex_Digit_Display hex_digit_display_6 (.value(LedData[11:8]));  // open: dp
  Hex_Digit_Display hex_digit_display_7 (.value(LedData[7:4]));  // open: dp
  // Probe on \总周期数 
  // Probe on adder_3_out
  Hex_Digit_Display hex_digit_display_8 (.value(LedData[3:0]));  // open: dp
  or or_2 (jump, JAL, JALR);
  Multiplexer #(.select(2), .width(32), .disabled("Z"), .enable("false")) multiplexer_3 (
    .in0(PC_4), .in1(adder_2_out), .in2(adder_3_out), .in3({result1[31:1], 1'b0}), .out(PC_next),
    .sel({jump, or_3_out[0]}));
  or or_3 (or_3_out[0], JALR, branch);
  or or_4 (IR1_t, IR1, IRA);
  // RiscV_Probe riscv_probe_1: pin names not known; wires that end beside it: IR
  or or_5 (IR2_t, IR2, IRB);
  ROM #(.addrWidth(10), .dataWidth(32), .Select("high")) rom_1 (.addr(PC[11:2]), .data(IR));
  or or_6 (IR3_t, IR3, IRC);
  \单周期硬布线控制器  \u_单周期硬布线控制器_1  (
    .Funct({IR[30], IR[25], IR[14:12]}), .OP(IR[6:2]), .ALU_OP(ALUOP), .MemToReg(MemToReg),
    .MemWrite(MemWrite), .ALU_SRC(\单周期硬布线控制器_1_alu_src ), .RegWrite(RegWrite), .ecall(ecall),
    .S_type(S_type), .Beq(Beq), .in_3(IR[21]), .uret(uret), .Jalr(JALR), .JAL(JAL), .Blt(Blt), .Bge(Bge),
    .Lb(Lb), .Lhu(Lhu), .Bne(Bne));  // open: CSRRSI, CSRRCI
  Multiplexer #(.select(1), .width(5), .disabled("Z"), .enable("false")) multiplexer_4 (
    .in0(IR[19:15]), .in1(5'b10001), .out(multiplexer_4_out), .sel(ecall));
  Multiplexer #(.select(2), .width(32), .disabled("Z"), .enable("false")) multiplexer_5 (
    .in0(result1), .in1(multiplexer_6_out), .in2(PC_4), .out(RDin), .sel({jump, MemToReg}));  // open: in3
  Multiplexer #(.select(2), .width(32), .disabled("Z"), .enable("false")) multiplexer_6 (
    .in0(MemData), .in1(MemHUData), .in2(MemBData), .out(multiplexer_6_out), .sel({Lb, Lhu}));  // open: in3
  assign bit_extender_1_out = {{20{IR[31]}}, IR[31:20]};  // Bit_Extender bit_extender_1
  assign bit_extender_2_out = {{20{1'b0}}, {IR[31:25], IR[11:7]}};  // Bit_Extender bit_extender_2
  Multiplier #(.width(12)) multiplier_1 (
    .a({IR[31], IR[7], IR[30:25], IR[11:8]}), .b(12'h2), .out(multiplier_1_out));  // open: cin, cout
  Multiplier #(.width(20)) multiplier_2 (
    .a({IR[31], IR[19:12], IR[20], IR[30:21]}), .b(20'h2), .out(multiplier_2_out));  // open: cin, cout
  // Probe on S_type
  Multiplexer #(.select(1), .width(5), .disabled("Z"), .enable("false")) multiplexer_7 (
    .in0(IR[24:20]), .in1(5'b01010), .out(multiplexer_7_out), .sel(ecall));
  assign signed_imm_b = {{20{multiplier_1_out[11]}}, multiplier_1_out};  // Bit_Extender bit_extender_3
  Multiplexer #(.select(1), .width(32), .disabled("Z"), .enable("false")) multiplexer_8 (
    .in0(bit_extender_1_out), .in1(bit_extender_2_out), .out(multiplexer_8_out), .sel(S_type));
  assign signed_imm_j = {{12{multiplier_2_out[19]}}, multiplier_2_out};  // Bit_Extender bit_extender_4
  Regifile regifile_1 (
    .Din(RDin), .Clk(CLK), .R1(regifile_1_r1), .R2(MDin), .WE(RegWrite), .W_num(IR[11:7]),
    .R1_num(multiplexer_4_out), .R2_num(multiplexer_7_out));
  Multiplexer #(.select(1), .width(32), .disabled("Z"), .enable("false")) multiplexer_9 (
    .in0(multiplexer_8_out), .in1(32'h22), .out(multiplexer_9_out), .sel(ecall));
  Multiplexer #(.select(1), .width(1), .disabled("Z"), .enable("false")) multiplexer_10 (
    .in0(Bne), .in1(Beq), .out(multiplexer_10_out), .sel(equal));
  or or_7 (branch, multiplexer_10_out, multiplexer_11_out);
  Multiplexer #(.select(1), .width(1), .disabled("Z"), .enable("false")) multiplexer_11 (
    .in0(Bge), .in1(Blt), .out(multiplexer_11_out), .sel(less));
  Multiplexer #(.select(1), .width(32), .disabled("Z"), .enable("false")) multiplexer_12 (
    .in0(MDin), .in1(multiplexer_9_out), .out(multiplexer_12_out), .sel(\单周期硬布线控制器_1_alu_src ));
  D_Flip_Flop #(.trigger("high"), .Pre_Clr_Positions("LEGACY"), .NegatePresetClear("false"), .enable("true"), .NewFFLayout("false")) d_ff_1 (.Q(d_ff_1_q));  // open: clk, D, Qn, preset, en, reset
  // Probe on 13'h45
  ALU alu_1 (
    .X(regifile_1_r1), .Y(multiplexer_12_out), .AluOP(ALUOP), .Equal(equal), .Result(result1), .out_6(less));  // open: Result_2, out_4
  Comparator #(.width(13), .mode("twosComplement")) comparator_5 (
    .a(CNT_num), .b(13'h45), .eq(comparator_5_eq), .lt(comparator_5_lt));  // open: gt
  Clock #(.highDuration(1), .lowDuration(1)) clock_1 (.out(clock_1_out));
  Multiplexer #(.select(1), .width(4), .disabled("Z"), .enable("false")) multiplexer_13 (
    .in0(4'b0011), .in1(4'b1100), .out(multiplexer_13_out), .sel(result1[1]));
  Shifter #(.width(4), .shift("ll")) shifter_1 (.in(4'b0001), .\dist (result1[1:0]), .out(shifter_1_out));
  Counter #(.width(13), .max('h1fff), .ongoal("stay"), .trigger("rising"), .behavior("old")) counter_1 (
    .count(comparator_5_lt), .Q(CNT_num), .clk(clock_1_out));  // open: load, D, carry, clr, preset
  nand nand_1 (nand_1_out, d_ff_1_q, comparator_5_eq);
  or or_8 (W1, IR1_q, d_ff_2_q);
  or or_9 (W2, IR2_q, d_ff_3_q);
  or or_10 (W3, IR3_q, d_ff_4_q);
  Multiplexer #(.select(2), .width(4), .disabled("Z"), .enable("false")) multiplexer_14 (
    .in0(4'b1111), .in1(multiplexer_13_out), .in2(shifter_1_out), .out(multiplexer_14_out), .sel({Lb, Lhu}));  // open: in3
  assign CLK = nand_1_out ? clock_1_out : 1'bz;  // Controlled_Buffer controlled_buffer_1
  Pull_Resistor #(.pull(1)) pull_resistor_4 (.node(CLK));
  D_Flip_Flop #(.trigger("rising"), .Pre_Clr_Positions("LEGACY"), .NegatePresetClear("false"), .enable("true"), .NewFFLayout("false")) d_ff_2 (
    .clk(IR1_t), .D(1'b1), .Q(d_ff_2_q), .reset(IR1_q));  // open: Qn, preset, en
  D_Flip_Flop #(.trigger("rising"), .Pre_Clr_Positions("LEGACY"), .NegatePresetClear("false"), .enable("true"), .NewFFLayout("false")) d_ff_3 (
    .clk(IR2_t), .D(1'b1), .Q(d_ff_3_q), .reset(IR2_q));  // open: Qn, preset, en
  D_Flip_Flop #(.trigger("rising"), .Pre_Clr_Positions("LEGACY"), .NegatePresetClear("false"), .enable("true"), .NewFFLayout("false")) d_ff_4 (
    .clk(IR3_t), .D(1'b1), .Q(d_ff_4_q), .reset(IR3_q));  // open: Qn, preset, en
  Counter #(.width(16), .max('hffff), .ongoal("stay"), .trigger("rising"), .behavior("old")) counter_2 (
    .Q(\总周期数 ), .clk(CLK));  // open: load, D, count, carry, clr, preset
  or or_11 (or_11_out, d_ff_2_q, IR1_q);
  or or_12 (or_12_out, d_ff_3_q, IR2_q);
  or or_13 (or_13_out, d_ff_4_q, IR3_q);
  // MIPS_RAM mips_ram_1: pin names not known; wires that end beside it: result1[11:2], MDin, MemWrite, multiplexer_14_out, CLK, MemData
  Pull_Resistor #(.pull(0)) pull_resistor_5 (.node(MemData));
  and and_1 (and_1_out, or_11_out, ~clear1);  // AND_Gate
  and and_2 (and_2_out, or_12_out, ~clear2);  // AND_Gate
  and and_3 (and_3_out, or_13_out, ~clear3);  // AND_Gate
  Multiplexer #(.select(1), .width(5), .disabled("Z"), .enable("false")) multiplexer_15 (
    .in0({5{1'b0}}), .in1(5'b10000), .out(multiplexer_15_out), .sel(result1[1]));
  D_Flip_Flop #(.trigger("rising"), .Pre_Clr_Positions("LEGACY"), .NegatePresetClear("false"), .enable("true"), .NewFFLayout("false")) u_IR1 (
    .clk(CLK), .D(and_1_out), .Q(IR1_q));  // open: Qn, preset, en, reset
  D_Flip_Flop #(.trigger("rising"), .Pre_Clr_Positions("LEGACY"), .NegatePresetClear("false"), .enable("true"), .NewFFLayout("false")) u_IR2 (
    .clk(CLK), .D(and_2_out), .Q(IR2_q));  // open: Qn, preset, en, reset
  D_Flip_Flop #(.trigger("rising"), .Pre_Clr_Positions("LEGACY"), .NegatePresetClear("false"), .enable("true"), .NewFFLayout("false")) u_IR3 (
    .clk(CLK), .D(and_3_out), .Q(IR3_q));  // open: Qn, preset, en, reset
  Shifter #(.width(32), .shift("lr")) shifter_2 (.in(MemData), .\dist (multiplexer_15_out), .out(MemHUData));
  Multiplexer #(.select(2), .width(5), .disabled("Z"), .enable("false")) multiplexer_16 (
    .in0({5{1'b0}}), .in1(5'b01000), .in2(5'b10000), .in3(5'b11000), .out(multiplexer_16_out),
    .sel(result1[1:0]));
  Shifter #(.width(32), .shift("lr")) shifter_3 (.in(MemData), .\dist (multiplexer_16_out), .out(MemBData));
  Priority_Encoder #(.select(2), .disabled("Z")) priority_encoder_1 (
    .in0(1'b0), .in1(IR1_q), .in2(IR2_q), .in3(IR3_q), .out(interrupt_num), .gs(interrupt_sign));  // open: en_out, en_in
  not not_4 (not_4_out, uret);
  and and_4 (and_4_out, interrupt_sign, not_4_out);
  and and_5 (interrupt, interrupt_sign, IE);
  Multiplexer #(.select(2), .width(32), .disabled("Z"), .enable("false")) multiplexer_17 (
    .in1(32'h30ac), .in2(32'h3150), .in3(32'h31f4), .out(interrupt_PC), .sel(interrupt_num));  // open: in0
  D_Flip_Flop #(.trigger("rising"), .Pre_Clr_Positions("ABOVE_BELOW"), .NegatePresetClear("false"), .enable("false"), .NewFFLayout("true")) \IE中断使能寄存器  (
    .clk(CLK), .D(and_4_out), .Qn(IE));  // open: Q, preset, reset
  Register #(.width(32), .trigger("rising"), .Select("low")) u_EPC (
    .D(PC_next), .en(interrupt), .Q(EPC), .clk(CLK));  // open: clr
  Register #(.width(2), .trigger("rising"), .Select("low")) register_1 (
    .D(interrupt_num), .en(interrupt), .Q(register_1_q), .clk(CLK));  // open: clr
  Decoder #(.select(2), .tristate("false"), .disabled("Z"), .enable("false")) decoder_1 (
    .out1(decoder_1_out1), .out2(decoder_1_out2), .out3(decoder_1_out3), .sel(register_1_q));  // open: out0
  and and_6 (clear1, decoder_1_out1, uret);
  and and_7 (clear2, decoder_1_out2, uret);
  and and_8 (clear3, decoder_1_out3, uret);

  // Other names for the same wires on the sheet: R2_data[31:0] = MDin

  // Notes on the sheet:
  //   中断源
  //   中断等待指示
  //   总复位信号应将除ROM以外所有存储组件全部清零
  //   单级中断测试信号模拟器
  //   数码管输出
  //   数码管输出应该用寄存器锁存，否则显示数据只能一闪而过
  //   指令探针
  //   指令存储器
  //   指令字
  //   contents of rom_1 (hex, n*v repeats v):
  //   7d000113 100413 1f41993 41f9d993 433 c00913 800b13 140413 f47413 800293 100313 499993 89e9b3 1300533
  //   2200893 73 406282b3 fe0294e3 140413 f00f93 1f47433 1c41413 800293 100313 49d993 89e9b3 1300533
  //   2200893 73 406282b3 fe0294e3 1c45413 406b0b33 b0463 f95ff06f 2b3 fff2c293 1029293 fff2e293 500533
  //   2200893 73 f5dff06f 1112023 410113 a12023 410113 812023 410113 1312023 410113 1412023 410113 1512023
  //   410113 1612023 410113 100b13 300a13 100a93 1600433 441413 14469b3 1300533 2200893 73 fe0416e3
  //   415a0a33 fe0a10e3 ffc10113 12b03 ffc10113 12a83 ffc10113 12a03 ffc10113 12983 ffc10113 12403
  //   ffc10113 12503 ffc10113 12883 200073 1112023 410113 a12023 410113 812023 410113 1312023 410113
  //   1412023 410113 1512023 410113 1612023 410113 200b13 300a13 100a93 1600433 441413 14469b3 1300533
  //   2200893 73 fe0416e3 415a0a33 fe0a10e3 ffc10113 12b03 ffc10113 12a83 ffc10113 12a03 ffc10113 12983
  //   ffc10113 12403 ffc10113 12503 ffc10113 12883 200073 1112023 410113 a12023 410113 812023 410113
  //   1312023 410113 1412023 410113 1512023 410113 1612023 410113 300b13 300a13 100a93 1600433 441413
  //   14469b3 1300533 2200893 73 fe0416e3 415a0a33 fe0a10e3 ffc10113 12b03 ffc10113 12a83 ffc10113 12a03
  //   ffc10113 12983 ffc10113 12403 ffc10113 12503 ffc10113 12883 200073
  //   JAL
  //   JALR
  //   rs1
  //   rs2
  //   rd
  //   imm_i
  //   imm_s
  //   imm_b
  //   imm_j
  //   Beq
  //   Bne
  //   MemToReg
  //   MemWrite
  //   AluOP
  //   AluSrcB
  //   RegWrite
  //   S_type
  //   ecall
  //   为方便自动评测，需要输出PC，IR，寄存器堆写如数据RDin
  //   中断信号采样
  //   RAM写使能MemWrite、RAM写入数据MDin等信号
  //   控制位
  //   暂停节拍，不能为0
  //   戳工具置1进入计数暂停模式，ctrl+k时钟自动运行到对应节拍暂停
  //   ctrl+k关闭时钟连续运行，将控制位置零，进入单步调试模式调试
  //   可计数暂停的时钟源
  //   数据存储器
  //   Reset 
  //   同步清零信号
  //   Reset 
  //   同步清零信号
  //   Reset 
  //   同步清零信号
endmodule

module \封装正确性测试  (
);

  wire IR1, IR2, IR3, MemW, RegW;
  wire [31:0] EX_PC, ID_PC, IF_PC, IR, LED, MDin, MDinr, MEM_PC, PC, RDin, RDinr, WB_PC;

  \单周期RISC_V  \u_单周期risc_v_1  (
    .IR1(IR1), .IR2(IR2), .IR3(IR3), .RegWrite(RegW), .MemWrite(MemW), .PC(PC), .IR(IR), .RDin(RDin),
    .MDin(MDin), .LedData(LED));
  \气泡流水线  \u_气泡流水线_1  (
    .RegWrite(RegW), .MemWrite(MemW), .IF_PC(IF_PC), .ID_PC(ID_PC), .EX_PC(EX_PC), .M_PC(MEM_PC),
    .WB_PC(WB_PC), .RDin(RDinr), .MDin(MDinr), .LedData(LED));
  \单周期_单级中断  \u_单周期_单级中断_1  (
    .IR1(IR1), .IR2(IR2), .IR3(IR3), .RegWrite(RegW), .MemWrite(MemW), .PC(PC), .IR(IR), .RDin(RDin),
    .MDin(MDin), .LedData(LED));
  \理想流水线  \u_理想流水线_1  (
    .RegWrite(RegW), .MemWrite(MemW), .IF_PC(IF_PC), .ID_PC(ID_PC), .EX_PC(EX_PC), .M_PC(MEM_PC),
    .WB_PC(WB_PC), .RDin(RDinr), .MDin(MDinr), .LedData(LED));
  \重定向流水线  \u_重定向流水线_1  (
    .RegWrite(RegW), .MemWrite(MemW), .IF_PC(IF_PC), .ID_PC(ID_PC), .EX_PC(EX_PC), .M_PC(MEM_PC),
    .WB_PC(WB_PC), .RDin(RDinr), .MDin(MDinr), .LedData(LED));
  \单周期_多级中断  \u_单周期_多级中断_1  (
    .IR1(IR1), .IR2(IR2), .IR3(IR3), .RegWrite(RegW), .MemWrite(MemW), .PC(PC), .IR(IR), .RDin(RDin),
    .MDin(MDin), .LedData(LED));

  // Notes on the sheet:
  //   单周期封装测试
  //   气泡流水封装测试
  //   单周期+单级中断封装测试
  //   请检查上面封装有无位宽不匹配，引脚标签是否和连接的标签相对应，否则无法在educoder平台上正确测试
  //   理想流水封装测试
  //   重定向流水封装测试
  //   单周期+多级中断封装测试
endmodule

module ecall_halt (
  input  go_button,
  input  ecall,
  input  equal,
  input  [31:0] R2_data,
  input  clk,
  output halt,
  output [31:0] led_data
);

  wire demultiplexer_1_out0, demultiplexer_1_out1, not_1_out;

  Demultiplexer #(.select(1), .width(1), .tristate("false"), .disabled("Z"), .enable("false")) demultiplexer_1 (
    .out0(demultiplexer_1_out0), .out1(demultiplexer_1_out1), .in(ecall), .sel(equal));
  not not_1 (not_1_out, halt);
  Register #(.width(1), .trigger("falling"), .Select("low")) register_1 (
    .D(demultiplexer_1_out0), .en(not_1_out), .Q(halt), .clk(clk), .clr(go_button));
  Register #(.width(32), .trigger("rising"), .Select("low")) register_2 (
    .D(R2_data), .en(demultiplexer_1_out1), .Q(led_data), .clk(clk));  // open: clr
endmodule

module ID_EX (
  input  [31:0] PC_in,
  input  [31:0] RS1_in,
  input  [31:0] RS2_in,
  input  [4:0] RD_in,
  input  [18:0] control_sign_in,
  input  [31:0] Imm_in,
  input  halt,
  input  clk,
  output [31:0] PC_out,
  output [31:0] RS1_out,
  output [31:0] RS2_out,
  output [4:0] RD_out,
  output [18:0] control_sign_out,
  output [31:0] Imm_out
);

  wire not_1_out;

  not not_1 (not_1_out, halt);
  Register #(.width(32), .trigger("rising"), .Select("low")) PC (
    .D(PC_in), .en(not_1_out), .Q(PC_out), .clk(clk));  // open: clr
  Register #(.width(32), .trigger("rising"), .Select("low")) RS1 (
    .D(RS1_in), .en(not_1_out), .Q(RS1_out), .clk(clk));  // open: clr
  Register #(.width(32), .trigger("rising"), .Select("low")) RS2 (
    .D(RS2_in), .en(not_1_out), .Q(RS2_out), .clk(clk));  // open: clr
  Register #(.width(5), .trigger("rising"), .Select("low")) RD (
    .D(RD_in), .en(not_1_out), .Q(RD_out), .clk(clk));  // open: clr
  Register #(.width(19), .trigger("rising"), .Select("low")) control_sign (
    .D(control_sign_in), .en(not_1_out), .Q(control_sign_out), .clk(clk));  // open: clr
  Register #(.width(32), .trigger("rising"), .Select("low")) Imm (
    .D(Imm_in), .en(not_1_out), .Q(Imm_out), .clk(clk));  // open: clr
endmodule

module IF_ID (
  input  [31:0] pc,
  input  [31:0] instr,
  input  clk,
  input  halt,
  output [31:0] pc_out,
  output [31:0] instr_out
);

  wire not_1_out;

  not not_1 (not_1_out, halt);
  Register #(.width(32), .trigger("rising"), .Select("low")) register_1 (
    .D(pc), .en(not_1_out), .Q(pc_out), .clk(clk));  // open: clr
  Register #(.width(32), .trigger("rising"), .Select("low")) register_2 (
    .D(instr), .en(not_1_out), .Q(instr_out), .clk(clk));  // open: clr
endmodule

module EX_MEM (
  input  [31:0] pc_in,
  input  [31:0] result_in,
  input  [31:0] wd_in,
  input  [4:0] RD_in,
  input  RegWrite_in,
  input  MemToReg_in,
  input  MemWrite_in,
  input  jal_in,
  input  jalr_in,
  input  lhu_in,
  input  lb_in,
  input  CLK,
  output [31:0] pc_out,
  output [31:0] result_out,
  output [31:0] wd_out,
  output [4:0] RD_out,
  output RegWrite_out,
  output MemToReg_out,
  output MemWrite_out,
  output jal_out,
  output jalr_out,
  output lhu_out,
  output lb_out
);

  Register #(.width(5), .trigger("rising"), .Select("low")) register_1 (
    .D(RD_in), .Q(RD_out), .clk(CLK));  // open: en, clr
  Register #(.width(1), .trigger("rising"), .Select("low")) register_2 (
    .D(RegWrite_in), .Q(RegWrite_out), .clk(CLK));  // open: en, clr
  Register #(.width(1), .trigger("rising"), .Select("low")) register_3 (
    .D(MemToReg_in), .Q(MemToReg_out), .clk(CLK));  // open: en, clr
  Register #(.width(1), .trigger("rising"), .Select("low")) register_4 (
    .D(MemWrite_in), .Q(MemWrite_out), .clk(CLK));  // open: en, clr
  Register #(.width(1), .trigger("rising"), .Select("low")) register_5 (
    .D(jal_in), .Q(jal_out), .clk(CLK));  // open: en, clr
  Register #(.width(1), .trigger("rising"), .Select("low")) register_6 (
    .D(jalr_in), .Q(jalr_out), .clk(CLK));  // open: en, clr
  Register #(.width(1), .trigger("rising"), .Select("low")) register_7 (
    .D(lhu_in), .Q(lhu_out), .clk(CLK));  // open: en, clr
  Register #(.width(1), .trigger("rising"), .Select("low")) register_8 (
    .D(lb_in), .Q(lb_out), .clk(CLK));  // open: en, clr
  Register #(.width(32), .trigger("rising"), .Select("low")) register_9 (
    .D(pc_in), .Q(pc_out), .clk(CLK));  // open: en, clr
  Register #(.width(32), .trigger("rising"), .Select("low")) register_10 (
    .D(result_in), .Q(result_out), .clk(CLK));  // open: en, clr
  Register #(.width(32), .trigger("rising"), .Select("low")) register_11 (
    .D(wd_in), .Q(wd_out), .clk(CLK));  // open: en, clr
endmodule

module MEM_WB (
  input  [31:0] pc_in,
  input  [31:0] result_in,
  input  [31:0] memdata_in,
  input  [4:0] RD_in,
  input  RegWrite_in,
  input  MemToReg_in,
  input  jal_in,
  input  jalr_in,
  input  lhu_in,
  input  lb_in,
  input  CLK,
  output [31:0] pc_out,
  output [31:0] result_out,
  output [31:0] memdata_out,
  output [4:0] RD_out,
  output RegWrite_out,
  output MemToReg_out,
  output jal_out,
  output jalr_out,
  output lhu_out,
  output lb_out
);

  Pull_Resistor #(.pull(0)) pull_resistor_1 (.node(memdata_in));
  Register #(.width(5), .trigger("rising"), .Select("low")) register_1 (
    .D(RD_in), .Q(RD_out), .clk(CLK));  // open: en, clr
  Register #(.width(1), .trigger("rising"), .Select("low")) register_2 (
    .D(RegWrite_in), .Q(RegWrite_out), .clk(CLK));  // open: en, clr
  Register #(.width(1), .trigger("rising"), .Select("low")) register_3 (
    .D(MemToReg_in), .Q(MemToReg_out), .clk(CLK));  // open: en, clr
  Register #(.width(1), .trigger("rising"), .Select("low")) register_4 (
    .D(jal_in), .Q(jal_out), .clk(CLK));  // open: en, clr
  Register #(.width(1), .trigger("rising"), .Select("low")) register_5 (
    .D(jalr_in), .Q(jalr_out), .clk(CLK));  // open: en, clr
  Register #(.width(1), .trigger("rising"), .Select("low")) register_6 (
    .D(lhu_in), .Q(lhu_out), .clk(CLK));  // open: en, clr
  Register #(.width(1), .trigger("rising"), .Select("low")) register_7 (
    .D(lb_in), .Q(lb_out), .clk(CLK));  // open: en, clr
  Register #(.width(32), .trigger("rising"), .Select("low")) register_8 (
    .D(pc_in), .Q(pc_out), .clk(CLK));  // open: en, clr
  Register #(.width(32), .trigger("rising"), .Select("low")) register_9 (
    .D(result_in), .Q(result_out), .clk(CLK));  // open: en, clr
  Register #(.width(32), .trigger("rising"), .Select("low")) register_10 (
    .D(memdata_in), .Q(memdata_out), .clk(CLK));  // open: en, clr
endmodule

module \数据冲突识别器  (
  input  AluSrcB,
  input  sw,
  input  ecall,
  input  [4:0] R2,
  input  jal,
  input  nop,
  input  [4:0] R1,
  input  [4:0] rd_to_ID_EX,
  input  regwrite_to_ID_EX,
  input  CLK,
  output data_harzard
);

  wire and_1_out, and_2_out, and_3_out, and_4_out, and_7_out, comparator_1_eq, comparator_2_eq,
       comparator_3_eq, comparator_4_eq, comparator_5_eq, comparator_6_eq, not_1_out, not_2_out, not_3_out,
       or_1_out, or_2_out, or_3_out, or_4_out, register_2_q, register_4_q, register_6_q;
  wire [4:0] register_1_q, register_3_q, register_5_q;

  Register #(.width(5), .trigger("rising"), .Select("low")) register_1 (
    .D(rd_to_ID_EX), .Q(register_1_q), .clk(CLK));  // open: en, clr
  Register #(.width(1), .trigger("rising"), .Select("low")) register_2 (
    .D(regwrite_to_ID_EX), .Q(register_2_q), .clk(CLK));  // open: en, clr
  Comparator #(.width(5), .mode("twosComplement")) comparator_1 (
    .a(R2), .b(register_1_q), .eq(comparator_1_eq));  // open: gt, lt
  Comparator #(.width(5), .mode("twosComplement")) comparator_2 (
    .a(R1), .b(register_1_q), .eq(comparator_2_eq));  // open: gt, lt
  and and_1 (and_1_out, comparator_1_eq, register_2_q);
  and and_2 (and_2_out, comparator_2_eq, register_2_q);
  Register #(.width(5), .trigger("rising"), .Select("low")) register_3 (
    .D(register_1_q), .Q(register_3_q), .clk(CLK));  // open: en, clr
  Register #(.width(1), .trigger("rising"), .Select("low")) register_4 (
    .D(register_2_q), .Q(register_4_q), .clk(CLK));  // open: en, clr
  Comparator #(.width(5), .mode("twosComplement")) comparator_3 (
    .a(R2), .b(register_3_q), .eq(comparator_3_eq));  // open: gt, lt
  and and_3 (and_3_out, comparator_3_eq, register_4_q);
  Comparator #(.width(5), .mode("twosComplement")) comparator_4 (
    .a(R1), .b(register_3_q), .eq(comparator_4_eq));  // open: gt, lt
  and and_4 (and_4_out, comparator_4_eq, register_4_q);
  Register #(.width(5), .trigger("rising"), .Select("low")) register_5 (
    .D(register_3_q), .Q(register_5_q), .clk(CLK));  // open: en, clr
  Register #(.width(1), .trigger("rising"), .Select("low")) register_6 (
    .D(register_4_q), .Q(register_6_q), .clk(CLK));  // open: en, clr
  Comparator #(.width(5), .mode("twosComplement")) comparator_5 (
    .a(R2), .b(register_5_q), .eq(comparator_5_eq));  // open: gt, lt
  // AND_Gate and_5 has open pins: in0=comparator_5_eq, in1=register_6_q, out=open
  Comparator #(.width(5), .mode("twosComplement")) comparator_6 (
    .a(R1), .b(register_5_q), .eq(comparator_6_eq));  // open: gt, lt
  // AND_Gate and_6 has open pins: in0=comparator_6_eq, in1=register_6_q, out=open
  not not_1 (not_1_out, AluSrcB);
  or or_1 (or_1_out, not_1_out, sw, ecall);
  or or_2 (or_2_out, and_3_out, 1'b0, and_1_out);
  or or_3 (or_3_out, and_4_out, 1'b0, and_2_out);
  and and_7 (and_7_out, or_1_out, or_2_out);
  or or_4 (or_4_out, and_7_out, or_3_out);
  not not_2 (not_2_out, nop);
  not not_3 (not_3_out, jal);
  and and_8 (data_harzard, not_3_out, not_2_out, or_4_out);
endmodule

module \冲突识别器  (
  input  [31:0] IR,
  input  CLK,
  output stall
);

  Comparator #(.width(2), .mode("unsigned")) comparator_1 (.a(IR[1:0]), .b(2'b00), .eq(stall));  // open: gt, lt
endmodule

module \ID_EX气泡生成器  (
  input  [18:0] control_sign_in,
  input  nop,
  input  branch_harzard,
  input  data_harzard,
  input  [31:0] PC_in,
  output [18:0] control_sign_out,
  output [31:0] PC_out
);

  wire or_1_out;

  or or_1 (or_1_out, nop, branch_harzard, data_harzard);
  Multiplexer #(.select(1), .width(19), .disabled("Z"), .enable("false")) multiplexer_1 (
    .in0(control_sign_in), .in1({19{1'b0}}), .out(control_sign_out), .sel(or_1_out));
  Multiplexer #(.select(1), .width(32), .disabled("Z"), .enable("false")) multiplexer_2 (
    .in0(PC_in), .in1({32{1'b0}}), .out(PC_out), .sel(or_1_out));
endmodule

module \IF_ID气泡生成器  (
  input  [31:0] IR_in,
  input  data_harzard,
  input  branch_harzard,
  input  [31:0] PC_in,
  output [31:0] IR_out,
  output [31:0] PC_out
);

  Multiplexer #(.select(1), .width(32), .disabled("Z"), .enable("false")) multiplexer_1 (
    .in0(IR_in), .in1({32{1'b0}}), .out(IR_out), .sel(branch_harzard));
  Multiplexer #(.select(1), .width(32), .disabled("Z"), .enable("false")) multiplexer_2 (
    .in0(PC_in), .in1({32{1'b0}}), .out(PC_out), .sel(branch_harzard));
endmodule

module \halt控制器  (
  input  halt,
  input  data_harzard,
  input  branch_harzard,
  output real_halt
);

  wire and_1_out, not_1_out;

  not not_1 (not_1_out, branch_harzard);
  and and_1 (and_1_out, data_harzard, not_1_out);
  or or_1 (real_halt, halt, and_1_out);
endmodule

module regfile_hl (
  input  [31:0] Din,
  input  Clk,
  input  WE,
  input  [4:0] R1_num,
  input  [4:0] R2_num,
  input  [4:0] W_num,
  output [31:0] R1,
  output [31:0] R2
);

  // RegisterFile registerfile_1: pin names not known; wires that end beside it: Din, Clk, WE, W_num, R1_num, R2_num, R1, R2
endmodule

module stack_32bits_size3 (
  input  [31:0] \input ,
  input  clk,
  input  pop,
  input  push,
  output [31:0] top
);

  wire or_1_out;
  wire [31:0] EPC2, EPC3, multiplexer_1_out, multiplexer_2_out, multiplexer_3_out;

  or or_1 (or_1_out, pop, push);
  Multiplexer #(.select(1), .width(32), .disabled("Z"), .enable("false")) multiplexer_1 (
    .in0(\input ), .in1(EPC2), .out(multiplexer_1_out), .sel(pop));
  Multiplexer #(.select(1), .width(32), .disabled("Z"), .enable("false")) multiplexer_2 (
    .in0(top), .in1(EPC3), .out(multiplexer_2_out), .sel(pop));
  Multiplexer #(.select(1), .width(32), .disabled("Z"), .enable("false")) multiplexer_3 (
    .in0(EPC2), .in1({32{1'b0}}), .out(multiplexer_3_out), .sel(pop));
  Register #(.width(32), .trigger("rising"), .Select("low")) EPC1 (
    .D(multiplexer_1_out), .en(or_1_out), .Q(top), .clk(clk));  // open: clr
  Register #(.width(32), .trigger("rising"), .Select("low")) u_EPC2 (
    .D(multiplexer_2_out), .en(or_1_out), .Q(EPC2), .clk(clk));  // open: clr
  Register #(.width(32), .trigger("rising"), .Select("low")) u_EPC3 (
    .D(multiplexer_3_out), .en(or_1_out), .Q(EPC3), .clk(clk));  // open: clr

  // Other names for the same wires on the sheet: EPC1[31:0] = top
endmodule

module stack_2bits_size3 (
  input  [1:0] \input ,
  input  clk,
  input  pop,
  input  push,
  output [1:0] top
);

  wire or_1_out;
  wire [1:0] multiplexer_1_out, multiplexer_2_out, multiplexer_3_out, s2, s3;

  or or_1 (or_1_out, pop, push);
  Multiplexer #(.select(1), .width(2), .disabled("Z"), .enable("false")) multiplexer_1 (
    .in0(\input ), .in1(s2), .out(multiplexer_1_out), .sel(pop));
  Multiplexer #(.select(1), .width(2), .disabled("Z"), .enable("false")) multiplexer_2 (
    .in0(top), .in1(s3), .out(multiplexer_2_out), .sel(pop));
  Multiplexer #(.select(1), .width(2), .disabled("Z"), .enable("false")) multiplexer_3 (
    .in0(s2), .in1(2'b00), .out(multiplexer_3_out), .sel(pop));
  Register #(.width(2), .trigger("rising"), .Select("low")) s1 (
    .D(multiplexer_1_out), .en(or_1_out), .Q(top), .clk(clk));  // open: clr
  Register #(.width(2), .trigger("rising"), .Select("low")) u_s2 (
    .D(multiplexer_2_out), .en(or_1_out), .Q(s2), .clk(clk));  // open: clr
  Register #(.width(2), .trigger("rising"), .Select("low")) u_s3 (
    .D(multiplexer_3_out), .en(or_1_out), .Q(s3), .clk(clk));  // open: clr

  // Other names for the same wires on the sheet: s1[1:0] = top
endmodule

module \数据冲突识别器_重定向  (
  input  AluSrcB,
  input  [4:0] R2,
  input  sw,
  input  ecall,
  input  jal,
  input  [4:0] R1,
  input  nop,
  input  [4:0] rd_to_ID_EX,
  input  regwrite_to_ID_EX,
  input  CLK,
  input  memtoreg_to_ID_EX,
  input  jalr_to_ID_EX,
  input  jal_to_ID_EX,
  output [2:0] R2_relaycode,
  output stall,
  output [2:0] R1_relaycode
);

  wire and_1_out, and_2_out, and_3_out, and_4_out, and_5_out, comparator_1_eq, comparator_2_eq,
       comparator_3_eq, comparator_4_eq, comparator_5_eq, comparator_6_eq, ex_jump, ex_memtoreg, mem_jump,
       mem_memtoreg, not_1_out, not_2_out, or_1_out, or_3_out, or_4_out, register_2_q, register_6_q;
  wire [2:0] relay_encoder_1_relay_code, relay_encoder_2_relay_code;
  wire [4:0] register_1_q, register_5_q;

  or or_1 (or_1_out, jalr_to_ID_EX, jal_to_ID_EX);
  Register #(.width(5), .trigger("rising"), .Select("low")) register_1 (
    .D(rd_to_ID_EX), .Q(register_1_q), .clk(CLK));  // open: en, clr
  Register #(.width(1), .trigger("rising"), .Select("low")) register_2 (
    .D(regwrite_to_ID_EX), .Q(register_2_q), .clk(CLK));  // open: en, clr
  Register #(.width(1), .trigger("rising"), .Select("low")) register_3 (
    .D(memtoreg_to_ID_EX), .Q(ex_memtoreg), .clk(CLK));  // open: en, clr
  Register #(.width(1), .trigger("rising"), .Select("low")) register_4 (
    .D(or_1_out), .Q(ex_jump), .clk(CLK));  // open: en, clr
  Comparator #(.width(5), .mode("twosComplement")) comparator_1 (
    .a(R1), .b(register_1_q), .eq(comparator_1_eq));  // open: gt, lt
  and and_1 (and_1_out, comparator_1_eq, register_2_q);
  Comparator #(.width(5), .mode("twosComplement")) comparator_2 (
    .a(R2), .b(register_1_q), .eq(comparator_2_eq));  // open: gt, lt
  and and_2 (and_2_out, comparator_2_eq, register_2_q);
  Register #(.width(5), .trigger("rising"), .Select("low")) register_5 (
    .D(register_1_q), .Q(register_5_q), .clk(CLK));  // open: en, clr
  Register #(.width(1), .trigger("rising"), .Select("low")) register_6 (
    .D(register_2_q), .Q(register_6_q), .clk(CLK));  // open: en, clr
  Register #(.width(1), .trigger("rising"), .Select("low")) register_7 (
    .D(ex_memtoreg), .Q(mem_memtoreg), .clk(CLK));  // open: en, clr
  Register #(.width(1), .trigger("rising"), .Select("low")) register_8 (
    .D(ex_jump), .Q(mem_jump), .clk(CLK));  // open: en, clr
  Comparator #(.width(5), .mode("twosComplement")) comparator_3 (
    .a(R1), .b(register_5_q), .eq(comparator_3_eq));  // open: gt, lt
  and and_3 (and_3_out, comparator_3_eq, register_6_q);
  Comparator #(.width(5), .mode("twosComplement")) comparator_4 (
    .a(R2), .b(register_5_q), .eq(comparator_4_eq));  // open: gt, lt
  and and_4 (and_4_out, comparator_4_eq, register_6_q);
  relay_encoder relay_encoder_1 (
    .mem_eq(and_4_out), .mem_memtoreg(mem_memtoreg), .mem_jump(mem_jump), .ex_eq(and_2_out),
    .ex_memtoreg(ex_memtoreg), .ex_jump(ex_jump), .relay_code(relay_encoder_1_relay_code));
  relay_encoder relay_encoder_2 (
    .mem_eq(and_3_out), .mem_memtoreg(mem_memtoreg), .mem_jump(mem_jump), .ex_eq(and_1_out),
    .ex_memtoreg(ex_memtoreg), .ex_jump(ex_jump), .relay_code(relay_encoder_2_relay_code));
  Comparator #(.width(3), .mode("unsigned")) comparator_5 (
    .a(relay_encoder_1_relay_code), .b(3'b101), .eq(comparator_5_eq));  // open: gt, lt
  Comparator #(.width(3), .mode("unsigned")) comparator_6 (
    .a(3'b101), .b(relay_encoder_2_relay_code), .eq(comparator_6_eq));  // open: gt, lt
  or or_2 (stall, comparator_5_eq, comparator_6_eq);
  or or_3 (or_3_out, jal, nop);
  not not_1 (not_1_out, AluSrcB);
  or or_4 (or_4_out, not_1_out, sw, ecall);
  Multiplexer #(.select(1), .width(3), .disabled("Z"), .enable("false")) multiplexer_1 (
    .in0(relay_encoder_2_relay_code), .in1(3'b000), .out(R1_relaycode), .sel(or_3_out));
  not not_2 (not_2_out, or_3_out);
  and and_5 (and_5_out, or_4_out, not_2_out);
  Multiplexer #(.select(1), .width(3), .disabled("Z"), .enable("false")) multiplexer_2 (
    .in0(3'b000), .in1(relay_encoder_1_relay_code), .out(R2_relaycode), .sel(and_5_out));
endmodule

module relay_encoder (
  input  mem_eq,
  input  mem_memtoreg,
  input  mem_jump,
  input  ex_eq,
  input  ex_memtoreg,
  input  ex_jump,
  output [2:0] relay_code
);

  wire and_1_out, and_2_out, and_3_out, and_4_out;

  and and_1 (and_1_out, mem_eq, mem_memtoreg);
  and and_2 (and_2_out, mem_eq, mem_jump);
  and and_3 (and_3_out, ex_eq, ex_memtoreg);
  and and_4 (and_4_out, ex_eq, ex_jump);
  Priority_Encoder #(.select(3), .disabled("Z")) priority_encoder_1 (
    .in0(1'b1), .in1(mem_eq), .in2(and_1_out), .in3(and_2_out), .in4(ex_eq), .in5(and_3_out),
    .in6(and_4_out), .out(relay_code));  // open: in7, gs, en_out, en_in
endmodule

module \数据转发器  (
  input  [31:0] ID_EX_R1,
  input  [31:0] WB_result,
  input  [31:0] RDin,
  input  [31:0] WB_PC,
  input  [31:0] ID_EX_R2,
  input  [31:0] MEM_result,
  input  [31:0] MEM_PC,
  input  [2:0] R1_relaycode,
  input  [2:0] R2_relaycode,
  input  CLK,
  output [31:0] EX_R1,
  output [31:0] EX_R2
);

  wire [2:0] register_1_q, register_2_q;
  wire [31:0] d3, d6;

  Register #(.width(3), .trigger("rising"), .Select("low")) register_1 (
    .D(R1_relaycode), .Q(register_1_q), .clk(CLK));  // open: en, clr
  Register #(.width(3), .trigger("rising"), .Select("low")) register_2 (
    .D(R2_relaycode), .Q(register_2_q), .clk(CLK));  // open: en, clr
  Multiplexer #(.select(3), .width(32), .disabled("Z"), .enable("false")) multiplexer_1 (
    .in0(ID_EX_R1), .in1(WB_result), .in2(RDin), .in3(d3), .in4(MEM_result), .in5({32{1'b0}}), .in6(d6),
    .out(EX_R1), .sel(register_1_q));  // open: in7
  Multiplexer #(.select(3), .width(32), .disabled("Z"), .enable("false")) multiplexer_2 (
    .in0(ID_EX_R2), .in1(WB_result), .in2(RDin), .in3(d3), .in4(MEM_result), .in5({32{1'b0}}), .in6(d6),
    .out(EX_R2), .sel(register_2_q));  // open: in7
  Adder #(.width(32)) adder_1 (.a(MEM_PC), .b(32'h4), .out(d6));  // open: cin, cout
  Adder #(.width(32)) adder_2 (.a(WB_PC), .b(32'h4), .out(d3));  // open: cin, cout

  // Other names for the same wires on the sheet: d0r1[31:0] = ID_EX_R1; d0r2[31:0] = ID_EX_R2; d1[31:0] = WB_result;
  //   d2[31:0] = RDin; d4[31:0] = MEM_result
endmodule
